// Logisim project Brookshear.circ as structural Verilog
module UN_PIPELINED (
);

  wire and_1_out, and_3_out, and_4_out, and_5_out, and_6_out, and_7_out, and_8_out, and_9_out, and_10_out,
       and_11_out, ARITHMETIC_LOGIC_UNIT_sr, ARITHMETIC_LOGIC_UNIT_sr_w, AUTO_p1, CLK_out,
       CONTROL_UNIT_alu_read, CONTROL_UNIT_hlt, CONTROL_UNIT_increment_pc, CONTROL_UNIT_load_acc,
       CONTROL_UNIT_load_cir, CONTROL_UNIT_load_mar, CONTROL_UNIT_load_out, CONTROL_UNIT_read_acc,
       CONTROL_UNIT_read_mbr, CONTROL_UNIT_read_ram, CONTROL_UNIT_register_read, CONTROL_UNIT_register_write,
       CONTROL_UNIT_reset_pc, CONTROL_UNIT_write_ram, CONTROL_UNIT_xy_e, d_ff_1_q, d_ff_1_qn, not_7_out,
       or_1_out, or_2_out, RESET_out, STATUS_REG_q, STEP_out;
  wire [2:0] CONTROL_UNIT_alu_instr, not_3_out_2, not_4_out_2, not_5_out_2, not_6_out_2, not_8_out_2,
       not_10_out_2, not_21_out_2, not_22_out_2;
  wire [3:0] ARITHMETIC_LOGIC_UNIT_data_out, ARITHMETIC_LOGIC_UNIT_data_out_2, BUS_COORDINATOR_1_bus_out,
       BUS_COORDINATOR_1_bus_out_2, CIR_q, CIR_q_2, CIR_q_3, CIR_q_4, CONTROL_UNIT_register_read_select,
       CONTROL_UNIT_register_write_select, CONTROL_UNIT_xy, CONTROL_UNIT_xy_2, j_k_ff_1_q, j_k_ff_5_q, MAR_q,
       MAR_q_2, not_3_out, not_4_out, not_5_out, not_6_out, not_8_out, not_10_out, not_21_out, not_22_out,
       OUTPUT_REG_q, OUTPUT_REG_q_2, register_2_q, register_2_q_2;
  wire [4:0] CONTROL_UNIT_ring_counter;
  wire [6:0] Hexdecoder_1_output_bus_1, Hexdecoder_2_output_bus_1, Hexdecoder_3_output_bus_1,
       Hexdecoder_4_output_bus_1, Hexdecoder_5_output_bus_1, Hexdecoder_6_output_bus_1,
       Hexdecoder_7_output_bus_1, Hexdecoder_8_output_bus_1, Hexdecoder_9_output_bus_1,
       Hexdecoder_10_output_bus_1, Hexdecoder_11_output_bus_1, Hexdecoder_12_output_bus_1,
       Hexdecoder_13_output_bus_1, Hexdecoder_14_output_bus_1, Hexdecoder_15_output_bus_1,
       Hexdecoder_16_output_bus_1, Hexdecoder_17_output_bus_1, Hexdecoder_18_output_bus_1,
       Hexdecoder_19_output_bus_1, Hexdecoder_20_output_bus_1, Hexdecoder_21_output_bus_1,
       Hexdecoder_22_output_bus_1, Hexdecoder_23_output_bus_1, not_1_out, not_2_out, not_9_out, not_11_out,
       not_12_out, not_13_out, not_14_out, not_15_out, not_16_out, not_17_out, not_18_out, not_19_out,
       not_20_out, not_23_out, not_24_out;
  wire [7:0] and_2_out, MAIN_MEMORY_data_out, register_1_q, REGISTERS_data_out;
  wire [7:7] CONTROL_UNIT_load_pc;
  wire [15:0] INSTRUCTIONS_data;

  _7_Segment_Display #(.active("false")) R_WRITE (
    .g(not_1_out[0]), .f(not_1_out[1]), .a(not_1_out[6]), .b(not_1_out[5]), .e(not_1_out[2]),
    .d(not_1_out[3]), .c(not_1_out[4]), .dp(1'b1));
  assign not_1_out = ~Hexdecoder_12_output_bus_1;  // NOT_Gate not_1, 7 bits wide
  Hexdecoder Hexdecoder_12 (
    .Input_bus_1(CONTROL_UNIT_register_write_select), .E(CONTROL_UNIT_register_write),
    .Output_bus_1(Hexdecoder_12_output_bus_1));
  _7_Segment_Display #(.active("false"), .decimalPoint("false")) R_READ (
    .g(not_2_out[0]), .f(not_2_out[1]), .a(not_2_out[6]), .b(not_2_out[5]), .e(not_2_out[2]),
    .d(not_2_out[3]), .c(not_2_out[4]));
  assign not_2_out = ~Hexdecoder_13_output_bus_1;  // NOT_Gate not_2, 7 bits wide
  Hexdecoder Hexdecoder_13 (
    .Input_bus_1(CONTROL_UNIT_register_read_select), .E(CONTROL_UNIT_register_read),
    .Output_bus_1(Hexdecoder_13_output_bus_1));
  and and_1 (and_1_out, CONTROL_UNIT_increment_pc, and_6_out);
  J_K_Flip_Flop #(.trigger("falling")) j_k_ff_1 (
    .J(1'b1), .K(1'b1), .clk(and_1_out), .Q(j_k_ff_1_q[0]), .preset(and_2_out[0]), .reset(or_1_out));  // open: Qn
  or or_1 (or_1_out, CONTROL_UNIT_reset_pc, RESET_out);
  _7_Segment_Display #(.active("false"), .decimalPoint("false")) PC_1 (
    .g(not_3_out[0]), .f(not_3_out[1]), .a(not_3_out[3]), .b(not_3_out[2]), .e(not_3_out_2[0]),
    .d(not_3_out_2[1]), .c(not_3_out_2[2]));
  MEMORY_16B REGISTERS (
    .RESET(RESET_out), .READ_ADDRESS(CONTROL_UNIT_register_read_select), .WRITE(CONTROL_UNIT_register_write),
    .DATA_IN({BUS_COORDINATOR_1_bus_out_2, BUS_COORDINATOR_1_bus_out}),
    .WRITE_ADDRESS(CONTROL_UNIT_register_write_select), .CLK(and_6_out), .DATA_OUT(REGISTERS_data_out));
  assign and_2_out = {8{CONTROL_UNIT_load_pc[7]}} & {BUS_COORDINATOR_1_bus_out_2, BUS_COORDINATOR_1_bus_out};  // AND_Gate and_2, 8 bits wide
  Hexdecoder Hexdecoder_7 (.Input_bus_1(j_k_ff_5_q), .E(1'b1), .Output_bus_1(Hexdecoder_7_output_bus_1));
  Hexdecoder Hexdecoder_8 (.Input_bus_1(j_k_ff_1_q), .E(1'b1), .Output_bus_1(Hexdecoder_8_output_bus_1));
  assign {not_3_out[3:2], not_3_out_2, not_3_out[1:0]} = ~Hexdecoder_7_output_bus_1;  // NOT_Gate not_3, 7 bits wide
  assign {not_4_out[3:2], not_4_out_2, not_4_out[1:0]} = ~Hexdecoder_8_output_bus_1;  // NOT_Gate not_4, 7 bits wide
  _7_Segment_Display #(.active("false"), .decimalPoint("false")) PC_0 (
    .g(not_4_out[0]), .f(not_4_out[1]), .a(not_4_out[3]), .b(not_4_out[2]), .e(not_4_out_2[0]),
    .d(not_4_out_2[1]), .c(not_4_out_2[2]));
  J_K_Flip_Flop #(.trigger("falling")) j_k_ff_2 (
    .J(j_k_ff_1_q[0]), .K(j_k_ff_1_q[0]), .clk(and_1_out), .Q(j_k_ff_1_q[1]), .preset(and_2_out[1]),
    .reset(or_1_out));  // open: Qn
  ROM #(.dataWidth(16)) INSTRUCTIONS (.addr({j_k_ff_5_q, j_k_ff_1_q}), .data(INSTRUCTIONS_data));
  J_K_Flip_Flop #(.trigger("falling")) j_k_ff_3 (
    .J(and_3_out), .K(and_3_out), .clk(and_1_out), .Q(j_k_ff_1_q[2]), .preset(and_2_out[2]), .reset(or_1_out));  // open: Qn
  and and_3 (and_3_out, j_k_ff_1_q[1], j_k_ff_1_q[0]);
  Hexdecoder Hexdecoder_20 (
    .Input_bus_1(BUS_COORDINATOR_1_bus_out_2), .E(1'b1), .Output_bus_1(Hexdecoder_20_output_bus_1));
  assign {not_5_out[3:2], not_5_out_2, not_5_out[1:0]} = ~Hexdecoder_20_output_bus_1;  // NOT_Gate not_5, 7 bits wide
  _7_Segment_Display #(.active("false"), .decimalPoint("false")) MAIN_BUS_1 (
    .g(not_5_out[0]), .f(not_5_out[1]), .a(not_5_out[3]), .b(not_5_out[2]), .e(not_5_out_2[0]),
    .d(not_5_out_2[1]), .c(not_5_out_2[2]));
  and and_4 (and_4_out, j_k_ff_1_q[2], and_3_out);
  Hexdecoder Hexdecoder_21 (
    .Input_bus_1(BUS_COORDINATOR_1_bus_out), .E(1'b1), .Output_bus_1(Hexdecoder_21_output_bus_1));
  assign {not_6_out[3:2], not_6_out_2, not_6_out[1:0]} = ~Hexdecoder_21_output_bus_1;  // NOT_Gate not_6, 7 bits wide
  _7_Segment_Display #(.active("false"), .decimalPoint("false")) MAIN_BUS_0 (
    .g(not_6_out[0]), .f(not_6_out[1]), .a(not_6_out[3]), .b(not_6_out[2]), .e(not_6_out_2[0]),
    .d(not_6_out_2[1]), .c(not_6_out_2[2]));
  J_K_Flip_Flop #(.trigger("falling")) j_k_ff_4 (
    .J(and_4_out), .K(and_4_out), .clk(and_1_out), .Q(j_k_ff_1_q[3]), .preset(and_2_out[3]), .reset(or_1_out));  // open: Qn
  and and_5 (and_5_out, j_k_ff_1_q[3], and_4_out);
  Register #(.width(16)) CIR (
    .D(INSTRUCTIONS_data), .en(CONTROL_UNIT_load_cir), .clk(and_6_out),
    .Q({CIR_q_4, CIR_q_3, CIR_q_2, CIR_q}), .clr(RESET_out));
  and and_6 (and_6_out, or_2_out, d_ff_1_qn);
  D_Flip_Flop #(.trigger("falling")) d_ff_1 (
    .D(CONTROL_UNIT_hlt), .clk(and_6_out), .Q(d_ff_1_q), .Qn(d_ff_1_qn), .preset(1'b0), .reset(RESET_out));
  J_K_Flip_Flop #(.trigger("falling")) j_k_ff_5 (
    .J(and_5_out), .K(and_5_out), .clk(and_1_out), .Q(j_k_ff_5_q[0]), .preset(and_2_out[4]), .reset(or_1_out));  // open: Qn
  and and_7 (and_7_out, STEP_out, not_7_out);
  or or_2 (or_2_out, and_7_out, and_8_out);
  and and_8 (and_8_out, AUTO_p1, CLK_out);
  LED HLT_REG (.in(d_ff_1_q));
  BUS_COORDINATOR BUS_COORDINATOR_1 (
    .xy({CONTROL_UNIT_xy_2, CONTROL_UNIT_xy}), .REGS(REGISTERS_data_out),
    .RAM({register_2_q_2, register_2_q}),
    .ALU({ARITHMETIC_LOGIC_UNIT_data_out_2, ARITHMETIC_LOGIC_UNIT_data_out}), .xy_E(CONTROL_UNIT_xy_e),
    .REGS_E(CONTROL_UNIT_register_read), .RAM_E(CONTROL_UNIT_read_mbr), .ALU_E(CONTROL_UNIT_alu_read),
    .BUS_OUT({BUS_COORDINATOR_1_bus_out_2, BUS_COORDINATOR_1_bus_out}));
  J_K_Flip_Flop #(.trigger("falling")) j_k_ff_6 (
    .J(and_9_out), .K(and_9_out), .clk(and_1_out), .Q(j_k_ff_5_q[1]), .preset(and_2_out[5]), .reset(or_1_out));  // open: Qn
  and and_9 (and_9_out, j_k_ff_5_q[0], and_5_out);
  not not_7 (not_7_out, AUTO_p1);
  LED AUTO_STATUS (.in(AUTO_p1));
  LED CLK_L (.in(CLK_out));
  and and_10 (and_10_out, j_k_ff_5_q[1], and_9_out);
  Button RESET (.out(RESET_out));
  Button STEP (.out(STEP_out));
  // DipSwitch #(.number(1)) AUTO: pin names not known; wires that end beside it: AUTO_p1
  Clock CLK (.out(CLK_out));
  J_K_Flip_Flop #(.trigger("falling")) j_k_ff_7 (
    .J(and_10_out), .K(and_10_out), .clk(and_1_out), .Q(j_k_ff_5_q[2]), .preset(and_2_out[6]),
    .reset(or_1_out));  // open: Qn
  Register #(.trigger("falling")) MAR (
    .D({BUS_COORDINATOR_1_bus_out_2, BUS_COORDINATOR_1_bus_out}), .en(CONTROL_UNIT_load_mar),
    .clk(and_6_out), .Q({MAR_q_2, MAR_q}), .clr(RESET_out));
  J_K_Flip_Flop #(.trigger("falling")) j_k_ff_8 (
    .J(and_11_out), .K(and_11_out), .clk(and_1_out), .Q(j_k_ff_5_q[3]), .preset(and_2_out[7]),
    .reset(or_1_out));  // open: Qn
  and and_11 (and_11_out, j_k_ff_5_q[2], and_10_out);
  Hexdecoder Hexdecoder_18 (.Input_bus_1(MAR_q_2), .E(1'b1), .Output_bus_1(Hexdecoder_18_output_bus_1));
  assign {not_8_out[3:2], not_8_out_2, not_8_out[1:0]} = ~Hexdecoder_18_output_bus_1;  // NOT_Gate not_8, 7 bits wide
  _7_Segment_Display #(.active("false"), .decimalPoint("false")) MAR_1 (
    .g(not_8_out[0]), .f(not_8_out[1]), .a(not_8_out[3]), .b(not_8_out[2]), .e(not_8_out_2[0]),
    .d(not_8_out_2[1]), .c(not_8_out_2[2]));
  assign not_9_out = ~Hexdecoder_1_output_bus_1;  // NOT_Gate not_9, 7 bits wide
  Hexdecoder Hexdecoder_1 (.Input_bus_1(CIR_q_4), .E(1'b1), .Output_bus_1(Hexdecoder_1_output_bus_1));
  CU CONTROL_UNIT (
    .Run(RESET_out), .SR(STATUS_REG_q), .INSTRUCTION({CIR_q_4, CIR_q_3, CIR_q_2, CIR_q}), .CLK(and_6_out),
    .RING_COUNTER(CONTROL_UNIT_ring_counter), .LOAD_CIR(CONTROL_UNIT_load_cir),
    .INCREMENT_PC(CONTROL_UNIT_increment_pc), .ALU_INSTR(CONTROL_UNIT_alu_instr),
    .LOAD_OUT(CONTROL_UNIT_load_out), .LOAD_MAR(CONTROL_UNIT_load_mar), .READ_RAM(CONTROL_UNIT_read_ram),
    .WRITE_RAM(CONTROL_UNIT_write_ram), .READ_MBR(CONTROL_UNIT_read_mbr), .READ_ACC(CONTROL_UNIT_read_acc),
    .LOAD_ACC(CONTROL_UNIT_load_acc), .ALU_READ(CONTROL_UNIT_alu_read),
    .REGISTER_READ_SELECT(CONTROL_UNIT_register_read_select),
    .REGISTER_WRITE_SELECT(CONTROL_UNIT_register_write_select), .XY_E(CONTROL_UNIT_xy_e),
    .xy({CONTROL_UNIT_xy_2, CONTROL_UNIT_xy}), .RESET_PC(CONTROL_UNIT_reset_pc),
    .LOAD_PC(CONTROL_UNIT_load_pc[7]), .HLT(CONTROL_UNIT_hlt), .REGISTER_READ(CONTROL_UNIT_register_read),
    .REGISTER_WRITE(CONTROL_UNIT_register_write));
  Register #(.trigger("falling")) register_1 (
    .D({BUS_COORDINATOR_1_bus_out_2, BUS_COORDINATOR_1_bus_out}), .en(CONTROL_UNIT_load_acc),
    .clk(and_6_out), .Q(register_1_q), .clr(RESET_out));
  Hexdecoder Hexdecoder_19 (.Input_bus_1(MAR_q), .E(1'b1), .Output_bus_1(Hexdecoder_19_output_bus_1));
  assign {not_10_out[3:2], not_10_out_2, not_10_out[1:0]} = ~Hexdecoder_19_output_bus_1;  // NOT_Gate not_10, 7 bits wide
  _7_Segment_Display #(.active("false"), .decimalPoint("false")) MAR_0 (
    .g(not_10_out[0]), .f(not_10_out[1]), .a(not_10_out[3]), .b(not_10_out[2]), .e(not_10_out_2[0]),
    .d(not_10_out_2[1]), .c(not_10_out_2[2]));
  _7_Segment_Display #(.active("false"), .decimalPoint("false")) CIR_3 (
    .g(not_9_out[0]), .f(not_9_out[1]), .a(not_9_out[6]), .b(not_9_out[5]), .e(not_9_out[2]),
    .d(not_9_out[3]), .c(not_9_out[4]));
  _7_Segment_Display #(.active("false"), .decimalPoint("false")) CIR_2 (
    .g(not_11_out[0]), .f(not_11_out[1]), .a(not_11_out[6]), .b(not_11_out[5]), .e(not_11_out[2]),
    .d(not_11_out[3]), .c(not_11_out[4]));
  assign not_11_out = ~Hexdecoder_2_output_bus_1;  // NOT_Gate not_11, 7 bits wide
  Hexdecoder Hexdecoder_2 (.Input_bus_1(CIR_q_3), .E(1'b1), .Output_bus_1(Hexdecoder_2_output_bus_1));
  _7_Segment_Display #(.active("false"), .decimalPoint("false")) CIR_1 (
    .g(not_12_out[0]), .f(not_12_out[1]), .a(not_12_out[6]), .b(not_12_out[5]), .e(not_12_out[2]),
    .d(not_12_out[3]), .c(not_12_out[4]));
  assign not_12_out = ~Hexdecoder_3_output_bus_1;  // NOT_Gate not_12, 7 bits wide
  assign not_13_out = ~Hexdecoder_4_output_bus_1;  // NOT_Gate not_13, 7 bits wide
  Hexdecoder Hexdecoder_3 (.Input_bus_1(CIR_q_2), .E(1'b1), .Output_bus_1(Hexdecoder_3_output_bus_1));
  Hexdecoder Hexdecoder_4 (.Input_bus_1(CIR_q), .E(1'b1), .Output_bus_1(Hexdecoder_4_output_bus_1));
  Hexdecoder Hexdecoder_14 (.Input_bus_1(register_1_q[7:4]), .E(1'b1), .Output_bus_1(Hexdecoder_14_output_bus_1));
  Hexdecoder Hexdecoder_15 (.Input_bus_1(register_1_q[3:0]), .E(1'b1), .Output_bus_1(Hexdecoder_15_output_bus_1));
  _7_Segment_Display #(.active("false"), .decimalPoint("false")) CIR_0 (
    .g(not_13_out[0]), .f(not_13_out[1]), .a(not_13_out[6]), .b(not_13_out[5]), .e(not_13_out[2]),
    .d(not_13_out[3]), .c(not_13_out[4]));
  ALU ARITHMETIC_LOGIC_UNIT (
    .R(RESET_out), .INSTR(CONTROL_UNIT_alu_instr),
    .DATA_IN({BUS_COORDINATOR_1_bus_out_2, BUS_COORDINATOR_1_bus_out}), .ACCUMULATOR(register_1_q),
    .CLK(and_6_out), .DATA_OUT({ARITHMETIC_LOGIC_UNIT_data_out_2, ARITHMETIC_LOGIC_UNIT_data_out}),
    .SR_W(ARITHMETIC_LOGIC_UNIT_sr_w), .SR(ARITHMETIC_LOGIC_UNIT_sr));
  MEMORY_256B MAIN_MEMORY (
    .READ_ADDRESS({MAR_q_2, MAR_q}), .WRITE(CONTROL_UNIT_write_ram), .WRITE_ADDRESS({MAR_q_2, MAR_q}),
    .DATA_IN({BUS_COORDINATOR_1_bus_out_2, BUS_COORDINATOR_1_bus_out}), .RESET(RESET_out), .CLK(and_6_out),
    .DATA_OUT(MAIN_MEMORY_data_out));
  LED RC_0 (.in(CONTROL_UNIT_ring_counter[0]));
  LED RC_1 (.in(CONTROL_UNIT_ring_counter[1]));
  LED RC_2 (.in(CONTROL_UNIT_ring_counter[2]));
  LED RC_3 (.in(CONTROL_UNIT_ring_counter[3]));
  LED RC_4 (.in(CONTROL_UNIT_ring_counter[4]));
  LED PC_INCR (.in(CONTROL_UNIT_increment_pc));
  LED CIR_LOAD (.in(CONTROL_UNIT_load_cir));
  LED REG_READ (.in(CONTROL_UNIT_register_read));
  LED REG_WRITE (.in(CONTROL_UNIT_register_write));
  LED MAR_LOAD (.in(CONTROL_UNIT_load_mar));
  LED RAM_READ (.in(CONTROL_UNIT_read_ram));
  LED RAM_WRITE (.in(CONTROL_UNIT_write_ram));
  LED MBR_READ (.in(CONTROL_UNIT_read_mbr));
  LED ACC_READ (.in(CONTROL_UNIT_read_acc));
  LED ACC_LOAD (.in(CONTROL_UNIT_load_acc));
  LED OUT_LOAD (.in(CONTROL_UNIT_load_out));
  LED ALU_READ (.in(CONTROL_UNIT_alu_read));
  LED PC_CLEAR (.in(CONTROL_UNIT_reset_pc));
  LED PC_LOAD (.in(CONTROL_UNIT_load_pc[7]));
  LED HLT (.in(CONTROL_UNIT_hlt));
  assign not_14_out = ~Hexdecoder_14_output_bus_1;  // NOT_Gate not_14, 7 bits wide
  assign not_15_out = ~Hexdecoder_15_output_bus_1;  // NOT_Gate not_15, 7 bits wide
  Register #(.trigger("falling"), .width(1)) STATUS_REG (
    .D(ARITHMETIC_LOGIC_UNIT_sr), .en(ARITHMETIC_LOGIC_UNIT_sr_w), .clk(and_6_out), .Q(STATUS_REG_q),
    .clr(RESET_out));
  Register register_2 (
    .D(MAIN_MEMORY_data_out), .en(CONTROL_UNIT_read_ram), .clk(and_6_out),
    .Q({register_2_q_2, register_2_q}), .clr(RESET_out));
  _7_Segment_Display #(.active("false"), .decimalPoint("false")) ACC_1 (
    .g(not_14_out[0]), .f(not_14_out[1]), .a(not_14_out[6]), .b(not_14_out[5]), .e(not_14_out[2]),
    .d(not_14_out[3]), .c(not_14_out[4]));
  LED SR_TEMP (.in(ARITHMETIC_LOGIC_UNIT_sr));
  LED SR_W_TEMP (.in(ARITHMETIC_LOGIC_UNIT_sr_w));
  assign not_16_out = ~Hexdecoder_5_output_bus_1;  // NOT_Gate not_16, 7 bits wide
  Hexdecoder Hexdecoder_5 (.Input_bus_1(OUTPUT_REG_q_2), .E(1'b1), .Output_bus_1(Hexdecoder_5_output_bus_1));
  _7_Segment_Display #(.active("false"), .decimalPoint("false")) ACC_0 (
    .g(not_15_out[0]), .f(not_15_out[1]), .a(not_15_out[6]), .b(not_15_out[5]), .e(not_15_out[2]),
    .d(not_15_out[3]), .c(not_15_out[4]));
  LED SR (.in(STATUS_REG_q));
  _7_Segment_Display #(.active("false"), .decimalPoint("false")) MBR_1 (
    .g(not_17_out[0]), .f(not_17_out[1]), .a(not_17_out[6]), .b(not_17_out[5]), .e(not_17_out[2]),
    .d(not_17_out[3]), .c(not_17_out[4]));
  assign not_17_out = ~Hexdecoder_16_output_bus_1;  // NOT_Gate not_17, 7 bits wide
  assign not_18_out = ~Hexdecoder_17_output_bus_1;  // NOT_Gate not_18, 7 bits wide
  Hexdecoder Hexdecoder_16 (.Input_bus_1(register_2_q_2), .E(1'b1), .Output_bus_1(Hexdecoder_16_output_bus_1));
  Hexdecoder Hexdecoder_17 (.Input_bus_1(register_2_q), .E(1'b1), .Output_bus_1(Hexdecoder_17_output_bus_1));
  _7_Segment_Display #(.active("false"), .decimalPoint("false")) OUTPUT_1 (
    .g(not_16_out[0]), .f(not_16_out[1]), .a(not_16_out[6]), .b(not_16_out[5]), .e(not_16_out[2]),
    .d(not_16_out[3]), .c(not_16_out[4]));
  assign not_19_out = ~Hexdecoder_6_output_bus_1;  // NOT_Gate not_19, 7 bits wide
  Hexdecoder Hexdecoder_6 (.Input_bus_1(OUTPUT_REG_q), .E(1'b1), .Output_bus_1(Hexdecoder_6_output_bus_1));
  Register #(.trigger("falling")) OUTPUT_REG (
    .D({BUS_COORDINATOR_1_bus_out_2, BUS_COORDINATOR_1_bus_out}), .en(CONTROL_UNIT_load_out),
    .clk(and_6_out), .Q({OUTPUT_REG_q_2, OUTPUT_REG_q}), .clr(RESET_out));
  _7_Segment_Display #(.active("false"), .decimalPoint("false")) MBR_0 (
    .g(not_18_out[0]), .f(not_18_out[1]), .a(not_18_out[6]), .b(not_18_out[5]), .e(not_18_out[2]),
    .d(not_18_out[3]), .c(not_18_out[4]));
  _7_Segment_Display #(.active("false"), .decimalPoint("false")) OUTPUT_0 (
    .g(not_19_out[0]), .f(not_19_out[1]), .a(not_19_out[6]), .b(not_19_out[5]), .e(not_19_out[2]),
    .d(not_19_out[3]), .c(not_19_out[4]));
  _7_Segment_Display #(.active("false"), .decimalPoint("false")) ALU_INSTR (
    .g(not_20_out[0]), .f(not_20_out[1]), .a(not_20_out[6]), .b(not_20_out[5]), .e(not_20_out[2]),
    .d(not_20_out[3]), .c(not_20_out[4]));
  assign not_20_out = ~Hexdecoder_9_output_bus_1;  // NOT_Gate not_20, 7 bits wide
  Hexdecoder Hexdecoder_9 (
    .Input_bus_1({1'b0, CONTROL_UNIT_alu_instr}), .E(1'b1), .Output_bus_1(Hexdecoder_9_output_bus_1));
  Hexdecoder Hexdecoder_10 (.Input_bus_1(CONTROL_UNIT_xy_2), .E(1'b0), .Output_bus_1(Hexdecoder_10_output_bus_1));
  assign {not_21_out[3:2], not_21_out_2, not_21_out[1:0]} = ~Hexdecoder_10_output_bus_1;  // NOT_Gate not_21, 7 bits wide
  _7_Segment_Display #(.active("false"), .decimalPoint("false")) XY_1_x (
    .g(not_21_out[0]), .f(not_21_out[1]), .a(not_21_out[3]), .b(not_21_out[2]), .e(not_21_out_2[0]),
    .d(not_21_out_2[1]), .c(not_21_out_2[2]));
  _7_Segment_Display #(.active("false"), .decimalPoint("false")) XY_0_y (
    .g(not_22_out[0]), .f(not_22_out[1]), .a(not_22_out[3]), .b(not_22_out[2]), .e(not_22_out_2[0]),
    .d(not_22_out_2[1]), .c(not_22_out_2[2]));
  Hexdecoder Hexdecoder_11 (.Input_bus_1(CONTROL_UNIT_xy), .E(1'b0), .Output_bus_1(Hexdecoder_11_output_bus_1));
  assign {not_22_out[3:2], not_22_out_2, not_22_out[1:0]} = ~Hexdecoder_11_output_bus_1;  // NOT_Gate not_22, 7 bits wide
  _7_Segment_Display #(.active("false"), .decimalPoint("false")) ALU_1 (
    .g(not_23_out[0]), .f(not_23_out[1]), .a(not_23_out[6]), .b(not_23_out[5]), .e(not_23_out[2]),
    .d(not_23_out[3]), .c(not_23_out[4]));
  assign not_23_out = ~Hexdecoder_22_output_bus_1;  // NOT_Gate not_23, 7 bits wide
  Hexdecoder Hexdecoder_22 (
    .Input_bus_1(ARITHMETIC_LOGIC_UNIT_data_out_2), .E(1'b1), .Output_bus_1(Hexdecoder_22_output_bus_1));
  _7_Segment_Display #(.active("false"), .decimalPoint("false")) ALU_0 (
    .g(not_24_out[0]), .f(not_24_out[1]), .a(not_24_out[6]), .b(not_24_out[5]), .e(not_24_out[2]),
    .d(not_24_out[3]), .c(not_24_out[4]));
  assign not_24_out = ~Hexdecoder_23_output_bus_1;  // NOT_Gate not_24, 7 bits wide
  Hexdecoder Hexdecoder_23 (
    .Input_bus_1(ARITHMETIC_LOGIC_UNIT_data_out), .E(1'b1), .Output_bus_1(Hexdecoder_23_output_bus_1));

  // Notes on the sheet:
  //   REG_WRITE
  //   REG_READ
  //   INCREMENT
  //   RESET_PC
  //   contents of INSTRUCTIONS (hex, n*v repeats v):
  //   2000 2101 2202 23ab 241c c000 c100 c200 c300 c400 6012 c000 2100 6134 c100 2200 6201 c200 ffff
  //   READ
  //   MAIN BUS
  //   PROGRAM COUNTER
  //   Register Bus
  //   HLT Register
  //   Memory Address Register
  //   Accumulator
  //   Read MBR
  //   Memory Buffer Register
  //   OUTPUT
  //   TOO ANNOYING
endmodule

module PIPELINED_2STAGE (
);

  wire alu_pipe_1_sr, alu_pipe_1_sr_w, and_1_out, and_2_out, and_3_out, AUTO_p1, CLK_out,
       cu_2stage_1_alu_1_load_route, cu_2stage_1_buffer_select, cu_2stage_1_halt, cu_2stage_1_mar_load,
       cu_2stage_1_mwb_load, cu_2stage_1_operand_forward_r1, cu_2stage_1_operand_forward_r2,
       cu_2stage_1_output_load, cu_2stage_1_pc_clear, cu_2stage_1_pc_increment, cu_2stage_1_pc_load,
       cu_2stage_1_ram_write, cu_2stage_1_register_write, cu_2stage_1_rtb_load, cu_2stage_1_sr_c, d_ff_1_q,
       d_ff_1_qn, demultiplexer_1_out0, demultiplexer_1_out1, demultiplexer_2_out0, demultiplexer_2_out1,
       demultiplexer_3_out0, demultiplexer_3_out1, not_1_out, not_2_out, not_3_out, or_1_out, or_2_out,
       or_3_out, or_4_out, RESET_out, SR_q, STEP_out, undriven_2;
  wire [1:0] cu_2stage_1_register_write_route;
  wire [2:0] cu_2stage_1_alu_instruction;
  wire [3:0] cu_2stage_1_register_read_1_select, cu_2stage_1_register_read_2_select,
       cu_2stage_1_register_write_select;
  wire [6:0] Hexdecoder_5_output_bus_1, Hexdecoder_6_output_bus_1, not_4_out, not_5_out;
  wire [7:0] ACC_q, alu_pipe_1_data_out, cu_2stage_1_direct_value_s1, cu_2stage_1_direct_value_s2, MAR_A_q,
       MAR_B_q, multiplexer_1_out, multiplexer_2_out, multiplexer_3_out, multiplexer_4_out,
       multiplexer_5_out, multiplexer_6_out, multiplexer_7_out, multiplexer_8_out, MWB_A_q, MWB_B_q,
       OUTPUT_REGISTER_q, pc_1_current_value, RAM_data_out, REGISTERS_data_out_1, REGISTERS_data_out_2,
       RTB_A_q, RTB_B_q, undriven;
  wire [15:0] INSTRUCTIONS_data;

  CU_2STAGE cu_2stage_1 (
    .STATUS_REGISTER(SR_q), .RESET(RESET_out), .CLK(and_1_out), .INSTRUCTION_IN(INSTRUCTIONS_data),
    .MAR_LOAD(cu_2stage_1_mar_load), .OPERAND_FORWARD_R1(cu_2stage_1_operand_forward_r1),
    .OPERAND_FORWARD_R2(cu_2stage_1_operand_forward_r2), .MWB_LOAD(cu_2stage_1_mwb_load),
    .RTB_LOAD(cu_2stage_1_rtb_load), .ALU_1_LOAD_ROUTE(cu_2stage_1_alu_1_load_route),
    .PC_INCREMENT(cu_2stage_1_pc_increment), .ALU_INSTRUCTION(cu_2stage_1_alu_instruction),
    .PC_CLEAR(cu_2stage_1_pc_clear), .OUTPUT_LOAD(cu_2stage_1_output_load), .SR_C(cu_2stage_1_sr_c),
    .HALT(cu_2stage_1_halt), .PC_LOAD(cu_2stage_1_pc_load),
    .REGISTER_WRITE_SELECT(cu_2stage_1_register_write_select), .DIRECT_VALUE_S2(cu_2stage_1_direct_value_s2),
    .BUFFER_SELECT(cu_2stage_1_buffer_select), .REGISTER_WRITE(cu_2stage_1_register_write),
    .REGISTER_WRITE_ROUTE(cu_2stage_1_register_write_route), .RAM_WRITE(cu_2stage_1_ram_write),
    .REGISTER_READ_1_SELECT(cu_2stage_1_register_read_1_select),
    .REGISTER_READ_2_SELECT(cu_2stage_1_register_read_2_select), .DIRECT_VALUE_S1(cu_2stage_1_direct_value_s1));
  Demultiplexer demultiplexer_1 (
    .out0(demultiplexer_1_out0), .out1(demultiplexer_1_out1), .in(cu_2stage_1_rtb_load),
    .sel(cu_2stage_1_buffer_select));
  Multiplexer #(.select(2), .width(8)) multiplexer_1 (
    .in0(cu_2stage_1_direct_value_s2), .in1(multiplexer_2_out), .in2(ACC_q), .in3(RAM_data_out),
    .out(multiplexer_1_out), .sel(cu_2stage_1_register_write_route));
  or or_1 (or_1_out, and_2_out, and_3_out);
  and and_1 (and_1_out, or_1_out, d_ff_1_qn);
  D_Flip_Flop #(.trigger("falling")) d_ff_1 (
    .D(cu_2stage_1_halt), .clk(and_1_out), .Q(d_ff_1_q), .Qn(d_ff_1_qn), .preset(1'b0), .reset(RESET_out));
  Register RTB_A (.D(undriven), .en(demultiplexer_1_out0), .clk(and_1_out), .Q(RTB_A_q), .clr(RESET_out));
  Register RTB_B (.D(undriven), .en(demultiplexer_1_out1), .clk(and_1_out), .Q(RTB_B_q), .clr(RESET_out));
  and and_2 (and_2_out, STEP_out, not_1_out);
  and and_3 (and_3_out, AUTO_p1, CLK_out);
  LED HLT_REG (.in(d_ff_1_q));
  MEMORY_16B_2S REGISTERS (
    .RESET(RESET_out), .READ_ADDRESS_1(cu_2stage_1_register_read_1_select),
    .READ_ADDRESS_2(cu_2stage_1_register_read_2_select), .WRITE(cu_2stage_1_register_write),
    .DATA_IN(multiplexer_1_out), .WRITE_ADDRESS(cu_2stage_1_register_write_select), .CLK(and_1_out),
    .DATA_OUT_2(REGISTERS_data_out_2), .DATA_OUT_1(REGISTERS_data_out_1));
  not not_1 (not_1_out, AUTO_p1);
  LED AUTO_STATUS (.in(AUTO_p1));
  Clock CLK (.out(CLK_out));
  LED CLK_L (.in(CLK_out));
  Multiplexer #(.width(8)) multiplexer_2 (.in0(RTB_A_q), .in1(RTB_B_q), .out(multiplexer_2_out), .sel(not_2_out));
  not not_2 (not_2_out, cu_2stage_1_buffer_select);
  Button RESET (.out(RESET_out));
  Button STEP (.out(STEP_out));
  // DipSwitch #(.number(1)) AUTO: pin names not known; wires that end beside it: AUTO_p1
  or or_2 (or_2_out, cu_2stage_1_pc_clear, RESET_out);
  Multiplexer #(.width(8)) multiplexer_3 (
    .in0(REGISTERS_data_out_1), .in1(multiplexer_1_out), .out(multiplexer_3_out),
    .sel(cu_2stage_1_operand_forward_r1));
  Multiplexer #(.width(8)) multiplexer_4 (
    .in0(REGISTERS_data_out_2), .in1(multiplexer_1_out), .out(multiplexer_4_out),
    .sel(cu_2stage_1_operand_forward_r2));
  PC pc_1 (
    .INCREMENT(cu_2stage_1_pc_increment), .CLK(and_1_out), .RESET(or_2_out),
    .OVERWRITE_VALUE(cu_2stage_1_direct_value_s2), .OVERWRITE(cu_2stage_1_pc_load),
    .CURRENT_VALUE(pc_1_current_value));
  Multiplexer #(.width(8)) multiplexer_5 (
    .in0(cu_2stage_1_direct_value_s1), .in1(multiplexer_3_out), .out(multiplexer_5_out),
    .sel(cu_2stage_1_alu_1_load_route));
  Demultiplexer demultiplexer_2 (
    .out0(demultiplexer_2_out0), .out1(demultiplexer_2_out1), .in(cu_2stage_1_mwb_load),
    .sel(cu_2stage_1_buffer_select));
  Demultiplexer demultiplexer_3 (
    .out0(demultiplexer_3_out0), .out1(demultiplexer_3_out1), .in(cu_2stage_1_mar_load),
    .sel(cu_2stage_1_buffer_select));
  ROM #(.dataWidth(16)) INSTRUCTIONS (.addr(multiplexer_6_out), .data(INSTRUCTIONS_data));
  Multiplexer #(.width(8)) multiplexer_6 (
    .in0(pc_1_current_value), .in1(cu_2stage_1_direct_value_s2), .out(multiplexer_6_out),
    .sel(cu_2stage_1_pc_clear));
  Register OUTPUT_REGISTER (
    .D(undriven), .en(cu_2stage_1_output_load), .clk(and_1_out), .Q(OUTPUT_REGISTER_q), .clr(RESET_out));
  Register MWB_A (.D(multiplexer_3_out), .en(demultiplexer_2_out0), .clk(and_1_out), .Q(MWB_A_q), .clr(RESET_out));
  Register MWB_B (.D(multiplexer_3_out), .en(demultiplexer_2_out1), .clk(and_1_out), .Q(MWB_B_q), .clr(undriven_2));
  Register MAR_A (
    .D(cu_2stage_1_direct_value_s1), .en(demultiplexer_3_out0), .clk(and_1_out), .Q(MAR_A_q), .clr(RESET_out));
  Register MAR_B (
    .D(cu_2stage_1_direct_value_s1), .en(demultiplexer_3_out1), .clk(and_1_out), .Q(MAR_B_q), .clr(RESET_out));
  not not_3 (not_3_out, cu_2stage_1_buffer_select);
  Multiplexer #(.width(8)) multiplexer_7 (.in0(MWB_A_q), .in1(MWB_B_q), .out(multiplexer_7_out), .sel(not_3_out));
  Multiplexer #(.width(8)) multiplexer_8 (.in0(MAR_A_q), .in1(MAR_B_q), .out(multiplexer_8_out), .sel(not_3_out));
  or or_3 (or_3_out, cu_2stage_1_alu_instruction[0], cu_2stage_1_alu_instruction[1], cu_2stage_1_alu_instruction[2]);
  ALU_PIPE alu_pipe_1 (
    .INSTR(cu_2stage_1_alu_instruction), .INPUT_A(multiplexer_5_out), .INPUT_B(multiplexer_4_out),
    .DATA_OUT(alu_pipe_1_data_out), .SR_W(alu_pipe_1_sr_w), .SR(alu_pipe_1_sr));
  MEMORY_256B RAM (
    .READ_ADDRESS(multiplexer_8_out), .WRITE(cu_2stage_1_ram_write), .WRITE_ADDRESS(multiplexer_8_out),
    .DATA_IN(multiplexer_7_out), .RESET(RESET_out), .CLK(and_1_out), .DATA_OUT(RAM_data_out));
  Register ACC (.D(alu_pipe_1_data_out), .en(or_3_out), .clk(and_1_out), .Q(ACC_q));  // open: clr
  Register #(.width(1)) SR (.D(alu_pipe_1_sr_w), .en(alu_pipe_1_sr), .clk(and_1_out), .Q(SR_q), .clr(or_4_out));
  or or_4 (or_4_out, RESET_out, cu_2stage_1_sr_c);
  _7_Segment_Display #(.active("false"), .decimalPoint("false")) OUTPUT_1 (
    .g(not_4_out[0]), .f(not_4_out[1]), .a(not_4_out[6]), .b(not_4_out[5]), .e(not_4_out[2]),
    .d(not_4_out[3]), .c(not_4_out[4]));
  assign not_4_out = ~Hexdecoder_5_output_bus_1;  // NOT_Gate not_4, 7 bits wide
  assign not_5_out = ~Hexdecoder_6_output_bus_1;  // NOT_Gate not_5, 7 bits wide
  Hexdecoder Hexdecoder_5 (.Input_bus_1(OUTPUT_REGISTER_q[7:4]), .E(1'b1), .Output_bus_1(Hexdecoder_5_output_bus_1));
  Hexdecoder Hexdecoder_6 (.Input_bus_1(OUTPUT_REGISTER_q[3:0]), .E(1'b1), .Output_bus_1(Hexdecoder_6_output_bus_1));
  _7_Segment_Display #(.active("false"), .decimalPoint("false")) OUTPUT_0 (
    .g(not_5_out[0]), .f(not_5_out[1]), .a(not_5_out[6]), .b(not_5_out[5]), .e(not_5_out[2]),
    .d(not_5_out[3]), .c(not_5_out[4]));

  // Notes on the sheet:
  //   HLT Register
  //   CLK
  //   RESET
  //   contents of INSTRUCTIONS (hex, n*v repeats v):
  //   210f 220f 5012 ffff
  //   RAM_W
  //   OUTPUT
endmodule

module CU (
  input  Run,
  input  CLK,
  input  [15:0] INSTRUCTION,
  input  SR,
  output [4:0] RING_COUNTER,
  output LOAD_CIR,
  output INCREMENT_PC,
  output LOAD_OUT,
  output LOAD_MAR,
  output READ_RAM,
  output WRITE_RAM,
  output READ_MBR,
  output READ_ACC,
  output LOAD_ACC,
  output ALU_READ,
  output REGISTER_READ,
  output [3:0] REGISTER_READ_SELECT,
  output REGISTER_WRITE,
  output [3:0] REGISTER_WRITE_SELECT,
  output XY_E,
  output [7:0] xy,
  output RESET_PC,
  output LOAD_PC,
  output HLT,
  output [2:0] ALU_INSTR
);

  wire and_1_out, and_2_out, and_3_out, and_4_out, and_5_out, and_6_out, and_7_out, and_8_out, and_9_out,
       and_10_out, and_11_out, and_12_out, and_13_out, and_14_out, and_15_out, and_17_out, and_18_out,
       and_19_out, and_22_out, and_23_out, and_24_out, and_26_out, and_27_out, and_28_out, and_29_out,
       and_30_out, and_31_out, and_32_out, and_33_out, and_34_out, and_35_out, and_36_out, and_37_out,
       and_38_out, and_39_out, and_40_out, and_41_out, and_42_out, and_43_out, and_44_out, and_45_out,
       and_46_out, and_47_out, and_48_out, and_49_out, and_52_out, and_53_out, and_54_out, and_55_out,
       and_56_out, d_ff_6_q, d_ff_7_q, nor_1_out, not_1_out, not_2_out, not_3_out, not_4_out, not_5_out,
       or_1_out, or_2_out, or_3_out, or_4_out, or_5_out, or_6_out, or_7_out, or_8_out, or_9_out,
       PEncoder_2_1_o_e, PEncoder_2_2_o_e;
  wire [1:0] PEncoder_2_1_o_0, PEncoder_2_2_o_0;

  not not_1 (not_1_out, INSTRUCTION[15]);
  not not_2 (not_2_out, INSTRUCTION[14]);
  and and_1 (and_1_out, not_1_out, not_2_out, not_3_out, not_4_out);
  and and_2 (and_2_out, not_1_out, not_2_out, not_3_out, INSTRUCTION[12]);
  and and_3 (and_3_out, not_1_out, not_2_out, INSTRUCTION[13], not_4_out);
  and and_4 (and_4_out, not_1_out, not_2_out, INSTRUCTION[13], INSTRUCTION[12]);
  and and_5 (and_5_out, not_1_out, INSTRUCTION[14], not_3_out, not_4_out);
  and and_6 (and_6_out, not_1_out, INSTRUCTION[14], not_3_out, INSTRUCTION[12]);
  and and_7 (and_7_out, not_1_out, INSTRUCTION[14], INSTRUCTION[13], not_4_out);
  and and_8 (and_8_out, not_1_out, INSTRUCTION[14], INSTRUCTION[13], INSTRUCTION[12]);
  and and_9 (and_9_out, INSTRUCTION[15], not_2_out, not_3_out, not_4_out);
  and and_10 (and_10_out, INSTRUCTION[15], not_2_out, not_3_out, INSTRUCTION[12]);
  and and_11 (and_11_out, INSTRUCTION[15], not_2_out, INSTRUCTION[13], not_4_out);
  and and_12 (and_12_out, INSTRUCTION[15], not_2_out, INSTRUCTION[13], INSTRUCTION[12]);
  and and_13 (and_13_out, INSTRUCTION[15], INSTRUCTION[14], not_3_out, not_4_out);
  and and_14 (and_14_out, INSTRUCTION[15], INSTRUCTION[14], not_3_out, INSTRUCTION[12]);
  and and_15 (and_15_out, INSTRUCTION[15], INSTRUCTION[14], INSTRUCTION[13], not_4_out);
  and and_16 (HLT, INSTRUCTION[15], INSTRUCTION[14], INSTRUCTION[13], INSTRUCTION[12]);
  not not_3 (not_3_out, INSTRUCTION[13]);
  not not_4 (not_4_out, INSTRUCTION[12]);
  PEncoder_2 PEncoder_2_1 (
    .I_3(or_3_out), .I_2(or_2_out), .I_1(or_1_out), .I_0(and_48_out), .O_E(PEncoder_2_1_o_e),
    .O_0(PEncoder_2_1_o_0[0]), .O_1(PEncoder_2_1_o_0[1]));
  or or_1 (or_1_out, WRITE_RAM, and_45_out, and_47_out, LOAD_OUT);
  or or_2 (or_2_out, and_27_out, and_29_out, and_32_out, and_36_out, and_39_out, and_42_out);
  or or_3 (or_3_out, and_30_out, and_33_out, and_35_out, and_38_out, and_41_out);
  or or_4 (or_4_out, READ_MBR, and_22_out, and_31_out, and_34_out, and_37_out, and_40_out, and_43_out, and_46_out);
  and and_17 (and_17_out, and_1_out, RING_COUNTER[1]);
  and and_18 (and_18_out, and_1_out, RING_COUNTER[2]);
  and and_19 (and_19_out, RING_COUNTER[1], and_2_out);
  PEncoder_2 PEncoder_2_2 (
    .I_3(or_5_out), .I_2(1'b0), .I_1(or_4_out), .I_0(1'b0), .O_E(PEncoder_2_2_o_e),
    .O_0(PEncoder_2_2_o_0[0]), .O_1(PEncoder_2_2_o_0[1]));
  Multiplexer #(.enable("true"), .select(2), .width(4)) multiplexer_1 (
    .in0(4'b0000), .in1(INSTRUCTION[11:8]), .in2(INSTRUCTION[7:4]), .in3(INSTRUCTION[3:0]),
    .out(REGISTER_READ_SELECT), .sel(PEncoder_2_1_o_0), .en(PEncoder_2_1_o_e));
  Multiplexer #(.enable("true"), .select(2), .width(4)) multiplexer_2 (
    .in0(4'b0000), .in1(INSTRUCTION[11:8]), .in2(INSTRUCTION[7:4]), .in3(INSTRUCTION[3:0]),
    .out(REGISTER_WRITE_SELECT), .sel(PEncoder_2_2_o_0), .en(PEncoder_2_2_o_e));
  D_Flip_Flop #(.trigger("falling")) d_ff_1 (
    .D(RING_COUNTER[4]), .clk(CLK), .Q(LOAD_CIR), .preset(or_6_out), .reset(1'b0));  // open: Qn
  and and_20 (READ_RAM, RING_COUNTER[2], and_2_out);
  and and_21 (READ_MBR, RING_COUNTER[3], and_2_out);
  D_Flip_Flop #(.trigger("falling")) d_ff_2 (
    .D(LOAD_CIR), .clk(CLK), .Q(RING_COUNTER[1]), .preset(1'b0), .reset(or_6_out));  // open: Qn
  and and_22 (and_22_out, and_3_out, RING_COUNTER[1]);
  and and_23 (and_23_out, and_3_out, RING_COUNTER[2]);
  or or_5 (or_5_out, and_27_out, and_44_out);
  D_Flip_Flop #(.trigger("falling")) d_ff_3 (
    .D(RING_COUNTER[1]), .clk(CLK), .Q(RING_COUNTER[2]), .preset(1'b0), .reset(or_6_out));  // open: Qn
  and and_24 (and_24_out, and_4_out, RING_COUNTER[1]);
  and and_25 (WRITE_RAM, and_4_out, RING_COUNTER[2]);
  and and_26 (and_26_out, and_4_out, RING_COUNTER[3]);
  D_Flip_Flop #(.trigger("falling")) d_ff_4 (
    .D(RING_COUNTER[2]), .clk(CLK), .Q(RING_COUNTER[3]), .preset(1'b0), .reset(or_6_out));  // open: Qn
  and and_27 (and_27_out, and_5_out, RING_COUNTER[1]);
  and and_28 (and_28_out, and_5_out, RING_COUNTER[2]);
  D_Flip_Flop #(.trigger("falling")) d_ff_5 (
    .D(RING_COUNTER[3]), .clk(CLK), .Q(RING_COUNTER[4]), .preset(1'b0), .reset(or_6_out));  // open: Qn
  and and_29 (and_29_out, and_6_out, RING_COUNTER[1]);
  and and_30 (and_30_out, and_6_out, RING_COUNTER[2]);
  and and_31 (and_31_out, and_6_out, RING_COUNTER[3]);
  nor nor_1 (nor_1_out, and_30_out, and_32_out, and_36_out, and_39_out, and_42_out, and_45_out, and_48_out);
  PEncoder_3 PCE (
    .I_7(and_48_out), .I_6(and_45_out), .I_5(and_42_out), .I_4(and_39_out), .I_3(and_36_out),
    .I_2(and_32_out), .I_1(and_30_out), .I_0(nor_1_out), .O_2(ALU_INSTR[2]), .O_1(ALU_INSTR[1]),
    .O_0(ALU_INSTR[0]));  // open: O_E
  and and_32 (and_32_out, and_7_out, RING_COUNTER[2]);
  and and_33 (and_33_out, and_7_out, RING_COUNTER[1]);
  and and_34 (and_34_out, and_7_out, RING_COUNTER[3]);
  and and_35 (and_35_out, and_8_out, RING_COUNTER[1]);
  and and_36 (and_36_out, and_8_out, RING_COUNTER[2]);
  and and_37 (and_37_out, and_8_out, RING_COUNTER[3]);
  and and_38 (and_38_out, and_9_out, RING_COUNTER[1]);
  and and_39 (and_39_out, and_9_out, RING_COUNTER[2]);
  and and_40 (and_40_out, and_9_out, RING_COUNTER[3]);
  and and_41 (and_41_out, and_10_out, RING_COUNTER[1]);
  and and_42 (and_42_out, and_10_out, RING_COUNTER[2]);
  and and_43 (and_43_out, and_10_out, RING_COUNTER[3]);
  and and_44 (and_44_out, and_11_out, RING_COUNTER[1]);
  and and_45 (and_45_out, and_11_out, RING_COUNTER[2]);
  or or_6 (or_6_out, Run, or_9_out);
  and and_46 (and_46_out, and_11_out, RING_COUNTER[3]);
  and and_47 (and_47_out, and_12_out, RING_COUNTER[1]);
  and and_48 (and_48_out, and_12_out, RING_COUNTER[2]);
  and and_49 (and_49_out, and_12_out, RING_COUNTER[3]);
  and and_50 (LOAD_OUT, and_13_out, RING_COUNTER[1]);
  and and_51 (RESET_PC, and_49_out, SR);
  and and_52 (and_52_out, and_13_out, RING_COUNTER[2]);
  and and_53 (and_53_out, and_14_out, RING_COUNTER[1]);
  LED CU_SR (.in(SR));
  and and_54 (and_54_out, and_14_out, RING_COUNTER[2]);
  and and_55 (and_55_out, and_15_out, RING_COUNTER[1]);
  and and_56 (and_56_out, and_15_out, RING_COUNTER[2]);
  or or_7 (or_7_out, and_55_out, and_53_out, LOAD_OUT, and_27_out, WRITE_RAM, and_22_out, and_17_out);
  or or_8 (or_8_out, RING_COUNTER[4], or_7_out);
  not not_5 (not_5_out, d_ff_7_q);
  D_Flip_Flop #(.trigger("high")) d_ff_6 (
    .D(RESET_PC), .clk(RESET_PC), .Q(d_ff_6_q), .preset(1'b0), .reset(LOAD_CIR));  // open: Qn
  and and_57 (INCREMENT_PC, or_8_out, not_5_out);
  or or_9 (or_9_out, and_56_out, and_54_out, and_52_out, and_28_out, and_26_out, and_23_out, and_18_out);
  or or_10 (XY_E, and_19_out, and_22_out, and_24_out, and_44_out, LOAD_PC);
  and and_58 (LOAD_PC, d_ff_6_q, RING_COUNTER[4]);
  D_Flip_Flop #(.trigger("high")) d_ff_7 (
    .D(RESET_PC), .clk(and_49_out), .Q(d_ff_7_q), .preset(1'b0), .reset(LOAD_CIR));  // open: Qn
  or or_11 (REGISTER_WRITE, READ_MBR, and_22_out, and_27_out, and_31_out, and_34_out, and_37_out, and_40_out, and_43_out, and_46_out);
  or or_12 (REGISTER_READ, WRITE_RAM, and_27_out, and_29_out, and_30_out, and_33_out, and_32_out, and_35_out, and_36_out, and_38_out, and_39_out, and_41_out, and_42_out, and_47_out, and_45_out, and_48_out, LOAD_OUT);
  or or_13 (LOAD_MAR, and_19_out, and_24_out);
  or or_14 (LOAD_ACC, and_29_out, and_33_out, and_35_out, and_38_out, and_41_out, and_44_out, and_47_out);
  or or_15 (ALU_READ, and_31_out, and_34_out, and_37_out, and_40_out, and_43_out, and_46_out);

  assign READ_ACC = 1'b0;
  assign RING_COUNTER[0] = LOAD_CIR;
  assign xy = INSTRUCTION[7:0];

  // Notes on the sheet:
  //   0: NO OPERATION
  //   4: MOVE REG TO REG
  //   5: ADD (TC)
  //   6: ADD (FP)
  //   7: OR
  //   8: AND
  //   9: XOR
  //   A: Rotate
  //   B: JUMP
  //   C: OUTPUT
  //   D: NO OPERATION
  //   E: NO OPERATION
  //   F: HALT
  //   1: LOAD REG WITH MEMORY
  //   2: LOAD REG WITH VALUE
  //   3: LOAD MEMORY WITH REG
  //   0
  //   READ
  //   WRITE
  //   1
  //   RING COUNTER
  //   2
  //   3
  //   4
  //   5
  //   6
  //   7
  //   8
  //   9
  //   A
  //   B
  //   C
  //   D
  //   E
  //   F
  //   EARLY INCREMENT PC
  //   EARLY RESET RC
  //   CURRENTLY UNUSED
  //   ALU INSTRUCTION SET
  //   000 : -
  //   001 : ADD (TC)
  //   010 : ADD (FP)
  //   011 : OR
  //   100 : AND
  //   101 : XOR
  //   110 : RIGHT ROTATE
  //   111 : EQ
endmodule

module CU_2STAGE (
  input  [15:0] INSTRUCTION_IN,
  input  RESET,
  input  CLK,
  input  STATUS_REGISTER,
  output OPERAND_FORWARD_R1,
  output OPERAND_FORWARD_R2,
  output BUFFER_SELECT,
  output SR_C,
  output PC_CLEAR,
  output PC_LOAD,
  output [3:0] REGISTER_READ_1_SELECT,
  output PC_INCREMENT,
  output [3:0] REGISTER_READ_2_SELECT,
  output [7:0] DIRECT_VALUE_S2,
  output [7:0] DIRECT_VALUE_S1,
  output [3:0] REGISTER_WRITE_SELECT,
  output MAR_LOAD,
  output MWB_LOAD,
  output ALU_1_LOAD_ROUTE,
  output HALT,
  output OUTPUT_LOAD,
  output RAM_WRITE,
  output RTB_LOAD,
  output [1:0] REGISTER_WRITE_ROUTE,
  output [2:0] ALU_INSTRUCTION,
  output REGISTER_WRITE
);

  wire and_2_out, and_6_out, and_7_out, and_8_out, and_9_out, and_10_out, and_11_out, and_12_out, and_22_out,
       and_23_out, and_25_out, and_26_out, and_27_out, and_28_out, and_29_out, and_30_out, and_31_out,
       d_ff_1_qn, not_1_out, not_2_out, not_3_out, not_4_out, not_5_out, not_6_out, not_7_out, not_8_out,
       not_9_out, not_10_out, not_11_out, not_12_out, or_1_out, or_2_out, or_5_out, xnor_1_out, xnor_2_out,
       xnor_3_out, xnor_4_out, xnor_5_out, xnor_6_out, xnor_7_out, xnor_8_out;
  wire [15:0] multiplexer_1_out;
  wire [15:8] S1_INSTRUCTION_q, S2_INSTRUCTION_q;

  Multiplexer #(.width(16)) multiplexer_1 (
    .in0(INSTRUCTION_IN), .in1({16{1'b0}}), .out(multiplexer_1_out), .sel(and_12_out));
  not not_1 (not_1_out, CLK);
  Register #(.width(16)) S1_INSTRUCTION (
    .D(multiplexer_1_out), .en(not_1_out), .clk(not_1_out), .Q({S1_INSTRUCTION_q, DIRECT_VALUE_S1}),
    .clr(RESET));
  not not_2 (not_2_out, and_12_out);
  Multiplexer #(.enable("true"), .width(4)) multiplexer_2 (
    .in0(DIRECT_VALUE_S1[7:4]), .in1(S1_INSTRUCTION_q[11:8]), .out(REGISTER_READ_1_SELECT), .sel(or_2_out),
    .en(not_2_out));
  Multiplexer #(.width(4)) multiplexer_3 (
    .in0(DIRECT_VALUE_S1[3:0]), .in1(S1_INSTRUCTION_q[11:8]), .out(REGISTER_READ_2_SELECT), .sel(or_1_out));
  not not_3 (not_3_out, S1_INSTRUCTION_q[14]);
  not not_4 (not_4_out, S1_INSTRUCTION_q[13]);
  not not_5 (not_5_out, S1_INSTRUCTION_q[15]);
  not not_6 (not_6_out, S1_INSTRUCTION_q[12]);
  xnor xnor_1 (xnor_1_out, REGISTER_READ_1_SELECT[0], REGISTER_WRITE_SELECT[0]);
  xnor xnor_2 (xnor_2_out, REGISTER_READ_1_SELECT[1], REGISTER_WRITE_SELECT[1]);
  xnor xnor_3 (xnor_3_out, REGISTER_READ_1_SELECT[2], REGISTER_WRITE_SELECT[2]);
  xnor xnor_4 (xnor_4_out, REGISTER_READ_1_SELECT[3], REGISTER_WRITE_SELECT[3]);
  xnor xnor_5 (xnor_5_out, REGISTER_WRITE_SELECT[0], REGISTER_READ_2_SELECT[0]);
  xnor xnor_6 (xnor_6_out, REGISTER_WRITE_SELECT[1], REGISTER_READ_2_SELECT[1]);
  xnor xnor_7 (xnor_7_out, REGISTER_WRITE_SELECT[2], REGISTER_READ_2_SELECT[2]);
  xnor xnor_8 (xnor_8_out, REGISTER_WRITE_SELECT[3], REGISTER_READ_2_SELECT[3]);
  // AND_Gate and_1 has open pins: in0=not_6_out, in1=not_4_out, in2=not_3_out, in3=not_5_out, out=open
  and and_2 (and_2_out, S1_INSTRUCTION_q[12], not_4_out, not_3_out, not_5_out);
  // AND_Gate and_3 has open pins: in0=not_6_out, in1=S1_INSTRUCTION_q[13], in2=not_3_out, in3=not_5_out, out=open
  and and_4 (MWB_LOAD, S1_INSTRUCTION_q[12], S1_INSTRUCTION_q[13], not_3_out);
  and and_5 (RTB_LOAD, not_6_out, not_4_out, S1_INSTRUCTION_q[14], not_5_out);
  and and_6 (and_6_out, S1_INSTRUCTION_q[12], not_4_out, S1_INSTRUCTION_q[14], not_5_out);
  and and_7 (and_7_out, not_6_out, S1_INSTRUCTION_q[13], S1_INSTRUCTION_q[14], not_5_out);
  and and_8 (and_8_out, S1_INSTRUCTION_q[12], S1_INSTRUCTION_q[13], S1_INSTRUCTION_q[14], not_5_out);
  and and_9 (and_9_out, not_6_out, not_4_out, not_3_out, S1_INSTRUCTION_q[15]);
  and and_10 (and_10_out, S1_INSTRUCTION_q[12], not_4_out, not_3_out, S1_INSTRUCTION_q[15]);
  and and_11 (and_11_out, not_6_out, S1_INSTRUCTION_q[13], not_3_out, S1_INSTRUCTION_q[15]);
  and and_12 (and_12_out, S1_INSTRUCTION_q[12], S1_INSTRUCTION_q[13], not_3_out, S1_INSTRUCTION_q[15]);
  and and_13 (OUTPUT_LOAD, not_6_out, not_4_out, S1_INSTRUCTION_q[14], S1_INSTRUCTION_q[15]);
  // AND_Gate and_14 has open pins: in0=S1_INSTRUCTION_q[12], in1=not_4_out, in2=S1_INSTRUCTION_q[14], in3=S1_INSTRUCTION_q[15], out=open
  // AND_Gate and_15 has open pins: in0=not_6_out, in1=S1_INSTRUCTION_q[13], in2=S1_INSTRUCTION_q[14], in3=S1_INSTRUCTION_q[15], out=open
  and and_16 (HALT, S1_INSTRUCTION_q[12], S1_INSTRUCTION_q[13], S1_INSTRUCTION_q[14], S1_INSTRUCTION_q[15]);
  or or_1 (or_1_out, and_11_out, and_12_out);
  or or_2 (or_2_out, MWB_LOAD, OUTPUT_LOAD);
  and and_17 (OPERAND_FORWARD_R1, xnor_1_out, xnor_2_out, xnor_3_out, xnor_4_out);
  and and_18 (OPERAND_FORWARD_R2, xnor_5_out, xnor_6_out, xnor_7_out, xnor_8_out);
  or or_3 (MAR_LOAD, and_2_out, MWB_LOAD);
  or or_4 (ALU_1_LOAD_ROUTE, and_6_out, and_7_out, and_8_out, and_9_out, and_10_out, and_12_out);
  D_Flip_Flop SR_CLEAR_REG (.D(STATUS_REGISTER), .clk(not_1_out), .Q(SR_C));  // open: Qn, preset, reset
  not not_7 (not_7_out, and_12_out);
  not not_8 (not_8_out, 1'b0);
  and and_19 (PC_INCREMENT, not_7_out, not_8_out);
  PEncoder_3 pencoder_3_1 (
    .I_7(and_12_out), .I_6(and_11_out), .I_5(and_10_out), .I_4(and_9_out), .I_3(and_8_out), .I_2(and_7_out),
    .I_1(and_6_out), .O_2(ALU_INSTRUCTION[2]), .O_1(ALU_INSTRUCTION[1]), .O_0(ALU_INSTRUCTION[0]));  // open: I_0, O_E
  and and_20 (PC_LOAD, not_1_out, STATUS_REGISTER);
  Register #(.width(16)) S2_INSTRUCTION (
    .D({S1_INSTRUCTION_q, DIRECT_VALUE_S1}), .en(not_1_out), .clk(not_1_out),
    .Q({S2_INSTRUCTION_q, DIRECT_VALUE_S2}), .clr(RESET));
  Multiplexer #(.width(4)) multiplexer_4 (
    .in0(S2_INSTRUCTION_q[11:8]), .in1(DIRECT_VALUE_S2[3:0]), .out(REGISTER_WRITE_SELECT), .sel(and_25_out));
  not not_9 (not_9_out, S2_INSTRUCTION_q[15]);
  not not_10 (not_10_out, S2_INSTRUCTION_q[14]);
  not not_11 (not_11_out, S2_INSTRUCTION_q[13]);
  not not_12 (not_12_out, S2_INSTRUCTION_q[12]);
  D_Flip_Flop d_ff_1 (
    .D(d_ff_1_qn), .clk(not_1_out), .Q(BUFFER_SELECT), .Qn(d_ff_1_qn), .reset(RESET));  // open: preset
  // AND_Gate and_21 has open pins: in0=not_12_out, in1=not_11_out, in2=not_10_out, in3=not_9_out, out=open
  and and_22 (and_22_out, S2_INSTRUCTION_q[12], not_11_out, not_10_out, not_9_out);
  and and_23 (and_23_out, not_12_out, S2_INSTRUCTION_q[13], not_10_out, not_9_out);
  and and_24 (RAM_WRITE, S2_INSTRUCTION_q[12], S2_INSTRUCTION_q[13], not_10_out);
  and and_25 (and_25_out, not_12_out, not_11_out, S2_INSTRUCTION_q[14], not_9_out);
  and and_26 (and_26_out, S2_INSTRUCTION_q[12], not_11_out, S2_INSTRUCTION_q[14], not_9_out);
  and and_27 (and_27_out, not_12_out, S2_INSTRUCTION_q[13], S2_INSTRUCTION_q[14], not_9_out);
  and and_28 (and_28_out, S2_INSTRUCTION_q[12], S2_INSTRUCTION_q[13], S2_INSTRUCTION_q[14], not_9_out);
  and and_29 (and_29_out, not_12_out, not_11_out, not_10_out, S2_INSTRUCTION_q[15]);
  and and_30 (and_30_out, S2_INSTRUCTION_q[12], not_11_out, not_10_out, S2_INSTRUCTION_q[15]);
  and and_31 (and_31_out, not_12_out, S2_INSTRUCTION_q[13], not_10_out, S2_INSTRUCTION_q[15]);
  // AND_Gate and_32 has open pins: in0=S2_INSTRUCTION_q[12], in1=S2_INSTRUCTION_q[13], in2=not_10_out, in3=S2_INSTRUCTION_q[15], out=open
  // AND_Gate and_33 has open pins: in0=not_12_out, in1=not_11_out, in2=S2_INSTRUCTION_q[14], in3=S2_INSTRUCTION_q[15], out=open
  // AND_Gate and_34 has open pins: in0=S2_INSTRUCTION_q[12], in1=not_11_out, in2=S2_INSTRUCTION_q[14], in3=S2_INSTRUCTION_q[15], out=open
  // AND_Gate and_35 has open pins: in0=not_12_out, in1=S2_INSTRUCTION_q[13], in2=S2_INSTRUCTION_q[14], in3=S2_INSTRUCTION_q[15], out=open
  // AND_Gate and_36 has open pins: in0=S2_INSTRUCTION_q[12], in1=S2_INSTRUCTION_q[13], in2=S2_INSTRUCTION_q[14], in3=S2_INSTRUCTION_q[15], out=open
  or or_5 (or_5_out, and_26_out, and_27_out, and_28_out, and_29_out, and_30_out, and_31_out);
  PEncoder_2 pencoder_2_1 (
    .I_3(and_22_out), .I_2(or_5_out), .I_1(and_25_out), .I_0(and_23_out), .O_E(REGISTER_WRITE),
    .O_0(REGISTER_WRITE_ROUTE[0]), .O_1(REGISTER_WRITE_ROUTE[1]));

  assign PC_CLEAR = STATUS_REGISTER;

  // Other names for the same wires on the sheet: REG_READ_1[3:0] = REGISTER_READ_1_SELECT;
  //   REG_READ_2[3:0] = REGISTER_READ_2_SELECT; REG_WRITE[3:0] = REGISTER_WRITE_SELECT

  // Notes on the sheet:
  //   5: ADD (TC)
  //   6: ADD (FP)
  //   7: OR
  //   8: AND
  //   9: XOR
  //   A: Rotate
  //   B: JUMP
  //   C: OUTPUT
  //   F: HALT
  //   ALU INSTRUCTION SET
  //   000 : -
  //   001 : ADD (TC)
  //   010 : ADD (FP)
  //   011 : OR
  //   100 : AND
  //   101 : XOR
  //   110 : RIGHT ROTATE
  //   111 : EQ
  //   0: NO OPERATION
  //   1: LOAD REG WITH MEMORY
  //   2: LOAD REG WITH VALUE
  //   3: LOAD MEMORY WITH REG
  //   4: MOVE REG TO REG
  //   D: NO OPERATION
  //   E: NO OPERATION
  //   BUBBLE
  //   OPERAND FORWARDING LOGIC
  //   0
  //   NOTHING
  //   1
  //   2
  //   3
  //   4
  //   5
  //   6
  //   7
  //   8
  //   9
  //   A
  //   B
  //   C
  //   D
  //   E
  //   F
  //   0
  //   1
  //   2
  //   3
  //   4
  //   5
  //   6
  //   7
  //   8
  //   9
  //   A
  //   B
  //   C
  //   D
  //   E
  //   F
endmodule

module PC (
  input  OVERWRITE,
  input  [7:0] OVERWRITE_VALUE,
  input  INCREMENT,
  input  CLK,
  input  RESET,
  output [7:0] CURRENT_VALUE
);

  wire and_1_out, and_3_out, and_4_out, and_5_out, and_6_out, and_7_out, and_8_out;
  wire [7:0] and_2_out;

  and and_1 (and_1_out, INCREMENT, CLK);
  J_K_Flip_Flop #(.trigger("falling")) j_k_ff_1 (
    .J(1'b1), .K(1'b1), .clk(and_1_out), .Q(CURRENT_VALUE[0]), .preset(and_2_out[0]), .reset(RESET));  // open: Qn
  assign and_2_out = {8{OVERWRITE}} & OVERWRITE_VALUE;  // AND_Gate and_2, 8 bits wide
  J_K_Flip_Flop #(.trigger("falling")) j_k_ff_2 (
    .J(CURRENT_VALUE[0]), .K(CURRENT_VALUE[0]), .clk(and_1_out), .Q(CURRENT_VALUE[1]), .preset(and_2_out[1]),
    .reset(RESET));  // open: Qn
  and and_3 (and_3_out, CURRENT_VALUE[1], CURRENT_VALUE[0]);
  J_K_Flip_Flop #(.trigger("falling")) j_k_ff_3 (
    .J(and_3_out), .K(and_3_out), .clk(and_1_out), .Q(CURRENT_VALUE[2]), .preset(and_2_out[2]), .reset(RESET));  // open: Qn
  J_K_Flip_Flop #(.trigger("falling")) j_k_ff_4 (
    .J(and_4_out), .K(and_4_out), .clk(and_1_out), .Q(CURRENT_VALUE[3]), .preset(and_2_out[3]), .reset(RESET));  // open: Qn
  and and_4 (and_4_out, CURRENT_VALUE[2], and_3_out);
  and and_5 (and_5_out, CURRENT_VALUE[3], and_4_out);
  J_K_Flip_Flop #(.trigger("falling")) j_k_ff_5 (
    .J(and_5_out), .K(and_5_out), .clk(and_1_out), .Q(CURRENT_VALUE[4]), .preset(and_2_out[4]), .reset(RESET));  // open: Qn
  J_K_Flip_Flop #(.trigger("falling")) j_k_ff_6 (
    .J(and_6_out), .K(and_6_out), .clk(and_1_out), .Q(CURRENT_VALUE[5]), .preset(and_2_out[5]), .reset(RESET));  // open: Qn
  and and_6 (and_6_out, CURRENT_VALUE[4], and_5_out);
  J_K_Flip_Flop #(.trigger("falling")) j_k_ff_7 (
    .J(and_7_out), .K(and_7_out), .clk(and_1_out), .Q(CURRENT_VALUE[6]), .preset(and_2_out[6]), .reset(RESET));  // open: Qn
  and and_7 (and_7_out, CURRENT_VALUE[5], and_6_out);
  and and_8 (and_8_out, CURRENT_VALUE[6], and_7_out);
  J_K_Flip_Flop #(.trigger("falling")) j_k_ff_8 (
    .J(and_8_out), .K(and_8_out), .clk(and_1_out), .Q(CURRENT_VALUE[7]), .preset(and_2_out[7]), .reset(RESET));  // open: Qn

  // Notes on the sheet:
  //   READ
  //   PROGRAM COUNTER
endmodule

module OLD_ALU (
  input  READ,
  input  [2:0] INSTR,
  input  [7:0] DATA_IN,
  input  [7:0] ACCUMULATOR,
  input  CLK,
  output [7:0] DATA_OUT,
  output SR_W,
  output SR
);

  wire and_1_out, and_2_out, and_3_out, and_4_out, and_13_out, and_14_out, and_16_out, not_1_out, not_2_out,
       not_3_out, or_9_out, xnor_1_out, xnor_2_out, xnor_3_out, xnor_4_out, xnor_5_out, xnor_6_out,
       xnor_7_out, xnor_8_out;
  wire [7:0] and_5_out, controlled_buffer_1_out, fp_adder_1_o, or_1_out, register_1_q, RightRotator_1_o,
       TCAdder_1_o, xor_1_out;

  not not_1 (not_1_out, INSTR[2]);
  not not_2 (not_2_out, INSTR[1]);
  not not_3 (not_3_out, INSTR[0]);
  and and_1 (and_1_out, INSTR[0], not_2_out, not_1_out);
  TCAdder TCAdder_1 (.A(DATA_IN), .B(ACCUMULATOR), .C(1'b0), .O(TCAdder_1_o));  // open: S
  and and_2 (and_2_out, not_3_out, INSTR[1], not_1_out);
  FP_Adder fp_adder_1 (.A(DATA_IN), .B(ACCUMULATOR), .O(fp_adder_1_o));
  and and_3 (and_3_out, INSTR[0], INSTR[1], not_1_out);
  or or_1 (or_1_out[0], ACCUMULATOR[0], DATA_IN[0]);
  or or_2 (or_1_out[1], ACCUMULATOR[1], DATA_IN[1]);
  or or_3 (or_1_out[2], ACCUMULATOR[2], DATA_IN[2]);
  or or_4 (or_1_out[3], ACCUMULATOR[3], DATA_IN[3]);
  or or_5 (or_1_out[4], ACCUMULATOR[4], DATA_IN[4]);
  or or_6 (or_1_out[5], ACCUMULATOR[5], DATA_IN[5]);
  or or_7 (or_1_out[6], ACCUMULATOR[6], DATA_IN[6]);
  or or_8 (or_1_out[7], ACCUMULATOR[7], DATA_IN[7]);
  and and_4 (and_4_out, not_3_out, not_2_out, INSTR[2]);
  and and_5 (and_5_out[0], ACCUMULATOR[0], DATA_IN[0]);
  and and_6 (and_5_out[1], ACCUMULATOR[1], DATA_IN[1]);
  and and_7 (and_5_out[2], ACCUMULATOR[2], DATA_IN[2]);
  and and_8 (and_5_out[3], ACCUMULATOR[3], DATA_IN[3]);
  and and_9 (and_5_out[4], ACCUMULATOR[4], DATA_IN[4]);
  and and_10 (and_5_out[5], ACCUMULATOR[5], DATA_IN[5]);
  and and_11 (and_5_out[6], ACCUMULATOR[6], DATA_IN[6]);
  and and_12 (and_5_out[7], ACCUMULATOR[7], DATA_IN[7]);
  and and_13 (and_13_out, INSTR[0], not_2_out, INSTR[2]);
  xor xor_1 (xor_1_out[0], ACCUMULATOR[0], DATA_IN[0]);
  xor xor_2 (xor_1_out[1], ACCUMULATOR[1], DATA_IN[1]);
  xor xor_3 (xor_1_out[2], ACCUMULATOR[2], DATA_IN[2]);
  xor xor_4 (xor_1_out[3], ACCUMULATOR[3], DATA_IN[3]);
  xor xor_5 (xor_1_out[4], ACCUMULATOR[4], DATA_IN[4]);
  xor xor_6 (xor_1_out[5], ACCUMULATOR[5], DATA_IN[5]);
  xor xor_7 (xor_1_out[6], ACCUMULATOR[6], DATA_IN[6]);
  xor xor_8 (xor_1_out[7], ACCUMULATOR[7], DATA_IN[7]);
  and and_14 (and_14_out, not_3_out, INSTR[1], INSTR[2]);
  RightRotator RightRotator_1 (.S(ACCUMULATOR[3:0]), .I(DATA_IN), .O(RightRotator_1_o));
  and and_15 (SR_W, INSTR[0], INSTR[1], INSTR[2]);
  xnor xnor_1 (xnor_1_out, ACCUMULATOR[0], DATA_IN[0]);
  xnor xnor_2 (xnor_2_out, ACCUMULATOR[1], DATA_IN[1]);
  xnor xnor_3 (xnor_3_out, ACCUMULATOR[2], DATA_IN[2]);
  xnor xnor_4 (xnor_4_out, ACCUMULATOR[3], DATA_IN[3]);
  xnor xnor_5 (xnor_5_out, ACCUMULATOR[4], DATA_IN[4]);
  xnor xnor_6 (xnor_6_out, ACCUMULATOR[5], DATA_IN[5]);
  xnor xnor_7 (xnor_7_out, ACCUMULATOR[6], DATA_IN[6]);
  xnor xnor_8 (xnor_8_out, ACCUMULATOR[7], DATA_IN[7]);
  or or_9 (or_9_out, INSTR[0], INSTR[1], INSTR[2]);
  Register register_1 (.D(controlled_buffer_1_out), .en(or_9_out), .clk(CLK), .Q(register_1_q));  // open: clr
  assign controlled_buffer_1_out = and_1_out ? TCAdder_1_o : 8'bz;  // Controlled_Buffer controlled_buffer_1
  assign controlled_buffer_1_out = and_2_out ? fp_adder_1_o : 8'bz;  // Controlled_Buffer controlled_buffer_2
  assign controlled_buffer_1_out = and_3_out ? or_1_out : 8'bz;  // Controlled_Buffer controlled_buffer_3
  assign controlled_buffer_1_out = and_4_out ? and_5_out : 8'bz;  // Controlled_Buffer controlled_buffer_4
  assign controlled_buffer_1_out = and_13_out ? xor_1_out : 8'bz;  // Controlled_Buffer controlled_buffer_5
  assign controlled_buffer_1_out = and_14_out ? RightRotator_1_o : 8'bz;  // Controlled_Buffer controlled_buffer_6
  and and_16 (and_16_out, xnor_1_out, xnor_2_out, xnor_3_out, xnor_4_out, xnor_5_out, xnor_6_out, xnor_7_out, xnor_8_out);
  assign SR = SR_W ? and_16_out : 1'bz;  // Controlled_Buffer controlled_buffer_7
  assign DATA_OUT = READ ? register_1_q : 8'bz;  // Controlled_Buffer controlled_buffer_8

  // Notes on the sheet:
  //   INSTRUCTION SET
  //   000 : -
  //   010 : ADD (FP)
  //   011 : OR
  //   100 : AND
  //   101 : XOR
  //   110 : ROTATE
  //   111 : EQ
  //   001 : ADD (TC)
  //   ADD (TC)
  //   ADD (FP)
  //   OR
  //   AND
  //   XOR
  //   ROTATE
  //   EQ
endmodule

module ALU (
  input  [2:0] INSTR,
  input  [7:0] DATA_IN,
  input  [7:0] ACCUMULATOR,
  input  CLK,
  input  R,
  output [7:0] DATA_OUT,
  output SR_W,
  output SR
);

  wire or_9_out, xnor_1_out, xnor_2_out, xnor_3_out, xnor_4_out, xnor_5_out, xnor_6_out, xnor_7_out,
       xnor_8_out;
  wire [7:0] and_1_out, FPAdder_1_o, multiplexer_1_out, or_1_out, RightRotator_1_o, TCAdder_1_o, xor_1_out;

  TCAdder TCAdder_1 (.A(DATA_IN), .B(ACCUMULATOR), .C(1'b0), .O(TCAdder_1_o));  // open: S
  FP_Adder FPAdder_1 (.A(DATA_IN), .B(ACCUMULATOR), .O(FPAdder_1_o));
  or or_1 (or_1_out[0], ACCUMULATOR[0], DATA_IN[0]);
  or or_2 (or_1_out[1], ACCUMULATOR[1], DATA_IN[1]);
  or or_3 (or_1_out[2], ACCUMULATOR[2], DATA_IN[2]);
  or or_4 (or_1_out[3], ACCUMULATOR[3], DATA_IN[3]);
  or or_5 (or_1_out[4], ACCUMULATOR[4], DATA_IN[4]);
  or or_6 (or_1_out[5], ACCUMULATOR[5], DATA_IN[5]);
  or or_7 (or_1_out[6], ACCUMULATOR[6], DATA_IN[6]);
  or or_8 (or_1_out[7], ACCUMULATOR[7], DATA_IN[7]);
  and and_1 (and_1_out[0], ACCUMULATOR[0], DATA_IN[0]);
  and and_2 (and_1_out[1], ACCUMULATOR[1], DATA_IN[1]);
  and and_3 (and_1_out[2], ACCUMULATOR[2], DATA_IN[2]);
  and and_4 (and_1_out[3], ACCUMULATOR[3], DATA_IN[3]);
  and and_5 (and_1_out[4], ACCUMULATOR[4], DATA_IN[4]);
  and and_6 (and_1_out[5], ACCUMULATOR[5], DATA_IN[5]);
  and and_7 (and_1_out[6], ACCUMULATOR[6], DATA_IN[6]);
  and and_8 (and_1_out[7], ACCUMULATOR[7], DATA_IN[7]);
  xor xor_1 (xor_1_out[0], ACCUMULATOR[0], DATA_IN[0]);
  xor xor_2 (xor_1_out[1], ACCUMULATOR[1], DATA_IN[1]);
  xor xor_3 (xor_1_out[2], ACCUMULATOR[2], DATA_IN[2]);
  xor xor_4 (xor_1_out[3], ACCUMULATOR[3], DATA_IN[3]);
  xor xor_5 (xor_1_out[4], ACCUMULATOR[4], DATA_IN[4]);
  xor xor_6 (xor_1_out[5], ACCUMULATOR[5], DATA_IN[5]);
  xor xor_7 (xor_1_out[6], ACCUMULATOR[6], DATA_IN[6]);
  xor xor_8 (xor_1_out[7], ACCUMULATOR[7], DATA_IN[7]);
  RightRotator RightRotator_1 (.S(ACCUMULATOR[3:0]), .I(DATA_IN), .O(RightRotator_1_o));
  and and_9 (SR_W, INSTR[0], INSTR[1], INSTR[2]);
  xnor xnor_1 (xnor_1_out, ACCUMULATOR[0], DATA_IN[0]);
  xnor xnor_2 (xnor_2_out, ACCUMULATOR[1], DATA_IN[1]);
  xnor xnor_3 (xnor_3_out, ACCUMULATOR[2], DATA_IN[2]);
  xnor xnor_4 (xnor_4_out, ACCUMULATOR[3], DATA_IN[3]);
  xnor xnor_5 (xnor_5_out, ACCUMULATOR[4], DATA_IN[4]);
  xnor xnor_6 (xnor_6_out, ACCUMULATOR[5], DATA_IN[5]);
  xnor xnor_7 (xnor_7_out, ACCUMULATOR[6], DATA_IN[6]);
  xnor xnor_8 (xnor_8_out, ACCUMULATOR[7], DATA_IN[7]);
  or or_9 (or_9_out, INSTR[2], INSTR[1], INSTR[0]);
  and and_10 (SR, xnor_1_out, xnor_2_out, xnor_3_out, xnor_4_out, xnor_5_out, xnor_6_out, xnor_7_out, xnor_8_out);
  Multiplexer #(.select(3), .width(8)) multiplexer_1 (
    .in0({8{1'b0}}), .in1(TCAdder_1_o), .in2(FPAdder_1_o), .in3(or_1_out), .in4(and_1_out), .in5(xor_1_out),
    .in6(RightRotator_1_o), .in7({8{1'b0}}), .out(multiplexer_1_out), .sel(INSTR));
  Hex_Digit_Display #(.decimalPoint("false")) IGNORE (.value(ACCUMULATOR[7:4]));
  Register ALU_VAL (.D(multiplexer_1_out), .en(or_9_out), .clk(CLK), .Q(DATA_OUT), .clr(R));

  // Notes on the sheet:
  //   INSTRUCTION SET
  //   000 : -
  //   010 : ADD (FP)
  //   011 : OR
  //   100 : AND
  //   101 : XOR
  //   110 : ROTATE
  //   111 : EQ
  //   001 : ADD (TC)
  //   ADD (TC)
  //   ADD (FP)
  //   OR
  //   AND
  //   XOR
  //   ROTATE
  //   EQ
endmodule

module ALU_PIPE (
  input  [2:0] INSTR,
  input  [7:0] INPUT_A,
  input  [7:0] INPUT_B,
  output [7:0] DATA_OUT,
  output SR_W,
  output SR
);

  wire xnor_1_out, xnor_2_out, xnor_3_out, xnor_4_out, xnor_5_out, xnor_6_out, xnor_7_out, xnor_8_out;
  wire [7:0] and_1_out, FPAdder_1_o, or_1_out, RightRotator_1_o, TCAdder_1_o, xor_1_out;

  TCAdder TCAdder_1 (.A(INPUT_A), .B(INPUT_B), .C(1'b0), .O(TCAdder_1_o));  // open: S
  FP_Adder FPAdder_1 (.A(INPUT_A), .B(INPUT_B), .O(FPAdder_1_o));
  or or_1 (or_1_out[0], INPUT_B[0], INPUT_A[0]);
  or or_2 (or_1_out[1], INPUT_B[1], INPUT_A[1]);
  or or_3 (or_1_out[2], INPUT_B[2], INPUT_A[2]);
  or or_4 (or_1_out[3], INPUT_B[3], INPUT_A[3]);
  or or_5 (or_1_out[4], INPUT_B[4], INPUT_A[4]);
  or or_6 (or_1_out[5], INPUT_B[5], INPUT_A[5]);
  or or_7 (or_1_out[6], INPUT_B[6], INPUT_A[6]);
  or or_8 (or_1_out[7], INPUT_B[7], INPUT_A[7]);
  and and_1 (and_1_out[0], INPUT_B[0], INPUT_A[0]);
  and and_2 (and_1_out[1], INPUT_B[1], INPUT_A[1]);
  and and_3 (and_1_out[2], INPUT_B[2], INPUT_A[2]);
  and and_4 (and_1_out[3], INPUT_B[3], INPUT_A[3]);
  and and_5 (and_1_out[4], INPUT_B[4], INPUT_A[4]);
  and and_6 (and_1_out[5], INPUT_B[5], INPUT_A[5]);
  and and_7 (and_1_out[6], INPUT_B[6], INPUT_A[6]);
  and and_8 (and_1_out[7], INPUT_B[7], INPUT_A[7]);
  xor xor_1 (xor_1_out[0], INPUT_B[0], INPUT_A[0]);
  xor xor_2 (xor_1_out[1], INPUT_B[1], INPUT_A[1]);
  xor xor_3 (xor_1_out[2], INPUT_B[2], INPUT_A[2]);
  xor xor_4 (xor_1_out[3], INPUT_B[3], INPUT_A[3]);
  xor xor_5 (xor_1_out[4], INPUT_B[4], INPUT_A[4]);
  xor xor_6 (xor_1_out[5], INPUT_B[5], INPUT_A[5]);
  xor xor_7 (xor_1_out[6], INPUT_B[6], INPUT_A[6]);
  xor xor_8 (xor_1_out[7], INPUT_B[7], INPUT_A[7]);
  RightRotator RightRotator_1 (.S(INPUT_A[3:0]), .I(INPUT_B), .O(RightRotator_1_o));
  and and_9 (SR_W, INSTR[0], INSTR[1], INSTR[2]);
  xnor xnor_1 (xnor_1_out, INPUT_B[0], INPUT_A[0]);
  xnor xnor_2 (xnor_2_out, INPUT_B[1], INPUT_A[1]);
  xnor xnor_3 (xnor_3_out, INPUT_B[2], INPUT_A[2]);
  xnor xnor_4 (xnor_4_out, INPUT_B[3], INPUT_A[3]);
  xnor xnor_5 (xnor_5_out, INPUT_B[4], INPUT_A[4]);
  xnor xnor_6 (xnor_6_out, INPUT_B[5], INPUT_A[5]);
  xnor xnor_7 (xnor_7_out, INPUT_B[6], INPUT_A[6]);
  xnor xnor_8 (xnor_8_out, INPUT_B[7], INPUT_A[7]);
  and and_10 (SR, xnor_1_out, xnor_2_out, xnor_3_out, xnor_4_out, xnor_5_out, xnor_6_out, xnor_7_out, xnor_8_out);
  Multiplexer #(.select(3), .width(8)) multiplexer_1 (
    .in0({8{1'b0}}), .in1(TCAdder_1_o), .in2(FPAdder_1_o), .in3(or_1_out), .in4(and_1_out), .in5(xor_1_out),
    .in6(RightRotator_1_o), .in7({8{1'b0}}), .out(DATA_OUT), .sel(INSTR));
  Hex_Digit_Display #(.decimalPoint("false")) IGNORE (.value(INPUT_A[7:4]));

  // Notes on the sheet:
  //   INSTRUCTION SET
  //   000 : -
  //   010 : ADD (FP)
  //   011 : OR
  //   100 : AND
  //   101 : XOR
  //   110 : ROTATE
  //   111 : EQ
  //   001 : ADD (TC)
  //   ADD (TC)
  //   ADD (FP)
  //   OR
  //   AND
  //   XOR
  //   ROTATE
  //   EQ
endmodule
module MainMemory (
  input  READ,
  input  WRITE,
  input  [7:0] READ_ADDRESS,
  input  [7:0] WRITE_ADDRESS,
  input  CLK,
  input  [7:0] DATA_IN,
  input  RESET,
  output [7:0] DATA_OUT
);

  wire and_1_out, and_2_out, and_3_out, and_4_out, and_5_out, and_6_out, and_7_out, and_8_out, and_9_out,
       and_10_out, and_11_out, and_12_out, and_13_out, and_14_out, and_15_out, and_16_out, and_17_out,
       and_18_out, and_19_out, and_20_out, and_21_out, and_22_out, and_23_out, and_24_out, and_25_out,
       and_26_out, and_27_out, and_28_out, and_29_out, and_30_out, and_31_out, and_32_out, and_33_out,
       and_34_out, and_35_out, and_36_out, and_37_out, and_38_out, and_39_out, and_40_out, and_41_out,
       and_42_out, and_43_out, and_44_out, and_45_out, and_46_out, and_47_out, and_48_out, and_49_out,
       and_50_out, and_51_out, and_52_out, and_53_out, and_54_out, and_55_out, and_56_out, and_57_out,
       and_58_out, and_59_out, and_60_out, and_61_out, and_62_out, and_63_out, and_64_out, and_65_out,
       and_66_out, and_67_out, and_68_out, and_69_out, and_70_out, and_71_out, and_72_out, and_73_out,
       and_74_out, and_75_out, and_76_out, and_77_out, and_78_out, and_79_out, and_80_out, and_81_out,
       and_82_out, and_83_out, and_84_out, and_85_out, and_86_out, and_87_out, and_88_out, and_89_out,
       and_90_out, and_91_out, and_92_out, and_93_out, and_94_out, and_95_out, and_96_out, and_97_out,
       and_98_out, and_99_out, and_100_out, and_101_out, and_102_out, and_103_out, and_104_out, and_105_out,
       and_106_out, and_107_out, and_108_out, and_109_out, and_110_out, and_111_out, and_112_out,
       and_113_out, and_114_out, and_115_out, and_116_out, and_117_out, and_118_out, and_119_out,
       and_120_out, and_121_out, and_122_out, and_123_out, and_124_out, and_125_out, and_126_out,
       and_127_out, and_128_out, and_129_out, and_130_out, and_131_out, and_132_out, and_133_out,
       and_134_out, and_135_out, and_136_out, and_137_out, and_138_out, and_139_out, and_140_out,
       and_141_out, and_142_out, and_143_out, and_144_out, and_145_out, and_146_out, and_147_out,
       and_148_out, and_149_out, and_150_out, and_151_out, and_152_out, and_153_out, and_154_out,
       and_155_out, and_156_out, and_157_out, and_158_out, and_159_out, and_160_out, and_161_out,
       and_162_out, and_163_out, and_164_out, and_165_out, and_166_out, and_167_out, and_168_out,
       and_169_out, and_170_out, and_171_out, and_172_out, and_173_out, and_174_out, and_175_out,
       and_176_out, and_177_out, and_178_out, and_179_out, and_180_out, and_181_out, and_182_out,
       and_183_out, and_184_out, and_185_out, and_186_out, and_187_out, and_188_out, and_189_out,
       and_190_out, and_191_out, and_192_out, and_193_out, and_194_out, and_195_out, and_196_out,
       and_197_out, and_198_out, and_199_out, and_200_out, and_201_out, and_202_out, and_203_out,
       and_204_out, and_205_out, and_206_out, and_207_out, and_208_out, and_209_out, and_210_out,
       and_211_out, and_212_out, and_213_out, and_214_out, and_215_out, and_216_out, and_217_out,
       and_218_out, and_219_out, and_220_out, and_221_out, and_222_out, and_223_out, and_224_out,
       and_225_out, and_226_out, and_227_out, and_228_out, and_229_out, and_230_out, and_231_out,
       and_232_out, and_233_out, and_234_out, and_235_out, and_236_out, and_237_out, and_238_out,
       and_239_out, and_240_out, and_241_out, and_242_out, and_243_out, and_244_out, and_245_out,
       and_246_out, and_247_out, and_248_out, and_249_out, and_250_out, and_251_out, and_252_out,
       and_253_out, and_254_out, and_255_out, and_256_out, and_257_out, and_258_out, and_259_out,
       and_260_out, and_261_out, and_262_out, and_263_out, and_264_out, and_265_out, and_266_out,
       and_267_out, and_268_out, and_269_out, and_270_out, and_271_out, and_272_out, and_273_out,
       and_274_out, and_275_out, and_276_out, and_277_out, and_278_out, and_279_out, and_280_out,
       and_281_out, and_282_out, and_283_out, and_284_out, and_285_out, and_286_out, and_287_out,
       and_288_out, and_289_out, and_290_out, and_291_out, and_292_out, and_293_out, and_294_out,
       and_295_out, and_296_out, and_297_out, and_298_out, and_299_out, and_300_out, and_301_out,
       and_302_out, and_303_out, and_304_out, and_305_out, and_306_out, and_307_out, and_308_out,
       and_309_out, and_310_out, and_311_out, and_312_out, and_313_out, and_314_out, and_315_out,
       and_316_out, and_317_out, and_318_out, and_319_out, and_320_out, and_321_out, and_322_out,
       and_323_out, and_324_out, and_325_out, and_326_out, and_327_out, and_328_out, and_329_out,
       and_330_out, and_331_out, and_332_out, and_333_out, and_334_out, and_335_out, and_336_out,
       and_337_out, and_338_out, and_339_out, and_340_out, and_341_out, and_342_out, and_343_out,
       and_344_out, and_345_out, and_346_out, and_347_out, and_348_out, and_349_out, and_350_out,
       and_351_out, and_352_out, and_353_out, and_354_out, and_355_out, and_356_out, and_357_out,
       and_358_out, and_359_out, and_360_out, and_361_out, and_362_out, and_363_out, and_364_out,
       and_365_out, and_366_out, and_367_out, and_368_out, and_369_out, and_370_out, and_371_out,
       and_372_out, and_373_out, and_374_out, and_375_out, and_376_out, and_377_out, and_378_out,
       and_379_out, and_380_out, and_381_out, and_382_out, and_383_out, and_384_out, and_385_out,
       and_386_out, and_387_out, and_388_out, and_389_out, and_390_out, and_391_out, and_392_out,
       and_393_out, and_394_out, and_395_out, and_396_out, and_397_out, and_398_out, and_399_out,
       and_400_out, and_401_out, and_402_out, and_403_out, and_404_out, and_405_out, and_406_out,
       and_407_out, and_408_out, and_409_out, and_410_out, and_411_out, and_412_out, and_413_out,
       and_414_out, and_415_out, and_416_out, and_417_out, and_418_out, and_419_out, and_420_out,
       and_421_out, and_422_out, and_423_out, and_424_out, and_425_out, and_426_out, and_427_out,
       and_428_out, and_429_out, and_430_out, and_431_out, and_432_out, and_433_out, and_434_out,
       and_435_out, and_436_out, and_437_out, and_438_out, and_439_out, and_440_out, and_441_out,
       and_442_out, and_443_out, and_444_out, and_445_out, and_446_out, and_447_out, and_448_out,
       and_449_out, and_450_out, and_451_out, and_452_out, and_453_out, and_454_out, and_455_out,
       and_456_out, and_457_out, and_458_out, and_459_out, and_460_out, and_461_out, and_462_out,
       and_463_out, and_464_out, and_465_out, and_466_out, and_467_out, and_468_out, and_469_out,
       and_470_out, and_471_out, and_472_out, and_473_out, and_474_out, and_475_out, and_476_out,
       and_477_out, and_478_out, and_479_out, and_480_out, and_481_out, and_482_out, and_483_out,
       and_484_out, and_485_out, and_486_out, and_487_out, and_488_out, and_489_out, and_490_out,
       and_491_out, and_492_out, and_493_out, and_494_out, and_495_out, and_496_out, and_497_out,
       and_498_out, and_499_out, and_500_out, and_501_out, and_502_out, and_503_out, and_504_out,
       and_505_out, and_506_out, and_507_out, and_508_out, and_509_out, and_510_out, and_511_out,
       and_512_out, demultiplexer_1_out0, demultiplexer_1_out1, demultiplexer_1_out2, demultiplexer_1_out3,
       demultiplexer_1_out4, demultiplexer_1_out5, demultiplexer_1_out6, demultiplexer_1_out7,
       demultiplexer_1_out8, demultiplexer_1_out9, demultiplexer_1_out10, demultiplexer_1_out11,
       demultiplexer_1_out12, demultiplexer_1_out13, demultiplexer_1_out14, demultiplexer_1_out15,
       demultiplexer_2_out0, demultiplexer_2_out1, demultiplexer_2_out2, demultiplexer_2_out3,
       demultiplexer_2_out4, demultiplexer_2_out5, demultiplexer_2_out6, demultiplexer_2_out7,
       demultiplexer_2_out8, demultiplexer_2_out9, demultiplexer_2_out10, demultiplexer_2_out11,
       demultiplexer_2_out12, demultiplexer_2_out13, demultiplexer_2_out14, demultiplexer_2_out15,
       demultiplexer_3_out0, demultiplexer_3_out1, demultiplexer_3_out2, demultiplexer_3_out3,
       demultiplexer_3_out4, demultiplexer_3_out5, demultiplexer_3_out6, demultiplexer_3_out7,
       demultiplexer_3_out8, demultiplexer_3_out9, demultiplexer_3_out10, demultiplexer_3_out11,
       demultiplexer_3_out12, demultiplexer_3_out13, demultiplexer_3_out14, demultiplexer_3_out15,
       demultiplexer_4_out0, demultiplexer_4_out1, demultiplexer_4_out2, demultiplexer_4_out3,
       demultiplexer_4_out4, demultiplexer_4_out5, demultiplexer_4_out6, demultiplexer_4_out7,
       demultiplexer_4_out8, demultiplexer_4_out9, demultiplexer_4_out10, demultiplexer_4_out11,
       demultiplexer_4_out12, demultiplexer_4_out13, demultiplexer_4_out14, demultiplexer_4_out15;
  wire [7:0] register_1_q, register_2_q, register_3_q, register_4_q, register_5_q, register_6_q,
       register_7_q, register_8_q, register_9_q, register_10_q, register_11_q, register_12_q, register_13_q,
       register_14_q, register_15_q, register_16_q, register_17_q, register_18_q, register_19_q,
       register_20_q, register_21_q, register_22_q, register_23_q, register_24_q, register_25_q,
       register_26_q, register_27_q, register_28_q, register_29_q, register_30_q, register_31_q,
       register_32_q, register_33_q, register_34_q, register_35_q, register_36_q, register_37_q,
       register_38_q, register_39_q, register_40_q, register_41_q, register_42_q, register_43_q,
       register_44_q, register_45_q, register_46_q, register_47_q, register_48_q, register_49_q,
       register_50_q, register_51_q, register_52_q, register_53_q, register_54_q, register_55_q,
       register_56_q, register_57_q, register_58_q, register_59_q, register_60_q, register_61_q,
       register_62_q, register_63_q, register_64_q, register_65_q, register_66_q, register_67_q,
       register_68_q, register_69_q, register_70_q, register_71_q, register_72_q, register_73_q,
       register_74_q, register_75_q, register_76_q, register_77_q, register_78_q, register_79_q,
       register_80_q, register_81_q, register_82_q, register_83_q, register_84_q, register_85_q,
       register_86_q, register_87_q, register_88_q, register_89_q, register_90_q, register_91_q,
       register_92_q, register_93_q, register_94_q, register_95_q, register_96_q, register_97_q,
       register_98_q, register_99_q, register_100_q, register_101_q, register_102_q, register_103_q,
       register_104_q, register_105_q, register_106_q, register_107_q, register_108_q, register_109_q,
       register_110_q, register_111_q, register_112_q, register_113_q, register_114_q, register_115_q,
       register_116_q, register_117_q, register_118_q, register_119_q, register_120_q, register_121_q,
       register_122_q, register_123_q, register_124_q, register_125_q, register_126_q, register_127_q,
       register_128_q, register_129_q, register_130_q, register_131_q, register_132_q, register_133_q,
       register_134_q, register_135_q, register_136_q, register_137_q, register_138_q, register_139_q,
       register_140_q, register_141_q, register_142_q, register_143_q, register_144_q, register_145_q,
       register_146_q, register_147_q, register_148_q, register_149_q, register_150_q, register_151_q,
       register_152_q, register_153_q, register_154_q, register_155_q, register_156_q, register_157_q,
       register_158_q, register_159_q, register_160_q, register_161_q, register_162_q, register_163_q,
       register_164_q, register_165_q, register_166_q, register_167_q, register_168_q, register_169_q,
       register_170_q, register_171_q, register_172_q, register_173_q, register_174_q, register_175_q,
       register_176_q, register_177_q, register_178_q, register_179_q, register_180_q, register_181_q,
       register_182_q, register_183_q, register_184_q, register_185_q, register_186_q, register_187_q,
       register_188_q, register_189_q, register_190_q, register_191_q, register_192_q, register_193_q,
       register_194_q, register_195_q, register_196_q, register_197_q, register_198_q, register_199_q,
       register_200_q, register_201_q, register_202_q, register_203_q, register_204_q, register_205_q,
       register_206_q, register_207_q, register_208_q, register_209_q, register_210_q, register_211_q,
       register_212_q, register_213_q, register_214_q, register_215_q, register_216_q, register_217_q,
       register_218_q, register_219_q, register_220_q, register_221_q, register_222_q, register_223_q,
       register_224_q, register_225_q, register_226_q, register_227_q, register_228_q, register_229_q,
       register_230_q, register_231_q, register_232_q, register_233_q, register_234_q, register_235_q,
       register_236_q, register_237_q, register_238_q, register_239_q, register_240_q, register_241_q,
       register_242_q, register_243_q, register_244_q, register_245_q, register_246_q, register_247_q,
       register_248_q, register_249_q, register_250_q, register_251_q, register_252_q, register_253_q,
       register_254_q, register_255_q, register_256_q;

  Demultiplexer #(.select(4)) demultiplexer_1 (
    .out0(demultiplexer_1_out0), .out1(demultiplexer_1_out1), .out2(demultiplexer_1_out2),
    .out3(demultiplexer_1_out3), .out4(demultiplexer_1_out4), .out5(demultiplexer_1_out5),
    .out6(demultiplexer_1_out6), .out7(demultiplexer_1_out7), .out8(demultiplexer_1_out8),
    .out9(demultiplexer_1_out9), .out10(demultiplexer_1_out10), .out11(demultiplexer_1_out11),
    .out12(demultiplexer_1_out12), .out13(demultiplexer_1_out13), .out14(demultiplexer_1_out14),
    .out15(demultiplexer_1_out15), .in(WRITE), .sel(WRITE_ADDRESS[7:4]));
  Demultiplexer #(.select(4)) demultiplexer_2 (
    .out0(demultiplexer_2_out0), .out1(demultiplexer_2_out1), .out2(demultiplexer_2_out2),
    .out3(demultiplexer_2_out3), .out4(demultiplexer_2_out4), .out5(demultiplexer_2_out5),
    .out6(demultiplexer_2_out6), .out7(demultiplexer_2_out7), .out8(demultiplexer_2_out8),
    .out9(demultiplexer_2_out9), .out10(demultiplexer_2_out10), .out11(demultiplexer_2_out11),
    .out12(demultiplexer_2_out12), .out13(demultiplexer_2_out13), .out14(demultiplexer_2_out14),
    .out15(demultiplexer_2_out15), .in(READ), .sel(READ_ADDRESS[7:4]));
  Register register_1 (.D(DATA_IN), .en(and_1_out), .clk(CLK), .Q(register_1_q), .clr(RESET));
  and and_1 (and_1_out, demultiplexer_3_out0, demultiplexer_1_out0);
  Register register_2 (.D(DATA_IN), .en(and_2_out), .clk(CLK), .Q(register_2_q), .clr(RESET));
  and and_2 (and_2_out, demultiplexer_3_out0, demultiplexer_1_out1);
  Register register_3 (.D(DATA_IN), .en(and_3_out), .clk(CLK), .Q(register_3_q), .clr(RESET));
  and and_3 (and_3_out, demultiplexer_3_out0, demultiplexer_1_out2);
  Register register_4 (.D(DATA_IN), .en(and_4_out), .clk(CLK), .Q(register_4_q), .clr(RESET));
  and and_4 (and_4_out, demultiplexer_3_out0, demultiplexer_1_out3);
  Register register_5 (.D(DATA_IN), .en(and_5_out), .clk(CLK), .Q(register_5_q), .clr(RESET));
  and and_5 (and_5_out, demultiplexer_3_out0, demultiplexer_1_out4);
  Register register_6 (.D(DATA_IN), .en(and_6_out), .clk(CLK), .Q(register_6_q), .clr(RESET));
  and and_6 (and_6_out, demultiplexer_3_out0, demultiplexer_1_out5);
  Register register_7 (.D(DATA_IN), .en(and_7_out), .clk(CLK), .Q(register_7_q), .clr(RESET));
  and and_7 (and_7_out, demultiplexer_3_out0, demultiplexer_1_out6);
  Register register_8 (.D(DATA_IN), .en(and_8_out), .clk(CLK), .Q(register_8_q), .clr(RESET));
  and and_8 (and_8_out, demultiplexer_3_out0, demultiplexer_1_out7);
  Register register_9 (.D(DATA_IN), .en(and_9_out), .clk(CLK), .Q(register_9_q), .clr(RESET));
  and and_9 (and_9_out, demultiplexer_3_out0, demultiplexer_1_out8);
  Register register_10 (.D(DATA_IN), .en(and_10_out), .clk(CLK), .Q(register_10_q), .clr(RESET));
  and and_10 (and_10_out, demultiplexer_3_out0, demultiplexer_1_out9);
  Register register_11 (.D(DATA_IN), .en(and_11_out), .clk(CLK), .Q(register_11_q), .clr(RESET));
  and and_11 (and_11_out, demultiplexer_3_out0, demultiplexer_1_out10);
  Register register_12 (.D(DATA_IN), .en(and_12_out), .clk(CLK), .Q(register_12_q), .clr(RESET));
  and and_12 (and_12_out, demultiplexer_3_out0, demultiplexer_1_out11);
  Register register_13 (.D(DATA_IN), .en(and_13_out), .clk(CLK), .Q(register_13_q), .clr(RESET));
  and and_13 (and_13_out, demultiplexer_3_out0, demultiplexer_1_out12);
  Register register_14 (.D(DATA_IN), .en(and_14_out), .clk(CLK), .Q(register_14_q), .clr(RESET));
  and and_14 (and_14_out, demultiplexer_3_out0, demultiplexer_1_out13);
  Register register_15 (.D(DATA_IN), .en(and_15_out), .clk(CLK), .Q(register_15_q), .clr(RESET));
  and and_15 (and_15_out, demultiplexer_3_out0, demultiplexer_1_out14);
  Register register_16 (.D(DATA_IN), .en(and_16_out), .clk(CLK), .Q(register_16_q), .clr(RESET));
  and and_16 (and_16_out, demultiplexer_3_out0, demultiplexer_1_out15);
  and and_17 (and_17_out, demultiplexer_2_out0, demultiplexer_4_out0);
  and and_18 (and_18_out, demultiplexer_2_out1, demultiplexer_4_out0);
  and and_19 (and_19_out, demultiplexer_2_out2, demultiplexer_4_out0);
  and and_20 (and_20_out, demultiplexer_2_out3, demultiplexer_4_out0);
  and and_21 (and_21_out, demultiplexer_2_out4, demultiplexer_4_out0);
  and and_22 (and_22_out, demultiplexer_2_out5, demultiplexer_4_out0);
  and and_23 (and_23_out, demultiplexer_2_out6, demultiplexer_4_out0);
  and and_24 (and_24_out, demultiplexer_2_out7, demultiplexer_4_out0);
  and and_25 (and_25_out, demultiplexer_2_out8, demultiplexer_4_out0);
  and and_26 (and_26_out, demultiplexer_2_out9, demultiplexer_4_out0);
  and and_27 (and_27_out, demultiplexer_2_out10, demultiplexer_4_out0);
  and and_28 (and_28_out, demultiplexer_2_out11, demultiplexer_4_out0);
  and and_29 (and_29_out, demultiplexer_2_out12, demultiplexer_4_out0);
  and and_30 (and_30_out, demultiplexer_2_out13, demultiplexer_4_out0);
  and and_31 (and_31_out, demultiplexer_2_out14, demultiplexer_4_out0);
  and and_32 (and_32_out, demultiplexer_2_out15, demultiplexer_4_out0);
  assign DATA_OUT = and_17_out ? register_1_q : 8'bz;  // Controlled_Buffer controlled_buffer_1
  and and_33 (and_33_out, demultiplexer_3_out1, demultiplexer_1_out0);
  assign DATA_OUT = and_18_out ? register_2_q : 8'bz;  // Controlled_Buffer controlled_buffer_2
  and and_34 (and_34_out, demultiplexer_3_out1, demultiplexer_1_out1);
  assign DATA_OUT = and_19_out ? register_3_q : 8'bz;  // Controlled_Buffer controlled_buffer_3
  and and_35 (and_35_out, demultiplexer_3_out1, demultiplexer_1_out2);
  assign DATA_OUT = and_20_out ? register_4_q : 8'bz;  // Controlled_Buffer controlled_buffer_4
  and and_36 (and_36_out, demultiplexer_3_out1, demultiplexer_1_out3);
  assign DATA_OUT = and_21_out ? register_5_q : 8'bz;  // Controlled_Buffer controlled_buffer_5
  and and_37 (and_37_out, demultiplexer_3_out1, demultiplexer_1_out4);
  assign DATA_OUT = and_22_out ? register_6_q : 8'bz;  // Controlled_Buffer controlled_buffer_6
  and and_38 (and_38_out, demultiplexer_3_out1, demultiplexer_1_out5);
  assign DATA_OUT = and_23_out ? register_7_q : 8'bz;  // Controlled_Buffer controlled_buffer_7
  and and_39 (and_39_out, demultiplexer_3_out1, demultiplexer_1_out6);
  assign DATA_OUT = and_24_out ? register_8_q : 8'bz;  // Controlled_Buffer controlled_buffer_8
  and and_40 (and_40_out, demultiplexer_3_out1, demultiplexer_1_out7);
  assign DATA_OUT = and_25_out ? register_9_q : 8'bz;  // Controlled_Buffer controlled_buffer_9
  and and_41 (and_41_out, demultiplexer_3_out1, demultiplexer_1_out8);
  assign DATA_OUT = and_26_out ? register_10_q : 8'bz;  // Controlled_Buffer controlled_buffer_10
  and and_42 (and_42_out, demultiplexer_3_out1, demultiplexer_1_out9);
  assign DATA_OUT = and_27_out ? register_11_q : 8'bz;  // Controlled_Buffer controlled_buffer_11
  and and_43 (and_43_out, demultiplexer_3_out1, demultiplexer_1_out10);
  assign DATA_OUT = and_28_out ? register_12_q : 8'bz;  // Controlled_Buffer controlled_buffer_12
  and and_44 (and_44_out, demultiplexer_3_out1, demultiplexer_1_out11);
  assign DATA_OUT = and_29_out ? register_13_q : 8'bz;  // Controlled_Buffer controlled_buffer_13
  and and_45 (and_45_out, demultiplexer_3_out1, demultiplexer_1_out12);
  assign DATA_OUT = and_30_out ? register_14_q : 8'bz;  // Controlled_Buffer controlled_buffer_14
  and and_46 (and_46_out, demultiplexer_3_out1, demultiplexer_1_out13);
  assign DATA_OUT = and_31_out ? register_15_q : 8'bz;  // Controlled_Buffer controlled_buffer_15
  and and_47 (and_47_out, demultiplexer_3_out1, demultiplexer_1_out14);
  assign DATA_OUT = and_32_out ? register_16_q : 8'bz;  // Controlled_Buffer controlled_buffer_16
  and and_48 (and_48_out, demultiplexer_3_out1, demultiplexer_1_out15);
  Register register_17 (.D(DATA_IN), .en(and_33_out), .clk(CLK), .Q(register_17_q), .clr(RESET));
  Register register_18 (.D(DATA_IN), .en(and_34_out), .clk(CLK), .Q(register_18_q), .clr(RESET));
  Register register_19 (.D(DATA_IN), .en(and_35_out), .clk(CLK), .Q(register_19_q), .clr(RESET));
  Register register_20 (.D(DATA_IN), .en(and_36_out), .clk(CLK), .Q(register_20_q), .clr(RESET));
  Register register_21 (.D(DATA_IN), .en(and_37_out), .clk(CLK), .Q(register_21_q), .clr(RESET));
  Register register_22 (.D(DATA_IN), .en(and_38_out), .clk(CLK), .Q(register_22_q), .clr(RESET));
  Register register_23 (.D(DATA_IN), .en(and_39_out), .clk(CLK), .Q(register_23_q), .clr(RESET));
  Register register_24 (.D(DATA_IN), .en(and_40_out), .clk(CLK), .Q(register_24_q), .clr(RESET));
  Register register_25 (.D(DATA_IN), .en(and_41_out), .clk(CLK), .Q(register_25_q), .clr(RESET));
  Register register_26 (.D(DATA_IN), .en(and_42_out), .clk(CLK), .Q(register_26_q), .clr(RESET));
  Register register_27 (.D(DATA_IN), .en(and_43_out), .clk(CLK), .Q(register_27_q), .clr(RESET));
  Register register_28 (.D(DATA_IN), .en(and_44_out), .clk(CLK), .Q(register_28_q), .clr(RESET));
  Register register_29 (.D(DATA_IN), .en(and_45_out), .clk(CLK), .Q(register_29_q), .clr(RESET));
  Register register_30 (.D(DATA_IN), .en(and_46_out), .clk(CLK), .Q(register_30_q), .clr(RESET));
  Register register_31 (.D(DATA_IN), .en(and_47_out), .clk(CLK), .Q(register_31_q), .clr(RESET));
  Register register_32 (.D(DATA_IN), .en(and_48_out), .clk(CLK), .Q(register_32_q), .clr(RESET));
  and and_49 (and_49_out, demultiplexer_2_out0, demultiplexer_4_out1);
  assign DATA_OUT = and_49_out ? register_17_q : 8'bz;  // Controlled_Buffer controlled_buffer_17
  and and_50 (and_50_out, demultiplexer_2_out1, demultiplexer_4_out1);
  assign DATA_OUT = and_50_out ? register_18_q : 8'bz;  // Controlled_Buffer controlled_buffer_18
  and and_51 (and_51_out, demultiplexer_2_out2, demultiplexer_4_out1);
  assign DATA_OUT = and_51_out ? register_19_q : 8'bz;  // Controlled_Buffer controlled_buffer_19
  and and_52 (and_52_out, demultiplexer_2_out3, demultiplexer_4_out1);
  assign DATA_OUT = and_52_out ? register_20_q : 8'bz;  // Controlled_Buffer controlled_buffer_20
  and and_53 (and_53_out, demultiplexer_2_out4, demultiplexer_4_out1);
  assign DATA_OUT = and_53_out ? register_21_q : 8'bz;  // Controlled_Buffer controlled_buffer_21
  and and_54 (and_54_out, demultiplexer_2_out5, demultiplexer_4_out1);
  assign DATA_OUT = and_54_out ? register_22_q : 8'bz;  // Controlled_Buffer controlled_buffer_22
  and and_55 (and_55_out, demultiplexer_2_out6, demultiplexer_4_out1);
  assign DATA_OUT = and_55_out ? register_23_q : 8'bz;  // Controlled_Buffer controlled_buffer_23
  and and_56 (and_56_out, demultiplexer_2_out7, demultiplexer_4_out1);
  assign DATA_OUT = and_56_out ? register_24_q : 8'bz;  // Controlled_Buffer controlled_buffer_24
  and and_57 (and_57_out, demultiplexer_2_out8, demultiplexer_4_out1);
  assign DATA_OUT = and_57_out ? register_25_q : 8'bz;  // Controlled_Buffer controlled_buffer_25
  and and_58 (and_58_out, demultiplexer_2_out9, demultiplexer_4_out1);
  assign DATA_OUT = and_58_out ? register_26_q : 8'bz;  // Controlled_Buffer controlled_buffer_26
  and and_59 (and_59_out, demultiplexer_2_out10, demultiplexer_4_out1);
  assign DATA_OUT = and_59_out ? register_27_q : 8'bz;  // Controlled_Buffer controlled_buffer_27
  and and_60 (and_60_out, demultiplexer_2_out11, demultiplexer_4_out1);
  assign DATA_OUT = and_60_out ? register_28_q : 8'bz;  // Controlled_Buffer controlled_buffer_28
  and and_61 (and_61_out, demultiplexer_2_out12, demultiplexer_4_out1);
  assign DATA_OUT = and_61_out ? register_29_q : 8'bz;  // Controlled_Buffer controlled_buffer_29
  and and_62 (and_62_out, demultiplexer_2_out13, demultiplexer_4_out1);
  assign DATA_OUT = and_62_out ? register_30_q : 8'bz;  // Controlled_Buffer controlled_buffer_30
  and and_63 (and_63_out, demultiplexer_2_out14, demultiplexer_4_out1);
  assign DATA_OUT = and_63_out ? register_31_q : 8'bz;  // Controlled_Buffer controlled_buffer_31
  and and_64 (and_64_out, demultiplexer_2_out15, demultiplexer_4_out1);
  assign DATA_OUT = and_64_out ? register_32_q : 8'bz;  // Controlled_Buffer controlled_buffer_32
  Register register_33 (.D(DATA_IN), .en(and_65_out), .clk(CLK), .Q(register_33_q), .clr(RESET));
  and and_65 (and_65_out, demultiplexer_3_out2, demultiplexer_1_out0);
  Register register_34 (.D(DATA_IN), .en(and_66_out), .clk(CLK), .Q(register_34_q), .clr(RESET));
  and and_66 (and_66_out, demultiplexer_3_out2, demultiplexer_1_out1);
  Register register_35 (.D(DATA_IN), .en(and_67_out), .clk(CLK), .Q(register_35_q), .clr(RESET));
  and and_67 (and_67_out, demultiplexer_3_out2, demultiplexer_1_out2);
  Register register_36 (.D(DATA_IN), .en(and_68_out), .clk(CLK), .Q(register_36_q), .clr(RESET));
  and and_68 (and_68_out, demultiplexer_3_out2, demultiplexer_1_out3);
  Register register_37 (.D(DATA_IN), .en(and_69_out), .clk(CLK), .Q(register_37_q), .clr(RESET));
  and and_69 (and_69_out, demultiplexer_3_out2, demultiplexer_1_out4);
  Register register_38 (.D(DATA_IN), .en(and_70_out), .clk(CLK), .Q(register_38_q), .clr(RESET));
  and and_70 (and_70_out, demultiplexer_3_out2, demultiplexer_1_out5);
  Register register_39 (.D(DATA_IN), .en(and_71_out), .clk(CLK), .Q(register_39_q), .clr(RESET));
  and and_71 (and_71_out, demultiplexer_3_out2, demultiplexer_1_out6);
  Register register_40 (.D(DATA_IN), .en(and_72_out), .clk(CLK), .Q(register_40_q), .clr(RESET));
  and and_72 (and_72_out, demultiplexer_3_out2, demultiplexer_1_out7);
  Register register_41 (.D(DATA_IN), .en(and_73_out), .clk(CLK), .Q(register_41_q), .clr(RESET));
  and and_73 (and_73_out, demultiplexer_3_out2, demultiplexer_1_out8);
  Register register_42 (.D(DATA_IN), .en(and_74_out), .clk(CLK), .Q(register_42_q), .clr(RESET));
  and and_74 (and_74_out, demultiplexer_3_out2, demultiplexer_1_out9);
  Register register_43 (.D(DATA_IN), .en(and_75_out), .clk(CLK), .Q(register_43_q), .clr(RESET));
  and and_75 (and_75_out, demultiplexer_3_out2, demultiplexer_1_out10);
  Register register_44 (.D(DATA_IN), .en(and_76_out), .clk(CLK), .Q(register_44_q), .clr(RESET));
  and and_76 (and_76_out, demultiplexer_3_out2, demultiplexer_1_out11);
  Register register_45 (.D(DATA_IN), .en(and_77_out), .clk(CLK), .Q(register_45_q), .clr(RESET));
  and and_77 (and_77_out, demultiplexer_3_out2, demultiplexer_1_out12);
  Register register_46 (.D(DATA_IN), .en(and_78_out), .clk(CLK), .Q(register_46_q), .clr(RESET));
  and and_78 (and_78_out, demultiplexer_3_out2, demultiplexer_1_out13);
  Register register_47 (.D(DATA_IN), .en(and_79_out), .clk(CLK), .Q(register_47_q), .clr(RESET));
  and and_79 (and_79_out, demultiplexer_3_out2, demultiplexer_1_out14);
  Register register_48 (.D(DATA_IN), .en(and_80_out), .clk(CLK), .Q(register_48_q), .clr(RESET));
  and and_80 (and_80_out, demultiplexer_3_out2, demultiplexer_1_out15);
  and and_81 (and_81_out, demultiplexer_2_out0, demultiplexer_4_out2);
  assign DATA_OUT = and_81_out ? register_33_q : 8'bz;  // Controlled_Buffer controlled_buffer_33
  and and_82 (and_82_out, demultiplexer_2_out1, demultiplexer_4_out2);
  assign DATA_OUT = and_82_out ? register_34_q : 8'bz;  // Controlled_Buffer controlled_buffer_34
  and and_83 (and_83_out, demultiplexer_2_out2, demultiplexer_4_out2);
  assign DATA_OUT = and_83_out ? register_35_q : 8'bz;  // Controlled_Buffer controlled_buffer_35
  and and_84 (and_84_out, demultiplexer_2_out3, demultiplexer_4_out2);
  assign DATA_OUT = and_84_out ? register_36_q : 8'bz;  // Controlled_Buffer controlled_buffer_36
  and and_85 (and_85_out, demultiplexer_2_out4, demultiplexer_4_out2);
  assign DATA_OUT = and_85_out ? register_37_q : 8'bz;  // Controlled_Buffer controlled_buffer_37
  and and_86 (and_86_out, demultiplexer_2_out5, demultiplexer_4_out2);
  assign DATA_OUT = and_86_out ? register_38_q : 8'bz;  // Controlled_Buffer controlled_buffer_38
  and and_87 (and_87_out, demultiplexer_2_out6, demultiplexer_4_out2);
  assign DATA_OUT = and_87_out ? register_39_q : 8'bz;  // Controlled_Buffer controlled_buffer_39
  and and_88 (and_88_out, demultiplexer_2_out7, demultiplexer_4_out2);
  assign DATA_OUT = and_88_out ? register_40_q : 8'bz;  // Controlled_Buffer controlled_buffer_40
  and and_89 (and_89_out, demultiplexer_2_out8, demultiplexer_4_out2);
  assign DATA_OUT = and_89_out ? register_41_q : 8'bz;  // Controlled_Buffer controlled_buffer_41
  and and_90 (and_90_out, demultiplexer_2_out9, demultiplexer_4_out2);
  assign DATA_OUT = and_90_out ? register_42_q : 8'bz;  // Controlled_Buffer controlled_buffer_42
  and and_91 (and_91_out, demultiplexer_2_out10, demultiplexer_4_out2);
  assign DATA_OUT = and_91_out ? register_43_q : 8'bz;  // Controlled_Buffer controlled_buffer_43
  and and_92 (and_92_out, demultiplexer_2_out11, demultiplexer_4_out2);
  assign DATA_OUT = and_92_out ? register_44_q : 8'bz;  // Controlled_Buffer controlled_buffer_44
  and and_93 (and_93_out, demultiplexer_2_out12, demultiplexer_4_out2);
  assign DATA_OUT = and_93_out ? register_45_q : 8'bz;  // Controlled_Buffer controlled_buffer_45
  and and_94 (and_94_out, demultiplexer_2_out13, demultiplexer_4_out2);
  assign DATA_OUT = and_94_out ? register_46_q : 8'bz;  // Controlled_Buffer controlled_buffer_46
  and and_95 (and_95_out, demultiplexer_2_out14, demultiplexer_4_out2);
  assign DATA_OUT = and_95_out ? register_47_q : 8'bz;  // Controlled_Buffer controlled_buffer_47
  and and_96 (and_96_out, demultiplexer_2_out15, demultiplexer_4_out2);
  assign DATA_OUT = and_96_out ? register_48_q : 8'bz;  // Controlled_Buffer controlled_buffer_48
  and and_97 (and_97_out, demultiplexer_3_out3, demultiplexer_1_out0);
  and and_98 (and_98_out, demultiplexer_3_out3, demultiplexer_1_out1);
  and and_99 (and_99_out, demultiplexer_3_out3, demultiplexer_1_out2);
  and and_100 (and_100_out, demultiplexer_3_out3, demultiplexer_1_out3);
  and and_101 (and_101_out, demultiplexer_3_out3, demultiplexer_1_out4);
  and and_102 (and_102_out, demultiplexer_3_out3, demultiplexer_1_out5);
  and and_103 (and_103_out, demultiplexer_3_out3, demultiplexer_1_out6);
  and and_104 (and_104_out, demultiplexer_3_out3, demultiplexer_1_out7);
  and and_105 (and_105_out, demultiplexer_3_out3, demultiplexer_1_out8);
  and and_106 (and_106_out, demultiplexer_3_out3, demultiplexer_1_out9);
  and and_107 (and_107_out, demultiplexer_3_out3, demultiplexer_1_out10);
  and and_108 (and_108_out, demultiplexer_3_out3, demultiplexer_1_out11);
  and and_109 (and_109_out, demultiplexer_3_out3, demultiplexer_1_out12);
  and and_110 (and_110_out, demultiplexer_3_out3, demultiplexer_1_out13);
  and and_111 (and_111_out, demultiplexer_3_out3, demultiplexer_1_out14);
  and and_112 (and_112_out, demultiplexer_3_out3, demultiplexer_1_out15);
  Register register_49 (.D(DATA_IN), .en(and_97_out), .clk(CLK), .Q(register_49_q), .clr(RESET));
  Register register_50 (.D(DATA_IN), .en(and_98_out), .clk(CLK), .Q(register_50_q), .clr(RESET));
  Register register_51 (.D(DATA_IN), .en(and_99_out), .clk(CLK), .Q(register_51_q), .clr(RESET));
  Register register_52 (.D(DATA_IN), .en(and_100_out), .clk(CLK), .Q(register_52_q), .clr(RESET));
  Register register_53 (.D(DATA_IN), .en(and_101_out), .clk(CLK), .Q(register_53_q), .clr(RESET));
  Register register_54 (.D(DATA_IN), .en(and_102_out), .clk(CLK), .Q(register_54_q), .clr(RESET));
  Register register_55 (.D(DATA_IN), .en(and_103_out), .clk(CLK), .Q(register_55_q), .clr(RESET));
  Register register_56 (.D(DATA_IN), .en(and_104_out), .clk(CLK), .Q(register_56_q), .clr(RESET));
  Register register_57 (.D(DATA_IN), .en(and_105_out), .clk(CLK), .Q(register_57_q), .clr(RESET));
  Register register_58 (.D(DATA_IN), .en(and_106_out), .clk(CLK), .Q(register_58_q), .clr(RESET));
  Register register_59 (.D(DATA_IN), .en(and_107_out), .clk(CLK), .Q(register_59_q), .clr(RESET));
  Register register_60 (.D(DATA_IN), .en(and_108_out), .clk(CLK), .Q(register_60_q), .clr(RESET));
  Register register_61 (.D(DATA_IN), .en(and_109_out), .clk(CLK), .Q(register_61_q), .clr(RESET));
  Register register_62 (.D(DATA_IN), .en(and_110_out), .clk(CLK), .Q(register_62_q), .clr(RESET));
  Register register_63 (.D(DATA_IN), .en(and_111_out), .clk(CLK), .Q(register_63_q), .clr(RESET));
  Register register_64 (.D(DATA_IN), .en(and_112_out), .clk(CLK), .Q(register_64_q), .clr(RESET));
  and and_113 (and_113_out, demultiplexer_2_out0, demultiplexer_4_out3);
  assign DATA_OUT = and_113_out ? register_49_q : 8'bz;  // Controlled_Buffer controlled_buffer_49
  and and_114 (and_114_out, demultiplexer_2_out1, demultiplexer_4_out3);
  assign DATA_OUT = and_114_out ? register_50_q : 8'bz;  // Controlled_Buffer controlled_buffer_50
  and and_115 (and_115_out, demultiplexer_2_out2, demultiplexer_4_out3);
  assign DATA_OUT = and_115_out ? register_51_q : 8'bz;  // Controlled_Buffer controlled_buffer_51
  and and_116 (and_116_out, demultiplexer_2_out3, demultiplexer_4_out3);
  assign DATA_OUT = and_116_out ? register_52_q : 8'bz;  // Controlled_Buffer controlled_buffer_52
  and and_117 (and_117_out, demultiplexer_2_out4, demultiplexer_4_out3);
  assign DATA_OUT = and_117_out ? register_53_q : 8'bz;  // Controlled_Buffer controlled_buffer_53
  and and_118 (and_118_out, demultiplexer_2_out5, demultiplexer_4_out3);
  assign DATA_OUT = and_118_out ? register_54_q : 8'bz;  // Controlled_Buffer controlled_buffer_54
  and and_119 (and_119_out, demultiplexer_2_out6, demultiplexer_4_out3);
  assign DATA_OUT = and_119_out ? register_55_q : 8'bz;  // Controlled_Buffer controlled_buffer_55
  and and_120 (and_120_out, demultiplexer_2_out7, demultiplexer_4_out3);
  assign DATA_OUT = and_120_out ? register_56_q : 8'bz;  // Controlled_Buffer controlled_buffer_56
  and and_121 (and_121_out, demultiplexer_2_out8, demultiplexer_4_out3);
  assign DATA_OUT = and_121_out ? register_57_q : 8'bz;  // Controlled_Buffer controlled_buffer_57
  and and_122 (and_122_out, demultiplexer_2_out9, demultiplexer_4_out3);
  assign DATA_OUT = and_122_out ? register_58_q : 8'bz;  // Controlled_Buffer controlled_buffer_58
  and and_123 (and_123_out, demultiplexer_2_out10, demultiplexer_4_out3);
  assign DATA_OUT = and_123_out ? register_59_q : 8'bz;  // Controlled_Buffer controlled_buffer_59
  and and_124 (and_124_out, demultiplexer_2_out11, demultiplexer_4_out3);
  assign DATA_OUT = and_124_out ? register_60_q : 8'bz;  // Controlled_Buffer controlled_buffer_60
  and and_125 (and_125_out, demultiplexer_2_out12, demultiplexer_4_out3);
  assign DATA_OUT = and_125_out ? register_61_q : 8'bz;  // Controlled_Buffer controlled_buffer_61
  and and_126 (and_126_out, demultiplexer_2_out13, demultiplexer_4_out3);
  assign DATA_OUT = and_126_out ? register_62_q : 8'bz;  // Controlled_Buffer controlled_buffer_62
  and and_127 (and_127_out, demultiplexer_2_out14, demultiplexer_4_out3);
  assign DATA_OUT = and_127_out ? register_63_q : 8'bz;  // Controlled_Buffer controlled_buffer_63
  and and_128 (and_128_out, demultiplexer_2_out15, demultiplexer_4_out3);
  assign DATA_OUT = and_128_out ? register_64_q : 8'bz;  // Controlled_Buffer controlled_buffer_64
  Register register_65 (.D(DATA_IN), .en(and_129_out), .clk(CLK), .Q(register_65_q), .clr(RESET));
  and and_129 (and_129_out, demultiplexer_3_out4, demultiplexer_1_out0);
  Register register_66 (.D(DATA_IN), .en(and_130_out), .clk(CLK), .Q(register_66_q), .clr(RESET));
  and and_130 (and_130_out, demultiplexer_3_out4, demultiplexer_1_out1);
  Register register_67 (.D(DATA_IN), .en(and_131_out), .clk(CLK), .Q(register_67_q), .clr(RESET));
  and and_131 (and_131_out, demultiplexer_3_out4, demultiplexer_1_out2);
  Register register_68 (.D(DATA_IN), .en(and_132_out), .clk(CLK), .Q(register_68_q), .clr(RESET));
  and and_132 (and_132_out, demultiplexer_3_out4, demultiplexer_1_out3);
  Register register_69 (.D(DATA_IN), .en(and_133_out), .clk(CLK), .Q(register_69_q), .clr(RESET));
  and and_133 (and_133_out, demultiplexer_3_out4, demultiplexer_1_out4);
  Register register_70 (.D(DATA_IN), .en(and_134_out), .clk(CLK), .Q(register_70_q), .clr(RESET));
  and and_134 (and_134_out, demultiplexer_3_out4, demultiplexer_1_out5);
  Register register_71 (.D(DATA_IN), .en(and_135_out), .clk(CLK), .Q(register_71_q), .clr(RESET));
  and and_135 (and_135_out, demultiplexer_3_out4, demultiplexer_1_out6);
  Register register_72 (.D(DATA_IN), .en(and_136_out), .clk(CLK), .Q(register_72_q), .clr(RESET));
  and and_136 (and_136_out, demultiplexer_3_out4, demultiplexer_1_out7);
  Register register_73 (.D(DATA_IN), .en(and_137_out), .clk(CLK), .Q(register_73_q), .clr(RESET));
  and and_137 (and_137_out, demultiplexer_3_out4, demultiplexer_1_out8);
  Register register_74 (.D(DATA_IN), .en(and_138_out), .clk(CLK), .Q(register_74_q), .clr(RESET));
  and and_138 (and_138_out, demultiplexer_3_out4, demultiplexer_1_out9);
  Register register_75 (.D(DATA_IN), .en(and_139_out), .clk(CLK), .Q(register_75_q), .clr(RESET));
  and and_139 (and_139_out, demultiplexer_3_out4, demultiplexer_1_out10);
  Register register_76 (.D(DATA_IN), .en(and_140_out), .clk(CLK), .Q(register_76_q), .clr(RESET));
  and and_140 (and_140_out, demultiplexer_3_out4, demultiplexer_1_out11);
  Register register_77 (.D(DATA_IN), .en(and_141_out), .clk(CLK), .Q(register_77_q), .clr(RESET));
  and and_141 (and_141_out, demultiplexer_3_out4, demultiplexer_1_out12);
  Register register_78 (.D(DATA_IN), .en(and_142_out), .clk(CLK), .Q(register_78_q), .clr(RESET));
  and and_142 (and_142_out, demultiplexer_3_out4, demultiplexer_1_out13);
  Register register_79 (.D(DATA_IN), .en(and_143_out), .clk(CLK), .Q(register_79_q), .clr(RESET));
  and and_143 (and_143_out, demultiplexer_3_out4, demultiplexer_1_out14);
  Register register_80 (.D(DATA_IN), .en(and_144_out), .clk(CLK), .Q(register_80_q), .clr(RESET));
  and and_144 (and_144_out, demultiplexer_3_out4, demultiplexer_1_out15);
  and and_145 (and_145_out, demultiplexer_2_out0, demultiplexer_4_out4);
  assign DATA_OUT = and_145_out ? register_65_q : 8'bz;  // Controlled_Buffer controlled_buffer_65
  and and_146 (and_146_out, demultiplexer_2_out1, demultiplexer_4_out4);
  assign DATA_OUT = and_146_out ? register_66_q : 8'bz;  // Controlled_Buffer controlled_buffer_66
  and and_147 (and_147_out, demultiplexer_2_out2, demultiplexer_4_out4);
  assign DATA_OUT = and_147_out ? register_67_q : 8'bz;  // Controlled_Buffer controlled_buffer_67
  and and_148 (and_148_out, demultiplexer_2_out3, demultiplexer_4_out4);
  assign DATA_OUT = and_148_out ? register_68_q : 8'bz;  // Controlled_Buffer controlled_buffer_68
  and and_149 (and_149_out, demultiplexer_2_out4, demultiplexer_4_out4);
  assign DATA_OUT = and_149_out ? register_69_q : 8'bz;  // Controlled_Buffer controlled_buffer_69
  and and_150 (and_150_out, demultiplexer_2_out5, demultiplexer_4_out4);
  assign DATA_OUT = and_150_out ? register_70_q : 8'bz;  // Controlled_Buffer controlled_buffer_70
  and and_151 (and_151_out, demultiplexer_2_out6, demultiplexer_4_out4);
  assign DATA_OUT = and_151_out ? register_71_q : 8'bz;  // Controlled_Buffer controlled_buffer_71
  and and_152 (and_152_out, demultiplexer_2_out7, demultiplexer_4_out4);
  assign DATA_OUT = and_152_out ? register_72_q : 8'bz;  // Controlled_Buffer controlled_buffer_72
  and and_153 (and_153_out, demultiplexer_2_out8, demultiplexer_4_out4);
  assign DATA_OUT = and_153_out ? register_73_q : 8'bz;  // Controlled_Buffer controlled_buffer_73
  and and_154 (and_154_out, demultiplexer_2_out9, demultiplexer_4_out4);
  assign DATA_OUT = and_154_out ? register_74_q : 8'bz;  // Controlled_Buffer controlled_buffer_74
  and and_155 (and_155_out, demultiplexer_2_out10, demultiplexer_4_out4);
  assign DATA_OUT = and_155_out ? register_75_q : 8'bz;  // Controlled_Buffer controlled_buffer_75
  and and_156 (and_156_out, demultiplexer_2_out11, demultiplexer_4_out4);
  assign DATA_OUT = and_156_out ? register_76_q : 8'bz;  // Controlled_Buffer controlled_buffer_76
  and and_157 (and_157_out, demultiplexer_2_out12, demultiplexer_4_out4);
  assign DATA_OUT = and_157_out ? register_77_q : 8'bz;  // Controlled_Buffer controlled_buffer_77
  and and_158 (and_158_out, demultiplexer_2_out13, demultiplexer_4_out4);
  assign DATA_OUT = and_158_out ? register_78_q : 8'bz;  // Controlled_Buffer controlled_buffer_78
  and and_159 (and_159_out, demultiplexer_2_out14, demultiplexer_4_out4);
  assign DATA_OUT = and_159_out ? register_79_q : 8'bz;  // Controlled_Buffer controlled_buffer_79
  and and_160 (and_160_out, demultiplexer_2_out15, demultiplexer_4_out4);
  assign DATA_OUT = and_160_out ? register_80_q : 8'bz;  // Controlled_Buffer controlled_buffer_80
  Register register_81 (.D(DATA_IN), .en(and_161_out), .clk(CLK), .Q(register_81_q), .clr(RESET));
  and and_161 (and_161_out, demultiplexer_3_out5, demultiplexer_1_out0);
  Register register_82 (.D(DATA_IN), .en(and_162_out), .clk(CLK), .Q(register_82_q), .clr(RESET));
  and and_162 (and_162_out, demultiplexer_3_out5, demultiplexer_1_out1);
  Register register_83 (.D(DATA_IN), .en(and_163_out), .clk(CLK), .Q(register_83_q), .clr(RESET));
  and and_163 (and_163_out, demultiplexer_3_out5, demultiplexer_1_out2);
  Register register_84 (.D(DATA_IN), .en(and_164_out), .clk(CLK), .Q(register_84_q), .clr(RESET));
  and and_164 (and_164_out, demultiplexer_3_out5, demultiplexer_1_out3);
  Register register_85 (.D(DATA_IN), .en(and_165_out), .clk(CLK), .Q(register_85_q), .clr(RESET));
  and and_165 (and_165_out, demultiplexer_3_out5, demultiplexer_1_out4);
  Register register_86 (.D(DATA_IN), .en(and_166_out), .clk(CLK), .Q(register_86_q), .clr(RESET));
  and and_166 (and_166_out, demultiplexer_3_out5, demultiplexer_1_out5);
  Register register_87 (.D(DATA_IN), .en(and_167_out), .clk(CLK), .Q(register_87_q), .clr(RESET));
  and and_167 (and_167_out, demultiplexer_3_out5, demultiplexer_1_out6);
  Register register_88 (.D(DATA_IN), .en(and_168_out), .clk(CLK), .Q(register_88_q), .clr(RESET));
  and and_168 (and_168_out, demultiplexer_3_out5, demultiplexer_1_out7);
  Register register_89 (.D(DATA_IN), .en(and_169_out), .clk(CLK), .Q(register_89_q), .clr(RESET));
  and and_169 (and_169_out, demultiplexer_3_out5, demultiplexer_1_out8);
  Register register_90 (.D(DATA_IN), .en(and_170_out), .clk(CLK), .Q(register_90_q), .clr(RESET));
  and and_170 (and_170_out, demultiplexer_3_out5, demultiplexer_1_out9);
  Register register_91 (.D(DATA_IN), .en(and_171_out), .clk(CLK), .Q(register_91_q), .clr(RESET));
  and and_171 (and_171_out, demultiplexer_3_out5, demultiplexer_1_out10);
  Register register_92 (.D(DATA_IN), .en(and_172_out), .clk(CLK), .Q(register_92_q), .clr(RESET));
  and and_172 (and_172_out, demultiplexer_3_out5, demultiplexer_1_out11);
  Register register_93 (.D(DATA_IN), .en(and_173_out), .clk(CLK), .Q(register_93_q), .clr(RESET));
  and and_173 (and_173_out, demultiplexer_3_out5, demultiplexer_1_out12);
  Register register_94 (.D(DATA_IN), .en(and_174_out), .clk(CLK), .Q(register_94_q), .clr(RESET));
  and and_174 (and_174_out, demultiplexer_3_out5, demultiplexer_1_out13);
  Register register_95 (.D(DATA_IN), .en(and_175_out), .clk(CLK), .Q(register_95_q), .clr(RESET));
  and and_175 (and_175_out, demultiplexer_3_out5, demultiplexer_1_out14);
  Register register_96 (.D(DATA_IN), .en(and_176_out), .clk(CLK), .Q(register_96_q), .clr(RESET));
  and and_176 (and_176_out, demultiplexer_3_out5, demultiplexer_1_out15);
  and and_177 (and_177_out, demultiplexer_2_out0, demultiplexer_4_out5);
  assign DATA_OUT = and_177_out ? register_81_q : 8'bz;  // Controlled_Buffer controlled_buffer_81
  and and_178 (and_178_out, demultiplexer_2_out1, demultiplexer_4_out5);
  assign DATA_OUT = and_178_out ? register_82_q : 8'bz;  // Controlled_Buffer controlled_buffer_82
  and and_179 (and_179_out, demultiplexer_2_out2, demultiplexer_4_out5);
  assign DATA_OUT = and_179_out ? register_83_q : 8'bz;  // Controlled_Buffer controlled_buffer_83
  and and_180 (and_180_out, demultiplexer_2_out3, demultiplexer_4_out5);
  assign DATA_OUT = and_180_out ? register_84_q : 8'bz;  // Controlled_Buffer controlled_buffer_84
  and and_181 (and_181_out, demultiplexer_2_out4, demultiplexer_4_out5);
  assign DATA_OUT = and_181_out ? register_85_q : 8'bz;  // Controlled_Buffer controlled_buffer_85
  and and_182 (and_182_out, demultiplexer_2_out5, demultiplexer_4_out5);
  assign DATA_OUT = and_182_out ? register_86_q : 8'bz;  // Controlled_Buffer controlled_buffer_86
  and and_183 (and_183_out, demultiplexer_2_out6, demultiplexer_4_out5);
  assign DATA_OUT = and_183_out ? register_87_q : 8'bz;  // Controlled_Buffer controlled_buffer_87
  and and_184 (and_184_out, demultiplexer_2_out7, demultiplexer_4_out5);
  assign DATA_OUT = and_184_out ? register_88_q : 8'bz;  // Controlled_Buffer controlled_buffer_88
  and and_185 (and_185_out, demultiplexer_2_out8, demultiplexer_4_out5);
  assign DATA_OUT = and_185_out ? register_89_q : 8'bz;  // Controlled_Buffer controlled_buffer_89
  and and_186 (and_186_out, demultiplexer_2_out9, demultiplexer_4_out5);
  assign DATA_OUT = and_186_out ? register_90_q : 8'bz;  // Controlled_Buffer controlled_buffer_90
  and and_187 (and_187_out, demultiplexer_2_out10, demultiplexer_4_out5);
  assign DATA_OUT = and_187_out ? register_91_q : 8'bz;  // Controlled_Buffer controlled_buffer_91
  and and_188 (and_188_out, demultiplexer_2_out11, demultiplexer_4_out5);
  assign DATA_OUT = and_188_out ? register_92_q : 8'bz;  // Controlled_Buffer controlled_buffer_92
  and and_189 (and_189_out, demultiplexer_2_out12, demultiplexer_4_out5);
  assign DATA_OUT = and_189_out ? register_93_q : 8'bz;  // Controlled_Buffer controlled_buffer_93
  and and_190 (and_190_out, demultiplexer_2_out13, demultiplexer_4_out5);
  assign DATA_OUT = and_190_out ? register_94_q : 8'bz;  // Controlled_Buffer controlled_buffer_94
  and and_191 (and_191_out, demultiplexer_2_out14, demultiplexer_4_out5);
  assign DATA_OUT = and_191_out ? register_95_q : 8'bz;  // Controlled_Buffer controlled_buffer_95
  and and_192 (and_192_out, demultiplexer_2_out15, demultiplexer_4_out5);
  assign DATA_OUT = and_192_out ? register_96_q : 8'bz;  // Controlled_Buffer controlled_buffer_96
  and and_193 (and_193_out, demultiplexer_3_out6, demultiplexer_1_out0);
  and and_194 (and_194_out, demultiplexer_3_out6, demultiplexer_1_out1);
  and and_195 (and_195_out, demultiplexer_3_out6, demultiplexer_1_out2);
  and and_196 (and_196_out, demultiplexer_3_out6, demultiplexer_1_out3);
  and and_197 (and_197_out, demultiplexer_3_out6, demultiplexer_1_out4);
  and and_198 (and_198_out, demultiplexer_3_out6, demultiplexer_1_out5);
  and and_199 (and_199_out, demultiplexer_3_out6, demultiplexer_1_out6);
  and and_200 (and_200_out, demultiplexer_3_out6, demultiplexer_1_out7);
  and and_201 (and_201_out, demultiplexer_3_out6, demultiplexer_1_out8);
  and and_202 (and_202_out, demultiplexer_3_out6, demultiplexer_1_out9);
  and and_203 (and_203_out, demultiplexer_3_out6, demultiplexer_1_out10);
  and and_204 (and_204_out, demultiplexer_3_out6, demultiplexer_1_out11);
  and and_205 (and_205_out, demultiplexer_3_out6, demultiplexer_1_out12);
  and and_206 (and_206_out, demultiplexer_3_out6, demultiplexer_1_out13);
  and and_207 (and_207_out, demultiplexer_3_out6, demultiplexer_1_out14);
  and and_208 (and_208_out, demultiplexer_3_out6, demultiplexer_1_out15);
  Register register_97 (.D(DATA_IN), .en(and_193_out), .clk(CLK), .Q(register_97_q), .clr(RESET));
  Register register_98 (.D(DATA_IN), .en(and_194_out), .clk(CLK), .Q(register_98_q), .clr(RESET));
  Register register_99 (.D(DATA_IN), .en(and_195_out), .clk(CLK), .Q(register_99_q), .clr(RESET));
  Register register_100 (.D(DATA_IN), .en(and_196_out), .clk(CLK), .Q(register_100_q), .clr(RESET));
  Register register_101 (.D(DATA_IN), .en(and_197_out), .clk(CLK), .Q(register_101_q), .clr(RESET));
  Register register_102 (.D(DATA_IN), .en(and_198_out), .clk(CLK), .Q(register_102_q), .clr(RESET));
  Register register_103 (.D(DATA_IN), .en(and_199_out), .clk(CLK), .Q(register_103_q), .clr(RESET));
  Register register_104 (.D(DATA_IN), .en(and_200_out), .clk(CLK), .Q(register_104_q), .clr(RESET));
  Register register_105 (.D(DATA_IN), .en(and_201_out), .clk(CLK), .Q(register_105_q), .clr(RESET));
  Register register_106 (.D(DATA_IN), .en(and_202_out), .clk(CLK), .Q(register_106_q), .clr(RESET));
  Register register_107 (.D(DATA_IN), .en(and_203_out), .clk(CLK), .Q(register_107_q), .clr(RESET));
  Register register_108 (.D(DATA_IN), .en(and_204_out), .clk(CLK), .Q(register_108_q), .clr(RESET));
  Register register_109 (.D(DATA_IN), .en(and_205_out), .clk(CLK), .Q(register_109_q), .clr(RESET));
  Register register_110 (.D(DATA_IN), .en(and_206_out), .clk(CLK), .Q(register_110_q), .clr(RESET));
  Register register_111 (.D(DATA_IN), .en(and_207_out), .clk(CLK), .Q(register_111_q), .clr(RESET));
  Register register_112 (.D(DATA_IN), .en(and_208_out), .clk(CLK), .Q(register_112_q), .clr(RESET));
  and and_209 (and_209_out, demultiplexer_2_out0, demultiplexer_4_out6);
  assign DATA_OUT = and_209_out ? register_97_q : 8'bz;  // Controlled_Buffer controlled_buffer_97
  and and_210 (and_210_out, demultiplexer_2_out1, demultiplexer_4_out6);
  assign DATA_OUT = and_210_out ? register_98_q : 8'bz;  // Controlled_Buffer controlled_buffer_98
  and and_211 (and_211_out, demultiplexer_2_out2, demultiplexer_4_out6);
  assign DATA_OUT = and_211_out ? register_99_q : 8'bz;  // Controlled_Buffer controlled_buffer_99
  and and_212 (and_212_out, demultiplexer_2_out3, demultiplexer_4_out6);
  assign DATA_OUT = and_212_out ? register_100_q : 8'bz;  // Controlled_Buffer controlled_buffer_100
  and and_213 (and_213_out, demultiplexer_2_out4, demultiplexer_4_out6);
  assign DATA_OUT = and_213_out ? register_101_q : 8'bz;  // Controlled_Buffer controlled_buffer_101
  and and_214 (and_214_out, demultiplexer_2_out5, demultiplexer_4_out6);
  assign DATA_OUT = and_214_out ? register_102_q : 8'bz;  // Controlled_Buffer controlled_buffer_102
  and and_215 (and_215_out, demultiplexer_2_out6, demultiplexer_4_out6);
  assign DATA_OUT = and_215_out ? register_103_q : 8'bz;  // Controlled_Buffer controlled_buffer_103
  and and_216 (and_216_out, demultiplexer_2_out7, demultiplexer_4_out6);
  assign DATA_OUT = and_216_out ? register_104_q : 8'bz;  // Controlled_Buffer controlled_buffer_104
  and and_217 (and_217_out, demultiplexer_2_out8, demultiplexer_4_out6);
  assign DATA_OUT = and_217_out ? register_105_q : 8'bz;  // Controlled_Buffer controlled_buffer_105
  and and_218 (and_218_out, demultiplexer_2_out9, demultiplexer_4_out6);
  assign DATA_OUT = and_218_out ? register_106_q : 8'bz;  // Controlled_Buffer controlled_buffer_106
  and and_219 (and_219_out, demultiplexer_2_out10, demultiplexer_4_out6);
  assign DATA_OUT = and_219_out ? register_107_q : 8'bz;  // Controlled_Buffer controlled_buffer_107
  and and_220 (and_220_out, demultiplexer_2_out11, demultiplexer_4_out6);
  assign DATA_OUT = and_220_out ? register_108_q : 8'bz;  // Controlled_Buffer controlled_buffer_108
  and and_221 (and_221_out, demultiplexer_2_out12, demultiplexer_4_out6);
  assign DATA_OUT = and_221_out ? register_109_q : 8'bz;  // Controlled_Buffer controlled_buffer_109
  and and_222 (and_222_out, demultiplexer_2_out13, demultiplexer_4_out6);
  assign DATA_OUT = and_222_out ? register_110_q : 8'bz;  // Controlled_Buffer controlled_buffer_110
  and and_223 (and_223_out, demultiplexer_2_out14, demultiplexer_4_out6);
  assign DATA_OUT = and_223_out ? register_111_q : 8'bz;  // Controlled_Buffer controlled_buffer_111
  and and_224 (and_224_out, demultiplexer_2_out15, demultiplexer_4_out6);
  assign DATA_OUT = and_224_out ? register_112_q : 8'bz;  // Controlled_Buffer controlled_buffer_112
  Register register_113 (.D(DATA_IN), .en(and_225_out), .clk(CLK), .Q(register_113_q), .clr(RESET));
  and and_225 (and_225_out, demultiplexer_3_out7, demultiplexer_1_out0);
  Register register_114 (.D(DATA_IN), .en(and_226_out), .clk(CLK), .Q(register_114_q), .clr(RESET));
  and and_226 (and_226_out, demultiplexer_3_out7, demultiplexer_1_out1);
  Register register_115 (.D(DATA_IN), .en(and_227_out), .clk(CLK), .Q(register_115_q), .clr(RESET));
  and and_227 (and_227_out, demultiplexer_3_out7, demultiplexer_1_out2);
  Register register_116 (.D(DATA_IN), .en(and_228_out), .clk(CLK), .Q(register_116_q), .clr(RESET));
  and and_228 (and_228_out, demultiplexer_3_out7, demultiplexer_1_out3);
  Register register_117 (.D(DATA_IN), .en(and_229_out), .clk(CLK), .Q(register_117_q), .clr(RESET));
  and and_229 (and_229_out, demultiplexer_3_out7, demultiplexer_1_out4);
  Register register_118 (.D(DATA_IN), .en(and_230_out), .clk(CLK), .Q(register_118_q), .clr(RESET));
  and and_230 (and_230_out, demultiplexer_3_out7, demultiplexer_1_out5);
  Register register_119 (.D(DATA_IN), .en(and_231_out), .clk(CLK), .Q(register_119_q), .clr(RESET));
  and and_231 (and_231_out, demultiplexer_3_out7, demultiplexer_1_out6);
  Register register_120 (.D(DATA_IN), .en(and_232_out), .clk(CLK), .Q(register_120_q), .clr(RESET));
  and and_232 (and_232_out, demultiplexer_3_out7, demultiplexer_1_out7);
  Register register_121 (.D(DATA_IN), .en(and_233_out), .clk(CLK), .Q(register_121_q), .clr(RESET));
  and and_233 (and_233_out, demultiplexer_3_out7, demultiplexer_1_out8);
  Register register_122 (.D(DATA_IN), .en(and_234_out), .clk(CLK), .Q(register_122_q), .clr(RESET));
  and and_234 (and_234_out, demultiplexer_3_out7, demultiplexer_1_out9);
  Register register_123 (.D(DATA_IN), .en(and_235_out), .clk(CLK), .Q(register_123_q), .clr(RESET));
  and and_235 (and_235_out, demultiplexer_3_out7, demultiplexer_1_out10);
  Register register_124 (.D(DATA_IN), .en(and_236_out), .clk(CLK), .Q(register_124_q), .clr(RESET));
  and and_236 (and_236_out, demultiplexer_3_out7, demultiplexer_1_out11);
  Register register_125 (.D(DATA_IN), .en(and_237_out), .clk(CLK), .Q(register_125_q), .clr(RESET));
  and and_237 (and_237_out, demultiplexer_3_out7, demultiplexer_1_out12);
  Register register_126 (.D(DATA_IN), .en(and_238_out), .clk(CLK), .Q(register_126_q), .clr(RESET));
  and and_238 (and_238_out, demultiplexer_3_out7, demultiplexer_1_out13);
  Register register_127 (.D(DATA_IN), .en(and_239_out), .clk(CLK), .Q(register_127_q), .clr(RESET));
  and and_239 (and_239_out, demultiplexer_3_out7, demultiplexer_1_out14);
  Register register_128 (.D(DATA_IN), .en(and_240_out), .clk(CLK), .Q(register_128_q), .clr(RESET));
  and and_240 (and_240_out, demultiplexer_3_out7, demultiplexer_1_out15);
  Demultiplexer #(.select(4)) demultiplexer_3 (
    .out0(demultiplexer_3_out0), .out1(demultiplexer_3_out1), .out2(demultiplexer_3_out2),
    .out3(demultiplexer_3_out3), .out4(demultiplexer_3_out4), .out5(demultiplexer_3_out5),
    .out6(demultiplexer_3_out6), .out7(demultiplexer_3_out7), .out8(demultiplexer_3_out8),
    .out9(demultiplexer_3_out9), .out10(demultiplexer_3_out10), .out11(demultiplexer_3_out11),
    .out12(demultiplexer_3_out12), .out13(demultiplexer_3_out13), .out14(demultiplexer_3_out14),
    .out15(demultiplexer_3_out15), .in(WRITE), .sel(WRITE_ADDRESS[3:0]));
  and and_241 (and_241_out, demultiplexer_2_out0, demultiplexer_4_out7);
  assign DATA_OUT = and_241_out ? register_113_q : 8'bz;  // Controlled_Buffer controlled_buffer_113
  and and_242 (and_242_out, demultiplexer_2_out1, demultiplexer_4_out7);
  assign DATA_OUT = and_242_out ? register_114_q : 8'bz;  // Controlled_Buffer controlled_buffer_114
  and and_243 (and_243_out, demultiplexer_2_out2, demultiplexer_4_out7);
  assign DATA_OUT = and_243_out ? register_115_q : 8'bz;  // Controlled_Buffer controlled_buffer_115
  and and_244 (and_244_out, demultiplexer_2_out3, demultiplexer_4_out7);
  assign DATA_OUT = and_244_out ? register_116_q : 8'bz;  // Controlled_Buffer controlled_buffer_116
  and and_245 (and_245_out, demultiplexer_2_out4, demultiplexer_4_out7);
  assign DATA_OUT = and_245_out ? register_117_q : 8'bz;  // Controlled_Buffer controlled_buffer_117
  and and_246 (and_246_out, demultiplexer_2_out5, demultiplexer_4_out7);
  assign DATA_OUT = and_246_out ? register_118_q : 8'bz;  // Controlled_Buffer controlled_buffer_118
  and and_247 (and_247_out, demultiplexer_2_out6, demultiplexer_4_out7);
  assign DATA_OUT = and_247_out ? register_119_q : 8'bz;  // Controlled_Buffer controlled_buffer_119
  and and_248 (and_248_out, demultiplexer_2_out7, demultiplexer_4_out7);
  assign DATA_OUT = and_248_out ? register_120_q : 8'bz;  // Controlled_Buffer controlled_buffer_120
  and and_249 (and_249_out, demultiplexer_2_out8, demultiplexer_4_out7);
  assign DATA_OUT = and_249_out ? register_121_q : 8'bz;  // Controlled_Buffer controlled_buffer_121
  and and_250 (and_250_out, demultiplexer_2_out9, demultiplexer_4_out7);
  assign DATA_OUT = and_250_out ? register_122_q : 8'bz;  // Controlled_Buffer controlled_buffer_122
  and and_251 (and_251_out, demultiplexer_2_out10, demultiplexer_4_out7);
  assign DATA_OUT = and_251_out ? register_123_q : 8'bz;  // Controlled_Buffer controlled_buffer_123
  and and_252 (and_252_out, demultiplexer_2_out11, demultiplexer_4_out7);
  assign DATA_OUT = and_252_out ? register_124_q : 8'bz;  // Controlled_Buffer controlled_buffer_124
  and and_253 (and_253_out, demultiplexer_2_out12, demultiplexer_4_out7);
  assign DATA_OUT = and_253_out ? register_125_q : 8'bz;  // Controlled_Buffer controlled_buffer_125
  and and_254 (and_254_out, demultiplexer_2_out13, demultiplexer_4_out7);
  assign DATA_OUT = and_254_out ? register_126_q : 8'bz;  // Controlled_Buffer controlled_buffer_126
  and and_255 (and_255_out, demultiplexer_2_out14, demultiplexer_4_out7);
  assign DATA_OUT = and_255_out ? register_127_q : 8'bz;  // Controlled_Buffer controlled_buffer_127
  and and_256 (and_256_out, demultiplexer_2_out15, demultiplexer_4_out7);
  assign DATA_OUT = and_256_out ? register_128_q : 8'bz;  // Controlled_Buffer controlled_buffer_128
  Register register_129 (.D(DATA_IN), .en(and_257_out), .clk(CLK), .Q(register_129_q), .clr(RESET));
  and and_257 (and_257_out, demultiplexer_3_out8, demultiplexer_1_out0);
  Register register_130 (.D(DATA_IN), .en(and_258_out), .clk(CLK), .Q(register_130_q), .clr(RESET));
  and and_258 (and_258_out, demultiplexer_3_out8, demultiplexer_1_out1);
  Register register_131 (.D(DATA_IN), .en(and_259_out), .clk(CLK), .Q(register_131_q), .clr(RESET));
  and and_259 (and_259_out, demultiplexer_3_out8, demultiplexer_1_out2);
  Register register_132 (.D(DATA_IN), .en(and_260_out), .clk(CLK), .Q(register_132_q), .clr(RESET));
  and and_260 (and_260_out, demultiplexer_3_out8, demultiplexer_1_out3);
  Register register_133 (.D(DATA_IN), .en(and_261_out), .clk(CLK), .Q(register_133_q), .clr(RESET));
  and and_261 (and_261_out, demultiplexer_3_out8, demultiplexer_1_out4);
  Register register_134 (.D(DATA_IN), .en(and_262_out), .clk(CLK), .Q(register_134_q), .clr(RESET));
  and and_262 (and_262_out, demultiplexer_3_out8, demultiplexer_1_out5);
  Register register_135 (.D(DATA_IN), .en(and_263_out), .clk(CLK), .Q(register_135_q), .clr(RESET));
  and and_263 (and_263_out, demultiplexer_3_out8, demultiplexer_1_out6);
  Register register_136 (.D(DATA_IN), .en(and_264_out), .clk(CLK), .Q(register_136_q), .clr(RESET));
  and and_264 (and_264_out, demultiplexer_3_out8, demultiplexer_1_out7);
  Register register_137 (.D(DATA_IN), .en(and_265_out), .clk(CLK), .Q(register_137_q), .clr(RESET));
  and and_265 (and_265_out, demultiplexer_3_out8, demultiplexer_1_out8);
  Register register_138 (.D(DATA_IN), .en(and_266_out), .clk(CLK), .Q(register_138_q), .clr(RESET));
  and and_266 (and_266_out, demultiplexer_3_out8, demultiplexer_1_out9);
  Register register_139 (.D(DATA_IN), .en(and_267_out), .clk(CLK), .Q(register_139_q), .clr(RESET));
  and and_267 (and_267_out, demultiplexer_3_out8, demultiplexer_1_out10);
  Register register_140 (.D(DATA_IN), .en(and_268_out), .clk(CLK), .Q(register_140_q), .clr(RESET));
  and and_268 (and_268_out, demultiplexer_3_out8, demultiplexer_1_out11);
  Register register_141 (.D(DATA_IN), .en(and_269_out), .clk(CLK), .Q(register_141_q), .clr(RESET));
  and and_269 (and_269_out, demultiplexer_3_out8, demultiplexer_1_out12);
  Register register_142 (.D(DATA_IN), .en(and_270_out), .clk(CLK), .Q(register_142_q), .clr(RESET));
  and and_270 (and_270_out, demultiplexer_3_out8, demultiplexer_1_out13);
  Register register_143 (.D(DATA_IN), .en(and_271_out), .clk(CLK), .Q(register_143_q), .clr(RESET));
  and and_271 (and_271_out, demultiplexer_3_out8, demultiplexer_1_out14);
  Register register_144 (.D(DATA_IN), .en(and_272_out), .clk(CLK), .Q(register_144_q), .clr(RESET));
  and and_272 (and_272_out, demultiplexer_3_out8, demultiplexer_1_out15);
  Demultiplexer #(.select(4)) demultiplexer_4 (
    .out0(demultiplexer_4_out0), .out1(demultiplexer_4_out1), .out2(demultiplexer_4_out2),
    .out3(demultiplexer_4_out3), .out4(demultiplexer_4_out4), .out5(demultiplexer_4_out5),
    .out6(demultiplexer_4_out6), .out7(demultiplexer_4_out7), .out8(demultiplexer_4_out8),
    .out9(demultiplexer_4_out9), .out10(demultiplexer_4_out10), .out11(demultiplexer_4_out11),
    .out12(demultiplexer_4_out12), .out13(demultiplexer_4_out13), .out14(demultiplexer_4_out14),
    .out15(demultiplexer_4_out15), .in(READ), .sel(READ_ADDRESS[3:0]));
  and and_273 (and_273_out, demultiplexer_2_out0, demultiplexer_4_out8);
  and and_274 (and_274_out, demultiplexer_2_out1, demultiplexer_4_out8);
  and and_275 (and_275_out, demultiplexer_2_out2, demultiplexer_4_out8);
  and and_276 (and_276_out, demultiplexer_2_out3, demultiplexer_4_out8);
  and and_277 (and_277_out, demultiplexer_2_out4, demultiplexer_4_out8);
  and and_278 (and_278_out, demultiplexer_2_out5, demultiplexer_4_out8);
  and and_279 (and_279_out, demultiplexer_2_out6, demultiplexer_4_out8);
  and and_280 (and_280_out, demultiplexer_2_out7, demultiplexer_4_out8);
  and and_281 (and_281_out, demultiplexer_2_out8, demultiplexer_4_out8);
  and and_282 (and_282_out, demultiplexer_2_out9, demultiplexer_4_out8);
  and and_283 (and_283_out, demultiplexer_2_out10, demultiplexer_4_out8);
  and and_284 (and_284_out, demultiplexer_2_out11, demultiplexer_4_out8);
  and and_285 (and_285_out, demultiplexer_2_out12, demultiplexer_4_out8);
  and and_286 (and_286_out, demultiplexer_2_out13, demultiplexer_4_out8);
  and and_287 (and_287_out, demultiplexer_2_out14, demultiplexer_4_out8);
  and and_288 (and_288_out, demultiplexer_2_out15, demultiplexer_4_out8);
  assign DATA_OUT = and_273_out ? register_129_q : 8'bz;  // Controlled_Buffer controlled_buffer_129
  and and_289 (and_289_out, demultiplexer_3_out9, demultiplexer_1_out0);
  assign DATA_OUT = and_274_out ? register_130_q : 8'bz;  // Controlled_Buffer controlled_buffer_130
  and and_290 (and_290_out, demultiplexer_3_out9, demultiplexer_1_out1);
  assign DATA_OUT = and_275_out ? register_131_q : 8'bz;  // Controlled_Buffer controlled_buffer_131
  and and_291 (and_291_out, demultiplexer_3_out9, demultiplexer_1_out2);
  assign DATA_OUT = and_276_out ? register_132_q : 8'bz;  // Controlled_Buffer controlled_buffer_132
  and and_292 (and_292_out, demultiplexer_3_out9, demultiplexer_1_out3);
  assign DATA_OUT = and_277_out ? register_133_q : 8'bz;  // Controlled_Buffer controlled_buffer_133
  and and_293 (and_293_out, demultiplexer_3_out9, demultiplexer_1_out4);
  assign DATA_OUT = and_278_out ? register_134_q : 8'bz;  // Controlled_Buffer controlled_buffer_134
  and and_294 (and_294_out, demultiplexer_3_out9, demultiplexer_1_out5);
  assign DATA_OUT = and_279_out ? register_135_q : 8'bz;  // Controlled_Buffer controlled_buffer_135
  and and_295 (and_295_out, demultiplexer_3_out9, demultiplexer_1_out6);
  assign DATA_OUT = and_280_out ? register_136_q : 8'bz;  // Controlled_Buffer controlled_buffer_136
  and and_296 (and_296_out, demultiplexer_3_out9, demultiplexer_1_out7);
  assign DATA_OUT = and_281_out ? register_137_q : 8'bz;  // Controlled_Buffer controlled_buffer_137
  and and_297 (and_297_out, demultiplexer_3_out9, demultiplexer_1_out8);
  assign DATA_OUT = and_282_out ? register_138_q : 8'bz;  // Controlled_Buffer controlled_buffer_138
  and and_298 (and_298_out, demultiplexer_3_out9, demultiplexer_1_out9);
  assign DATA_OUT = and_283_out ? register_139_q : 8'bz;  // Controlled_Buffer controlled_buffer_139
  and and_299 (and_299_out, demultiplexer_3_out9, demultiplexer_1_out10);
  assign DATA_OUT = and_284_out ? register_140_q : 8'bz;  // Controlled_Buffer controlled_buffer_140
  and and_300 (and_300_out, demultiplexer_3_out9, demultiplexer_1_out11);
  assign DATA_OUT = and_285_out ? register_141_q : 8'bz;  // Controlled_Buffer controlled_buffer_141
  and and_301 (and_301_out, demultiplexer_3_out9, demultiplexer_1_out12);
  assign DATA_OUT = and_286_out ? register_142_q : 8'bz;  // Controlled_Buffer controlled_buffer_142
  and and_302 (and_302_out, demultiplexer_3_out9, demultiplexer_1_out13);
  assign DATA_OUT = and_287_out ? register_143_q : 8'bz;  // Controlled_Buffer controlled_buffer_143
  and and_303 (and_303_out, demultiplexer_3_out9, demultiplexer_1_out14);
  assign DATA_OUT = and_288_out ? register_144_q : 8'bz;  // Controlled_Buffer controlled_buffer_144
  and and_304 (and_304_out, demultiplexer_3_out9, demultiplexer_1_out15);
  Register register_145 (.D(DATA_IN), .en(and_289_out), .clk(CLK), .Q(register_145_q), .clr(RESET));
  Register register_146 (.D(DATA_IN), .en(and_290_out), .clk(CLK), .Q(register_146_q), .clr(RESET));
  Register register_147 (.D(DATA_IN), .en(and_291_out), .clk(CLK), .Q(register_147_q), .clr(RESET));
  Register register_148 (.D(DATA_IN), .en(and_292_out), .clk(CLK), .Q(register_148_q), .clr(RESET));
  Register register_149 (.D(DATA_IN), .en(and_293_out), .clk(CLK), .Q(register_149_q), .clr(RESET));
  Register register_150 (.D(DATA_IN), .en(and_294_out), .clk(CLK), .Q(register_150_q), .clr(RESET));
  Register register_151 (.D(DATA_IN), .en(and_295_out), .clk(CLK), .Q(register_151_q), .clr(RESET));
  Register register_152 (.D(DATA_IN), .en(and_296_out), .clk(CLK), .Q(register_152_q), .clr(RESET));
  Register register_153 (.D(DATA_IN), .en(and_297_out), .clk(CLK), .Q(register_153_q), .clr(RESET));
  Register register_154 (.D(DATA_IN), .en(and_298_out), .clk(CLK), .Q(register_154_q), .clr(RESET));
  Register register_155 (.D(DATA_IN), .en(and_299_out), .clk(CLK), .Q(register_155_q), .clr(RESET));
  Register register_156 (.D(DATA_IN), .en(and_300_out), .clk(CLK), .Q(register_156_q), .clr(RESET));
  Register register_157 (.D(DATA_IN), .en(and_301_out), .clk(CLK), .Q(register_157_q), .clr(RESET));
  Register register_158 (.D(DATA_IN), .en(and_302_out), .clk(CLK), .Q(register_158_q), .clr(RESET));
  Register register_159 (.D(DATA_IN), .en(and_303_out), .clk(CLK), .Q(register_159_q), .clr(RESET));
  Register register_160 (.D(DATA_IN), .en(and_304_out), .clk(CLK), .Q(register_160_q), .clr(RESET));
  and and_305 (and_305_out, demultiplexer_2_out0, demultiplexer_4_out9);
  assign DATA_OUT = and_305_out ? register_145_q : 8'bz;  // Controlled_Buffer controlled_buffer_145
  and and_306 (and_306_out, demultiplexer_2_out1, demultiplexer_4_out9);
  assign DATA_OUT = and_306_out ? register_146_q : 8'bz;  // Controlled_Buffer controlled_buffer_146
  and and_307 (and_307_out, demultiplexer_2_out2, demultiplexer_4_out9);
  assign DATA_OUT = and_307_out ? register_147_q : 8'bz;  // Controlled_Buffer controlled_buffer_147
  and and_308 (and_308_out, demultiplexer_2_out3, demultiplexer_4_out9);
  assign DATA_OUT = and_308_out ? register_148_q : 8'bz;  // Controlled_Buffer controlled_buffer_148
  and and_309 (and_309_out, demultiplexer_2_out4, demultiplexer_4_out9);
  assign DATA_OUT = and_309_out ? register_149_q : 8'bz;  // Controlled_Buffer controlled_buffer_149
  and and_310 (and_310_out, demultiplexer_2_out5, demultiplexer_4_out9);
  assign DATA_OUT = and_310_out ? register_150_q : 8'bz;  // Controlled_Buffer controlled_buffer_150
  and and_311 (and_311_out, demultiplexer_2_out6, demultiplexer_4_out9);
  assign DATA_OUT = and_311_out ? register_151_q : 8'bz;  // Controlled_Buffer controlled_buffer_151
  and and_312 (and_312_out, demultiplexer_2_out7, demultiplexer_4_out9);
  assign DATA_OUT = and_312_out ? register_152_q : 8'bz;  // Controlled_Buffer controlled_buffer_152
  and and_313 (and_313_out, demultiplexer_2_out8, demultiplexer_4_out9);
  assign DATA_OUT = and_313_out ? register_153_q : 8'bz;  // Controlled_Buffer controlled_buffer_153
  and and_314 (and_314_out, demultiplexer_2_out9, demultiplexer_4_out9);
  assign DATA_OUT = and_314_out ? register_154_q : 8'bz;  // Controlled_Buffer controlled_buffer_154
  and and_315 (and_315_out, demultiplexer_2_out10, demultiplexer_4_out9);
  assign DATA_OUT = and_315_out ? register_155_q : 8'bz;  // Controlled_Buffer controlled_buffer_155
  and and_316 (and_316_out, demultiplexer_2_out11, demultiplexer_4_out9);
  assign DATA_OUT = and_316_out ? register_156_q : 8'bz;  // Controlled_Buffer controlled_buffer_156
  and and_317 (and_317_out, demultiplexer_2_out12, demultiplexer_4_out9);
  assign DATA_OUT = and_317_out ? register_157_q : 8'bz;  // Controlled_Buffer controlled_buffer_157
  and and_318 (and_318_out, demultiplexer_2_out13, demultiplexer_4_out9);
  assign DATA_OUT = and_318_out ? register_158_q : 8'bz;  // Controlled_Buffer controlled_buffer_158
  and and_319 (and_319_out, demultiplexer_2_out14, demultiplexer_4_out9);
  assign DATA_OUT = and_319_out ? register_159_q : 8'bz;  // Controlled_Buffer controlled_buffer_159
  and and_320 (and_320_out, demultiplexer_2_out15, demultiplexer_4_out9);
  assign DATA_OUT = and_320_out ? register_160_q : 8'bz;  // Controlled_Buffer controlled_buffer_160
  Register register_161 (.D(DATA_IN), .en(and_321_out), .clk(CLK), .Q(register_161_q), .clr(RESET));
  and and_321 (and_321_out, demultiplexer_3_out10, demultiplexer_1_out0);
  Register register_162 (.D(DATA_IN), .en(and_322_out), .clk(CLK), .Q(register_162_q), .clr(RESET));
  and and_322 (and_322_out, demultiplexer_3_out10, demultiplexer_1_out1);
  Register register_163 (.D(DATA_IN), .en(and_323_out), .clk(CLK), .Q(register_163_q), .clr(RESET));
  and and_323 (and_323_out, demultiplexer_3_out10, demultiplexer_1_out2);
  Register register_164 (.D(DATA_IN), .en(and_324_out), .clk(CLK), .Q(register_164_q), .clr(RESET));
  and and_324 (and_324_out, demultiplexer_3_out10, demultiplexer_1_out3);
  Register register_165 (.D(DATA_IN), .en(and_325_out), .clk(CLK), .Q(register_165_q), .clr(RESET));
  and and_325 (and_325_out, demultiplexer_3_out10, demultiplexer_1_out4);
  Register register_166 (.D(DATA_IN), .en(and_326_out), .clk(CLK), .Q(register_166_q), .clr(RESET));
  and and_326 (and_326_out, demultiplexer_3_out10, demultiplexer_1_out5);
  Register register_167 (.D(DATA_IN), .en(and_327_out), .clk(CLK), .Q(register_167_q), .clr(RESET));
  and and_327 (and_327_out, demultiplexer_3_out10, demultiplexer_1_out6);
  Register register_168 (.D(DATA_IN), .en(and_328_out), .clk(CLK), .Q(register_168_q), .clr(RESET));
  and and_328 (and_328_out, demultiplexer_3_out10, demultiplexer_1_out7);
  Register register_169 (.D(DATA_IN), .en(and_329_out), .clk(CLK), .Q(register_169_q), .clr(RESET));
  and and_329 (and_329_out, demultiplexer_3_out10, demultiplexer_1_out8);
  Register register_170 (.D(DATA_IN), .en(and_330_out), .clk(CLK), .Q(register_170_q), .clr(RESET));
  and and_330 (and_330_out, demultiplexer_3_out10, demultiplexer_1_out9);
  Register register_171 (.D(DATA_IN), .en(and_331_out), .clk(CLK), .Q(register_171_q), .clr(RESET));
  and and_331 (and_331_out, demultiplexer_3_out10, demultiplexer_1_out10);
  Register register_172 (.D(DATA_IN), .en(and_332_out), .clk(CLK), .Q(register_172_q), .clr(RESET));
  and and_332 (and_332_out, demultiplexer_3_out10, demultiplexer_1_out11);
  Register register_173 (.D(DATA_IN), .en(and_333_out), .clk(CLK), .Q(register_173_q), .clr(RESET));
  and and_333 (and_333_out, demultiplexer_3_out10, demultiplexer_1_out12);
  Register register_174 (.D(DATA_IN), .en(and_334_out), .clk(CLK), .Q(register_174_q), .clr(RESET));
  and and_334 (and_334_out, demultiplexer_3_out10, demultiplexer_1_out13);
  Register register_175 (.D(DATA_IN), .en(and_335_out), .clk(CLK), .Q(register_175_q), .clr(RESET));
  and and_335 (and_335_out, demultiplexer_3_out10, demultiplexer_1_out14);
  Register register_176 (.D(DATA_IN), .en(and_336_out), .clk(CLK), .Q(register_176_q), .clr(RESET));
  and and_336 (and_336_out, demultiplexer_3_out10, demultiplexer_1_out15);
  and and_337 (and_337_out, demultiplexer_2_out0, demultiplexer_4_out10);
  assign DATA_OUT = and_337_out ? register_161_q : 8'bz;  // Controlled_Buffer controlled_buffer_161
  and and_338 (and_338_out, demultiplexer_2_out1, demultiplexer_4_out10);
  assign DATA_OUT = and_338_out ? register_162_q : 8'bz;  // Controlled_Buffer controlled_buffer_162
  and and_339 (and_339_out, demultiplexer_2_out2, demultiplexer_4_out10);
  assign DATA_OUT = and_339_out ? register_163_q : 8'bz;  // Controlled_Buffer controlled_buffer_163
  and and_340 (and_340_out, demultiplexer_2_out3, demultiplexer_4_out10);
  assign DATA_OUT = and_340_out ? register_164_q : 8'bz;  // Controlled_Buffer controlled_buffer_164
  and and_341 (and_341_out, demultiplexer_2_out4, demultiplexer_4_out10);
  assign DATA_OUT = and_341_out ? register_165_q : 8'bz;  // Controlled_Buffer controlled_buffer_165
  and and_342 (and_342_out, demultiplexer_2_out5, demultiplexer_4_out10);
  assign DATA_OUT = and_342_out ? register_166_q : 8'bz;  // Controlled_Buffer controlled_buffer_166
  and and_343 (and_343_out, demultiplexer_2_out6, demultiplexer_4_out10);
  assign DATA_OUT = and_343_out ? register_167_q : 8'bz;  // Controlled_Buffer controlled_buffer_167
  and and_344 (and_344_out, demultiplexer_2_out7, demultiplexer_4_out10);
  assign DATA_OUT = and_344_out ? register_168_q : 8'bz;  // Controlled_Buffer controlled_buffer_168
  and and_345 (and_345_out, demultiplexer_2_out8, demultiplexer_4_out10);
  assign DATA_OUT = and_345_out ? register_169_q : 8'bz;  // Controlled_Buffer controlled_buffer_169
  and and_346 (and_346_out, demultiplexer_2_out9, demultiplexer_4_out10);
  assign DATA_OUT = and_346_out ? register_170_q : 8'bz;  // Controlled_Buffer controlled_buffer_170
  and and_347 (and_347_out, demultiplexer_2_out10, demultiplexer_4_out10);
  assign DATA_OUT = and_347_out ? register_171_q : 8'bz;  // Controlled_Buffer controlled_buffer_171
  and and_348 (and_348_out, demultiplexer_2_out11, demultiplexer_4_out10);
  assign DATA_OUT = and_348_out ? register_172_q : 8'bz;  // Controlled_Buffer controlled_buffer_172
  and and_349 (and_349_out, demultiplexer_2_out12, demultiplexer_4_out10);
  assign DATA_OUT = and_349_out ? register_173_q : 8'bz;  // Controlled_Buffer controlled_buffer_173
  and and_350 (and_350_out, demultiplexer_2_out13, demultiplexer_4_out10);
  assign DATA_OUT = and_350_out ? register_174_q : 8'bz;  // Controlled_Buffer controlled_buffer_174
  and and_351 (and_351_out, demultiplexer_2_out14, demultiplexer_4_out10);
  assign DATA_OUT = and_351_out ? register_175_q : 8'bz;  // Controlled_Buffer controlled_buffer_175
  and and_352 (and_352_out, demultiplexer_2_out15, demultiplexer_4_out10);
  assign DATA_OUT = and_352_out ? register_176_q : 8'bz;  // Controlled_Buffer controlled_buffer_176
  and and_353 (and_353_out, demultiplexer_3_out11, demultiplexer_1_out0);
  and and_354 (and_354_out, demultiplexer_3_out11, demultiplexer_1_out1);
  and and_355 (and_355_out, demultiplexer_3_out11, demultiplexer_1_out2);
  and and_356 (and_356_out, demultiplexer_3_out11, demultiplexer_1_out3);
  and and_357 (and_357_out, demultiplexer_3_out11, demultiplexer_1_out4);
  and and_358 (and_358_out, demultiplexer_3_out11, demultiplexer_1_out5);
  and and_359 (and_359_out, demultiplexer_3_out11, demultiplexer_1_out6);
  and and_360 (and_360_out, demultiplexer_3_out11, demultiplexer_1_out7);
  and and_361 (and_361_out, demultiplexer_3_out11, demultiplexer_1_out8);
  and and_362 (and_362_out, demultiplexer_3_out11, demultiplexer_1_out9);
  and and_363 (and_363_out, demultiplexer_3_out11, demultiplexer_1_out10);
  and and_364 (and_364_out, demultiplexer_3_out11, demultiplexer_1_out11);
  and and_365 (and_365_out, demultiplexer_3_out11, demultiplexer_1_out12);
  and and_366 (and_366_out, demultiplexer_3_out11, demultiplexer_1_out13);
  and and_367 (and_367_out, demultiplexer_3_out11, demultiplexer_1_out14);
  and and_368 (and_368_out, demultiplexer_3_out11, demultiplexer_1_out15);
  Register register_177 (.D(DATA_IN), .en(and_353_out), .clk(CLK), .Q(register_177_q), .clr(RESET));
  Register register_178 (.D(DATA_IN), .en(and_354_out), .clk(CLK), .Q(register_178_q), .clr(RESET));
  Register register_179 (.D(DATA_IN), .en(and_355_out), .clk(CLK), .Q(register_179_q), .clr(RESET));
  Register register_180 (.D(DATA_IN), .en(and_356_out), .clk(CLK), .Q(register_180_q), .clr(RESET));
  Register register_181 (.D(DATA_IN), .en(and_357_out), .clk(CLK), .Q(register_181_q), .clr(RESET));
  Register register_182 (.D(DATA_IN), .en(and_358_out), .clk(CLK), .Q(register_182_q), .clr(RESET));
  Register register_183 (.D(DATA_IN), .en(and_359_out), .clk(CLK), .Q(register_183_q), .clr(RESET));
  Register register_184 (.D(DATA_IN), .en(and_360_out), .clk(CLK), .Q(register_184_q), .clr(RESET));
  Register register_185 (.D(DATA_IN), .en(and_361_out), .clk(CLK), .Q(register_185_q), .clr(RESET));
  Register register_186 (.D(DATA_IN), .en(and_362_out), .clk(CLK), .Q(register_186_q), .clr(RESET));
  Register register_187 (.D(DATA_IN), .en(and_363_out), .clk(CLK), .Q(register_187_q), .clr(RESET));
  Register register_188 (.D(DATA_IN), .en(and_364_out), .clk(CLK), .Q(register_188_q), .clr(RESET));
  Register register_189 (.D(DATA_IN), .en(and_365_out), .clk(CLK), .Q(register_189_q), .clr(RESET));
  Register register_190 (.D(DATA_IN), .en(and_366_out), .clk(CLK), .Q(register_190_q), .clr(RESET));
  Register register_191 (.D(DATA_IN), .en(and_367_out), .clk(CLK), .Q(register_191_q), .clr(RESET));
  Register register_192 (.D(DATA_IN), .en(and_368_out), .clk(CLK), .Q(register_192_q), .clr(RESET));
  and and_369 (and_369_out, demultiplexer_2_out0, demultiplexer_4_out11);
  assign DATA_OUT = and_369_out ? register_177_q : 8'bz;  // Controlled_Buffer controlled_buffer_177
  and and_370 (and_370_out, demultiplexer_2_out1, demultiplexer_4_out11);
  assign DATA_OUT = and_370_out ? register_178_q : 8'bz;  // Controlled_Buffer controlled_buffer_178
  and and_371 (and_371_out, demultiplexer_2_out2, demultiplexer_4_out11);
  assign DATA_OUT = and_371_out ? register_179_q : 8'bz;  // Controlled_Buffer controlled_buffer_179
  and and_372 (and_372_out, demultiplexer_2_out3, demultiplexer_4_out11);
  assign DATA_OUT = and_372_out ? register_180_q : 8'bz;  // Controlled_Buffer controlled_buffer_180
  and and_373 (and_373_out, demultiplexer_2_out4, demultiplexer_4_out11);
  assign DATA_OUT = and_373_out ? register_181_q : 8'bz;  // Controlled_Buffer controlled_buffer_181
  and and_374 (and_374_out, demultiplexer_2_out5, demultiplexer_4_out11);
  assign DATA_OUT = and_374_out ? register_182_q : 8'bz;  // Controlled_Buffer controlled_buffer_182
  and and_375 (and_375_out, demultiplexer_2_out6, demultiplexer_4_out11);
  assign DATA_OUT = and_375_out ? register_183_q : 8'bz;  // Controlled_Buffer controlled_buffer_183
  and and_376 (and_376_out, demultiplexer_2_out7, demultiplexer_4_out11);
  assign DATA_OUT = and_376_out ? register_184_q : 8'bz;  // Controlled_Buffer controlled_buffer_184
  and and_377 (and_377_out, demultiplexer_2_out8, demultiplexer_4_out11);
  assign DATA_OUT = and_377_out ? register_185_q : 8'bz;  // Controlled_Buffer controlled_buffer_185
  and and_378 (and_378_out, demultiplexer_2_out9, demultiplexer_4_out11);
  assign DATA_OUT = and_378_out ? register_186_q : 8'bz;  // Controlled_Buffer controlled_buffer_186
  and and_379 (and_379_out, demultiplexer_2_out10, demultiplexer_4_out11);
  assign DATA_OUT = and_379_out ? register_187_q : 8'bz;  // Controlled_Buffer controlled_buffer_187
  and and_380 (and_380_out, demultiplexer_2_out11, demultiplexer_4_out11);
  assign DATA_OUT = and_380_out ? register_188_q : 8'bz;  // Controlled_Buffer controlled_buffer_188
  and and_381 (and_381_out, demultiplexer_2_out12, demultiplexer_4_out11);
  assign DATA_OUT = and_381_out ? register_189_q : 8'bz;  // Controlled_Buffer controlled_buffer_189
  and and_382 (and_382_out, demultiplexer_2_out13, demultiplexer_4_out11);
  assign DATA_OUT = and_382_out ? register_190_q : 8'bz;  // Controlled_Buffer controlled_buffer_190
  and and_383 (and_383_out, demultiplexer_2_out14, demultiplexer_4_out11);
  assign DATA_OUT = and_383_out ? register_191_q : 8'bz;  // Controlled_Buffer controlled_buffer_191
  and and_384 (and_384_out, demultiplexer_2_out15, demultiplexer_4_out11);
  assign DATA_OUT = and_384_out ? register_192_q : 8'bz;  // Controlled_Buffer controlled_buffer_192
  Register register_193 (.D(DATA_IN), .en(and_385_out), .clk(CLK), .Q(register_193_q), .clr(RESET));
  and and_385 (and_385_out, demultiplexer_3_out12, demultiplexer_1_out0);
  Register register_194 (.D(DATA_IN), .en(and_386_out), .clk(CLK), .Q(register_194_q), .clr(RESET));
  and and_386 (and_386_out, demultiplexer_3_out12, demultiplexer_1_out1);
  Register register_195 (.D(DATA_IN), .en(and_387_out), .clk(CLK), .Q(register_195_q), .clr(RESET));
  and and_387 (and_387_out, demultiplexer_3_out12, demultiplexer_1_out2);
  Register register_196 (.D(DATA_IN), .en(and_388_out), .clk(CLK), .Q(register_196_q), .clr(RESET));
  and and_388 (and_388_out, demultiplexer_3_out12, demultiplexer_1_out3);
  Register register_197 (.D(DATA_IN), .en(and_389_out), .clk(CLK), .Q(register_197_q), .clr(RESET));
  and and_389 (and_389_out, demultiplexer_3_out12, demultiplexer_1_out4);
  Register register_198 (.D(DATA_IN), .en(and_390_out), .clk(CLK), .Q(register_198_q), .clr(RESET));
  and and_390 (and_390_out, demultiplexer_3_out12, demultiplexer_1_out5);
  Register register_199 (.D(DATA_IN), .en(and_391_out), .clk(CLK), .Q(register_199_q), .clr(RESET));
  and and_391 (and_391_out, demultiplexer_3_out12, demultiplexer_1_out6);
  Register register_200 (.D(DATA_IN), .en(and_392_out), .clk(CLK), .Q(register_200_q), .clr(RESET));
  and and_392 (and_392_out, demultiplexer_3_out12, demultiplexer_1_out7);
  Register register_201 (.D(DATA_IN), .en(and_393_out), .clk(CLK), .Q(register_201_q), .clr(RESET));
  and and_393 (and_393_out, demultiplexer_3_out12, demultiplexer_1_out8);
  Register register_202 (.D(DATA_IN), .en(and_394_out), .clk(CLK), .Q(register_202_q), .clr(RESET));
  and and_394 (and_394_out, demultiplexer_3_out12, demultiplexer_1_out9);
  Register register_203 (.D(DATA_IN), .en(and_395_out), .clk(CLK), .Q(register_203_q), .clr(RESET));
  and and_395 (and_395_out, demultiplexer_3_out12, demultiplexer_1_out10);
  Register register_204 (.D(DATA_IN), .en(and_396_out), .clk(CLK), .Q(register_204_q), .clr(RESET));
  and and_396 (and_396_out, demultiplexer_3_out12, demultiplexer_1_out11);
  Register register_205 (.D(DATA_IN), .en(and_397_out), .clk(CLK), .Q(register_205_q), .clr(RESET));
  and and_397 (and_397_out, demultiplexer_3_out12, demultiplexer_1_out12);
  Register register_206 (.D(DATA_IN), .en(and_398_out), .clk(CLK), .Q(register_206_q), .clr(RESET));
  and and_398 (and_398_out, demultiplexer_3_out12, demultiplexer_1_out13);
  Register register_207 (.D(DATA_IN), .en(and_399_out), .clk(CLK), .Q(register_207_q), .clr(RESET));
  and and_399 (and_399_out, demultiplexer_3_out12, demultiplexer_1_out14);
  Register register_208 (.D(DATA_IN), .en(and_400_out), .clk(CLK), .Q(register_208_q), .clr(RESET));
  and and_400 (and_400_out, demultiplexer_3_out12, demultiplexer_1_out15);
  and and_401 (and_401_out, demultiplexer_2_out0, demultiplexer_4_out12);
  assign DATA_OUT = and_401_out ? register_193_q : 8'bz;  // Controlled_Buffer controlled_buffer_193
  and and_402 (and_402_out, demultiplexer_2_out1, demultiplexer_4_out12);
  assign DATA_OUT = and_402_out ? register_194_q : 8'bz;  // Controlled_Buffer controlled_buffer_194
  and and_403 (and_403_out, demultiplexer_2_out2, demultiplexer_4_out12);
  assign DATA_OUT = and_403_out ? register_195_q : 8'bz;  // Controlled_Buffer controlled_buffer_195
  and and_404 (and_404_out, demultiplexer_2_out3, demultiplexer_4_out12);
  assign DATA_OUT = and_404_out ? register_196_q : 8'bz;  // Controlled_Buffer controlled_buffer_196
  and and_405 (and_405_out, demultiplexer_2_out4, demultiplexer_4_out12);
  assign DATA_OUT = and_405_out ? register_197_q : 8'bz;  // Controlled_Buffer controlled_buffer_197
  and and_406 (and_406_out, demultiplexer_2_out5, demultiplexer_4_out12);
  assign DATA_OUT = and_406_out ? register_198_q : 8'bz;  // Controlled_Buffer controlled_buffer_198
  and and_407 (and_407_out, demultiplexer_2_out6, demultiplexer_4_out12);
  assign DATA_OUT = and_407_out ? register_199_q : 8'bz;  // Controlled_Buffer controlled_buffer_199
  and and_408 (and_408_out, demultiplexer_2_out7, demultiplexer_4_out12);
  assign DATA_OUT = and_408_out ? register_200_q : 8'bz;  // Controlled_Buffer controlled_buffer_200
  and and_409 (and_409_out, demultiplexer_2_out8, demultiplexer_4_out12);
  assign DATA_OUT = and_409_out ? register_201_q : 8'bz;  // Controlled_Buffer controlled_buffer_201
  and and_410 (and_410_out, demultiplexer_2_out9, demultiplexer_4_out12);
  assign DATA_OUT = and_410_out ? register_202_q : 8'bz;  // Controlled_Buffer controlled_buffer_202
  and and_411 (and_411_out, demultiplexer_2_out10, demultiplexer_4_out12);
  assign DATA_OUT = and_411_out ? register_203_q : 8'bz;  // Controlled_Buffer controlled_buffer_203
  and and_412 (and_412_out, demultiplexer_2_out11, demultiplexer_4_out12);
  assign DATA_OUT = and_412_out ? register_204_q : 8'bz;  // Controlled_Buffer controlled_buffer_204
  and and_413 (and_413_out, demultiplexer_2_out12, demultiplexer_4_out12);
  assign DATA_OUT = and_413_out ? register_205_q : 8'bz;  // Controlled_Buffer controlled_buffer_205
  and and_414 (and_414_out, demultiplexer_2_out13, demultiplexer_4_out12);
  assign DATA_OUT = and_414_out ? register_206_q : 8'bz;  // Controlled_Buffer controlled_buffer_206
  and and_415 (and_415_out, demultiplexer_2_out14, demultiplexer_4_out12);
  assign DATA_OUT = and_415_out ? register_207_q : 8'bz;  // Controlled_Buffer controlled_buffer_207
  and and_416 (and_416_out, demultiplexer_2_out15, demultiplexer_4_out12);
  assign DATA_OUT = and_416_out ? register_208_q : 8'bz;  // Controlled_Buffer controlled_buffer_208
  Register register_209 (.D(DATA_IN), .en(and_417_out), .clk(CLK), .Q(register_209_q), .clr(RESET));
  and and_417 (and_417_out, demultiplexer_3_out13, demultiplexer_1_out0);
  Register register_210 (.D(DATA_IN), .en(and_418_out), .clk(CLK), .Q(register_210_q), .clr(RESET));
  and and_418 (and_418_out, demultiplexer_3_out13, demultiplexer_1_out1);
  Register register_211 (.D(DATA_IN), .en(and_419_out), .clk(CLK), .Q(register_211_q), .clr(RESET));
  and and_419 (and_419_out, demultiplexer_3_out13, demultiplexer_1_out2);
  Register register_212 (.D(DATA_IN), .en(and_420_out), .clk(CLK), .Q(register_212_q), .clr(RESET));
  and and_420 (and_420_out, demultiplexer_3_out13, demultiplexer_1_out3);
  Register register_213 (.D(DATA_IN), .en(and_421_out), .clk(CLK), .Q(register_213_q), .clr(RESET));
  and and_421 (and_421_out, demultiplexer_3_out13, demultiplexer_1_out4);
  Register register_214 (.D(DATA_IN), .en(and_422_out), .clk(CLK), .Q(register_214_q), .clr(RESET));
  and and_422 (and_422_out, demultiplexer_3_out13, demultiplexer_1_out5);
  Register register_215 (.D(DATA_IN), .en(and_423_out), .clk(CLK), .Q(register_215_q), .clr(RESET));
  and and_423 (and_423_out, demultiplexer_3_out13, demultiplexer_1_out6);
  Register register_216 (.D(DATA_IN), .en(and_424_out), .clk(CLK), .Q(register_216_q), .clr(RESET));
  and and_424 (and_424_out, demultiplexer_3_out13, demultiplexer_1_out7);
  Register register_217 (.D(DATA_IN), .en(and_425_out), .clk(CLK), .Q(register_217_q), .clr(RESET));
  and and_425 (and_425_out, demultiplexer_3_out13, demultiplexer_1_out8);
  Register register_218 (.D(DATA_IN), .en(and_426_out), .clk(CLK), .Q(register_218_q), .clr(RESET));
  and and_426 (and_426_out, demultiplexer_3_out13, demultiplexer_1_out9);
  Register register_219 (.D(DATA_IN), .en(and_427_out), .clk(CLK), .Q(register_219_q), .clr(RESET));
  and and_427 (and_427_out, demultiplexer_3_out13, demultiplexer_1_out10);
  Register register_220 (.D(DATA_IN), .en(and_428_out), .clk(CLK), .Q(register_220_q), .clr(RESET));
  and and_428 (and_428_out, demultiplexer_3_out13, demultiplexer_1_out11);
  Register register_221 (.D(DATA_IN), .en(and_429_out), .clk(CLK), .Q(register_221_q), .clr(RESET));
  and and_429 (and_429_out, demultiplexer_3_out13, demultiplexer_1_out12);
  Register register_222 (.D(DATA_IN), .en(and_430_out), .clk(CLK), .Q(register_222_q), .clr(RESET));
  and and_430 (and_430_out, demultiplexer_3_out13, demultiplexer_1_out13);
  Register register_223 (.D(DATA_IN), .en(and_431_out), .clk(CLK), .Q(register_223_q), .clr(RESET));
  and and_431 (and_431_out, demultiplexer_3_out13, demultiplexer_1_out14);
  Register register_224 (.D(DATA_IN), .en(and_432_out), .clk(CLK), .Q(register_224_q), .clr(RESET));
  and and_432 (and_432_out, demultiplexer_3_out13, demultiplexer_1_out15);
  and and_433 (and_433_out, demultiplexer_2_out0, demultiplexer_4_out13);
  assign DATA_OUT = and_433_out ? register_209_q : 8'bz;  // Controlled_Buffer controlled_buffer_209
  and and_434 (and_434_out, demultiplexer_2_out1, demultiplexer_4_out13);
  assign DATA_OUT = and_434_out ? register_210_q : 8'bz;  // Controlled_Buffer controlled_buffer_210
  and and_435 (and_435_out, demultiplexer_2_out2, demultiplexer_4_out13);
  assign DATA_OUT = and_435_out ? register_211_q : 8'bz;  // Controlled_Buffer controlled_buffer_211
  and and_436 (and_436_out, demultiplexer_2_out3, demultiplexer_4_out13);
  assign DATA_OUT = and_436_out ? register_212_q : 8'bz;  // Controlled_Buffer controlled_buffer_212
  and and_437 (and_437_out, demultiplexer_2_out4, demultiplexer_4_out13);
  assign DATA_OUT = and_437_out ? register_213_q : 8'bz;  // Controlled_Buffer controlled_buffer_213
  and and_438 (and_438_out, demultiplexer_2_out5, demultiplexer_4_out13);
  assign DATA_OUT = and_438_out ? register_214_q : 8'bz;  // Controlled_Buffer controlled_buffer_214
  and and_439 (and_439_out, demultiplexer_2_out6, demultiplexer_4_out13);
  assign DATA_OUT = and_439_out ? register_215_q : 8'bz;  // Controlled_Buffer controlled_buffer_215
  and and_440 (and_440_out, demultiplexer_2_out7, demultiplexer_4_out13);
  assign DATA_OUT = and_440_out ? register_216_q : 8'bz;  // Controlled_Buffer controlled_buffer_216
  and and_441 (and_441_out, demultiplexer_2_out8, demultiplexer_4_out13);
  assign DATA_OUT = and_441_out ? register_217_q : 8'bz;  // Controlled_Buffer controlled_buffer_217
  and and_442 (and_442_out, demultiplexer_2_out9, demultiplexer_4_out13);
  assign DATA_OUT = and_442_out ? register_218_q : 8'bz;  // Controlled_Buffer controlled_buffer_218
  and and_443 (and_443_out, demultiplexer_2_out10, demultiplexer_4_out13);
  assign DATA_OUT = and_443_out ? register_219_q : 8'bz;  // Controlled_Buffer controlled_buffer_219
  and and_444 (and_444_out, demultiplexer_2_out11, demultiplexer_4_out13);
  assign DATA_OUT = and_444_out ? register_220_q : 8'bz;  // Controlled_Buffer controlled_buffer_220
  and and_445 (and_445_out, demultiplexer_2_out12, demultiplexer_4_out13);
  assign DATA_OUT = and_445_out ? register_221_q : 8'bz;  // Controlled_Buffer controlled_buffer_221
  and and_446 (and_446_out, demultiplexer_2_out13, demultiplexer_4_out13);
  assign DATA_OUT = and_446_out ? register_222_q : 8'bz;  // Controlled_Buffer controlled_buffer_222
  and and_447 (and_447_out, demultiplexer_2_out14, demultiplexer_4_out13);
  assign DATA_OUT = and_447_out ? register_223_q : 8'bz;  // Controlled_Buffer controlled_buffer_223
  and and_448 (and_448_out, demultiplexer_2_out15, demultiplexer_4_out13);
  assign DATA_OUT = and_448_out ? register_224_q : 8'bz;  // Controlled_Buffer controlled_buffer_224
  and and_449 (and_449_out, demultiplexer_3_out14, demultiplexer_1_out0);
  and and_450 (and_450_out, demultiplexer_3_out14, demultiplexer_1_out1);
  and and_451 (and_451_out, demultiplexer_3_out14, demultiplexer_1_out2);
  and and_452 (and_452_out, demultiplexer_3_out14, demultiplexer_1_out3);
  and and_453 (and_453_out, demultiplexer_3_out14, demultiplexer_1_out4);
  and and_454 (and_454_out, demultiplexer_3_out14, demultiplexer_1_out5);
  and and_455 (and_455_out, demultiplexer_3_out14, demultiplexer_1_out6);
  and and_456 (and_456_out, demultiplexer_3_out14, demultiplexer_1_out7);
  and and_457 (and_457_out, demultiplexer_3_out14, demultiplexer_1_out8);
  and and_458 (and_458_out, demultiplexer_3_out14, demultiplexer_1_out9);
  and and_459 (and_459_out, demultiplexer_3_out14, demultiplexer_1_out10);
  and and_460 (and_460_out, demultiplexer_3_out14, demultiplexer_1_out11);
  and and_461 (and_461_out, demultiplexer_3_out14, demultiplexer_1_out12);
  and and_462 (and_462_out, demultiplexer_3_out14, demultiplexer_1_out13);
  and and_463 (and_463_out, demultiplexer_3_out14, demultiplexer_1_out14);
  and and_464 (and_464_out, demultiplexer_3_out14, demultiplexer_1_out15);
  Register register_225 (.D(DATA_IN), .en(and_449_out), .clk(CLK), .Q(register_225_q), .clr(RESET));
  Register register_226 (.D(DATA_IN), .en(and_450_out), .clk(CLK), .Q(register_226_q), .clr(RESET));
  Register register_227 (.D(DATA_IN), .en(and_451_out), .clk(CLK), .Q(register_227_q), .clr(RESET));
  Register register_228 (.D(DATA_IN), .en(and_452_out), .clk(CLK), .Q(register_228_q), .clr(RESET));
  Register register_229 (.D(DATA_IN), .en(and_453_out), .clk(CLK), .Q(register_229_q), .clr(RESET));
  Register register_230 (.D(DATA_IN), .en(and_454_out), .clk(CLK), .Q(register_230_q), .clr(RESET));
  Register register_231 (.D(DATA_IN), .en(and_455_out), .clk(CLK), .Q(register_231_q), .clr(RESET));
  Register register_232 (.D(DATA_IN), .en(and_456_out), .clk(CLK), .Q(register_232_q), .clr(RESET));
  Register register_233 (.D(DATA_IN), .en(and_457_out), .clk(CLK), .Q(register_233_q), .clr(RESET));
  Register register_234 (.D(DATA_IN), .en(and_458_out), .clk(CLK), .Q(register_234_q), .clr(RESET));
  Register register_235 (.D(DATA_IN), .en(and_459_out), .clk(CLK), .Q(register_235_q), .clr(RESET));
  Register register_236 (.D(DATA_IN), .en(and_460_out), .clk(CLK), .Q(register_236_q), .clr(RESET));
  Register register_237 (.D(DATA_IN), .en(and_461_out), .clk(CLK), .Q(register_237_q), .clr(RESET));
  Register register_238 (.D(DATA_IN), .en(and_462_out), .clk(CLK), .Q(register_238_q), .clr(RESET));
  Register register_239 (.D(DATA_IN), .en(and_463_out), .clk(CLK), .Q(register_239_q), .clr(RESET));
  Register register_240 (.D(DATA_IN), .en(and_464_out), .clk(CLK), .Q(register_240_q), .clr(RESET));
  and and_465 (and_465_out, demultiplexer_2_out0, demultiplexer_4_out14);
  assign DATA_OUT = and_465_out ? register_225_q : 8'bz;  // Controlled_Buffer controlled_buffer_225
  and and_466 (and_466_out, demultiplexer_2_out1, demultiplexer_4_out14);
  assign DATA_OUT = and_466_out ? register_226_q : 8'bz;  // Controlled_Buffer controlled_buffer_226
  and and_467 (and_467_out, demultiplexer_2_out2, demultiplexer_4_out14);
  assign DATA_OUT = and_467_out ? register_227_q : 8'bz;  // Controlled_Buffer controlled_buffer_227
  and and_468 (and_468_out, demultiplexer_2_out3, demultiplexer_4_out14);
  assign DATA_OUT = and_468_out ? register_228_q : 8'bz;  // Controlled_Buffer controlled_buffer_228
  and and_469 (and_469_out, demultiplexer_2_out4, demultiplexer_4_out14);
  assign DATA_OUT = and_469_out ? register_229_q : 8'bz;  // Controlled_Buffer controlled_buffer_229
  and and_470 (and_470_out, demultiplexer_2_out5, demultiplexer_4_out14);
  assign DATA_OUT = and_470_out ? register_230_q : 8'bz;  // Controlled_Buffer controlled_buffer_230
  and and_471 (and_471_out, demultiplexer_2_out6, demultiplexer_4_out14);
  assign DATA_OUT = and_471_out ? register_231_q : 8'bz;  // Controlled_Buffer controlled_buffer_231
  and and_472 (and_472_out, demultiplexer_2_out7, demultiplexer_4_out14);
  assign DATA_OUT = and_472_out ? register_232_q : 8'bz;  // Controlled_Buffer controlled_buffer_232
  and and_473 (and_473_out, demultiplexer_2_out8, demultiplexer_4_out14);
  assign DATA_OUT = and_473_out ? register_233_q : 8'bz;  // Controlled_Buffer controlled_buffer_233
  and and_474 (and_474_out, demultiplexer_2_out9, demultiplexer_4_out14);
  assign DATA_OUT = and_474_out ? register_234_q : 8'bz;  // Controlled_Buffer controlled_buffer_234
  and and_475 (and_475_out, demultiplexer_2_out10, demultiplexer_4_out14);
  assign DATA_OUT = and_475_out ? register_235_q : 8'bz;  // Controlled_Buffer controlled_buffer_235
  and and_476 (and_476_out, demultiplexer_2_out11, demultiplexer_4_out14);
  assign DATA_OUT = and_476_out ? register_236_q : 8'bz;  // Controlled_Buffer controlled_buffer_236
  and and_477 (and_477_out, demultiplexer_2_out12, demultiplexer_4_out14);
  assign DATA_OUT = and_477_out ? register_237_q : 8'bz;  // Controlled_Buffer controlled_buffer_237
  and and_478 (and_478_out, demultiplexer_2_out13, demultiplexer_4_out14);
  assign DATA_OUT = and_478_out ? register_238_q : 8'bz;  // Controlled_Buffer controlled_buffer_238
  and and_479 (and_479_out, demultiplexer_2_out14, demultiplexer_4_out14);
  assign DATA_OUT = and_479_out ? register_239_q : 8'bz;  // Controlled_Buffer controlled_buffer_239
  and and_480 (and_480_out, demultiplexer_2_out15, demultiplexer_4_out14);
  assign DATA_OUT = and_480_out ? register_240_q : 8'bz;  // Controlled_Buffer controlled_buffer_240
  Register register_241 (.D(DATA_IN), .en(and_481_out), .clk(CLK), .Q(register_241_q), .clr(RESET));
  and and_481 (and_481_out, demultiplexer_3_out15, demultiplexer_1_out0);
  Register register_242 (.D(DATA_IN), .en(and_482_out), .clk(CLK), .Q(register_242_q), .clr(RESET));
  and and_482 (and_482_out, demultiplexer_3_out15, demultiplexer_1_out1);
  Register register_243 (.D(DATA_IN), .en(and_483_out), .clk(CLK), .Q(register_243_q), .clr(RESET));
  and and_483 (and_483_out, demultiplexer_3_out15, demultiplexer_1_out2);
  Register register_244 (.D(DATA_IN), .en(and_484_out), .clk(CLK), .Q(register_244_q), .clr(RESET));
  and and_484 (and_484_out, demultiplexer_3_out15, demultiplexer_1_out3);
  Register register_245 (.D(DATA_IN), .en(and_485_out), .clk(CLK), .Q(register_245_q), .clr(RESET));
  and and_485 (and_485_out, demultiplexer_3_out15, demultiplexer_1_out4);
  Register register_246 (.D(DATA_IN), .en(and_486_out), .clk(CLK), .Q(register_246_q), .clr(RESET));
  and and_486 (and_486_out, demultiplexer_3_out15, demultiplexer_1_out5);
  Register register_247 (.D(DATA_IN), .en(and_487_out), .clk(CLK), .Q(register_247_q), .clr(RESET));
  and and_487 (and_487_out, demultiplexer_3_out15, demultiplexer_1_out6);
  Register register_248 (.D(DATA_IN), .en(and_488_out), .clk(CLK), .Q(register_248_q), .clr(RESET));
  and and_488 (and_488_out, demultiplexer_3_out15, demultiplexer_1_out7);
  Register register_249 (.D(DATA_IN), .en(and_489_out), .clk(CLK), .Q(register_249_q), .clr(RESET));
  and and_489 (and_489_out, demultiplexer_3_out15, demultiplexer_1_out8);
  Register register_250 (.D(DATA_IN), .en(and_490_out), .clk(CLK), .Q(register_250_q), .clr(RESET));
  and and_490 (and_490_out, demultiplexer_3_out15, demultiplexer_1_out9);
  Register register_251 (.D(DATA_IN), .en(and_491_out), .clk(CLK), .Q(register_251_q), .clr(RESET));
  and and_491 (and_491_out, demultiplexer_3_out15, demultiplexer_1_out10);
  Register register_252 (.D(DATA_IN), .en(and_492_out), .clk(CLK), .Q(register_252_q), .clr(RESET));
  and and_492 (and_492_out, demultiplexer_3_out15, demultiplexer_1_out11);
  Register register_253 (.D(DATA_IN), .en(and_493_out), .clk(CLK), .Q(register_253_q), .clr(RESET));
  and and_493 (and_493_out, demultiplexer_3_out15, demultiplexer_1_out12);
  Register register_254 (.D(DATA_IN), .en(and_494_out), .clk(CLK), .Q(register_254_q), .clr(RESET));
  and and_494 (and_494_out, demultiplexer_3_out15, demultiplexer_1_out13);
  Register register_255 (.D(DATA_IN), .en(and_495_out), .clk(CLK), .Q(register_255_q), .clr(RESET));
  and and_495 (and_495_out, demultiplexer_3_out15, demultiplexer_1_out14);
  Register register_256 (.D(DATA_IN), .en(and_496_out), .clk(CLK), .Q(register_256_q), .clr(RESET));
  and and_496 (and_496_out, demultiplexer_3_out15, demultiplexer_1_out15);
  and and_497 (and_497_out, demultiplexer_2_out0, demultiplexer_4_out15);
  assign DATA_OUT = and_497_out ? register_241_q : 8'bz;  // Controlled_Buffer controlled_buffer_241
  and and_498 (and_498_out, demultiplexer_2_out1, demultiplexer_4_out15);
  assign DATA_OUT = and_498_out ? register_242_q : 8'bz;  // Controlled_Buffer controlled_buffer_242
  and and_499 (and_499_out, demultiplexer_2_out2, demultiplexer_4_out15);
  assign DATA_OUT = and_499_out ? register_243_q : 8'bz;  // Controlled_Buffer controlled_buffer_243
  and and_500 (and_500_out, demultiplexer_2_out3, demultiplexer_4_out15);
  assign DATA_OUT = and_500_out ? register_244_q : 8'bz;  // Controlled_Buffer controlled_buffer_244
  and and_501 (and_501_out, demultiplexer_2_out4, demultiplexer_4_out15);
  assign DATA_OUT = and_501_out ? register_245_q : 8'bz;  // Controlled_Buffer controlled_buffer_245
  and and_502 (and_502_out, demultiplexer_2_out5, demultiplexer_4_out15);
  assign DATA_OUT = and_502_out ? register_246_q : 8'bz;  // Controlled_Buffer controlled_buffer_246
  and and_503 (and_503_out, demultiplexer_2_out6, demultiplexer_4_out15);
  assign DATA_OUT = and_503_out ? register_247_q : 8'bz;  // Controlled_Buffer controlled_buffer_247
  and and_504 (and_504_out, demultiplexer_2_out7, demultiplexer_4_out15);
  assign DATA_OUT = and_504_out ? register_248_q : 8'bz;  // Controlled_Buffer controlled_buffer_248
  and and_505 (and_505_out, demultiplexer_2_out8, demultiplexer_4_out15);
  assign DATA_OUT = and_505_out ? register_249_q : 8'bz;  // Controlled_Buffer controlled_buffer_249
  and and_506 (and_506_out, demultiplexer_2_out9, demultiplexer_4_out15);
  assign DATA_OUT = and_506_out ? register_250_q : 8'bz;  // Controlled_Buffer controlled_buffer_250
  and and_507 (and_507_out, demultiplexer_2_out10, demultiplexer_4_out15);
  assign DATA_OUT = and_507_out ? register_251_q : 8'bz;  // Controlled_Buffer controlled_buffer_251
  and and_508 (and_508_out, demultiplexer_2_out11, demultiplexer_4_out15);
  assign DATA_OUT = and_508_out ? register_252_q : 8'bz;  // Controlled_Buffer controlled_buffer_252
  and and_509 (and_509_out, demultiplexer_2_out12, demultiplexer_4_out15);
  assign DATA_OUT = and_509_out ? register_253_q : 8'bz;  // Controlled_Buffer controlled_buffer_253
  and and_510 (and_510_out, demultiplexer_2_out13, demultiplexer_4_out15);
  assign DATA_OUT = and_510_out ? register_254_q : 8'bz;  // Controlled_Buffer controlled_buffer_254
  and and_511 (and_511_out, demultiplexer_2_out14, demultiplexer_4_out15);
  assign DATA_OUT = and_511_out ? register_255_q : 8'bz;  // Controlled_Buffer controlled_buffer_255
  and and_512 (and_512_out, demultiplexer_2_out15, demultiplexer_4_out15);
  assign DATA_OUT = and_512_out ? register_256_q : 8'bz;  // Controlled_Buffer controlled_buffer_256
endmodule

module MEMORY_256B (
  input  RESET,
  input  CLK,
  input  [7:0] DATA_IN,
  input  WRITE,
  input  [7:0] WRITE_ADDRESS,
  input  [7:0] READ_ADDRESS,
  output [7:0] DATA_OUT
);

  wire demultiplexer_1_out0, demultiplexer_1_out1, demultiplexer_1_out2, demultiplexer_1_out3,
       demultiplexer_1_out4, demultiplexer_1_out5, demultiplexer_1_out6, demultiplexer_1_out7,
       demultiplexer_1_out8, demultiplexer_1_out9, demultiplexer_1_out10, demultiplexer_1_out11,
       demultiplexer_1_out12, demultiplexer_1_out13, demultiplexer_1_out14, demultiplexer_1_out15;
  wire [3:0] demultiplexer_2_out0, demultiplexer_2_out1, demultiplexer_2_out2, demultiplexer_2_out3,
       demultiplexer_2_out4, demultiplexer_2_out5, demultiplexer_2_out6, demultiplexer_2_out7,
       demultiplexer_2_out8, demultiplexer_2_out9, demultiplexer_2_out10, demultiplexer_2_out11,
       demultiplexer_2_out12, demultiplexer_2_out13, demultiplexer_2_out14, demultiplexer_2_out15,
       demultiplexer_3_out0, demultiplexer_3_out1, demultiplexer_3_out2, demultiplexer_3_out3,
       demultiplexer_3_out4, demultiplexer_3_out5, demultiplexer_3_out6, demultiplexer_3_out7,
       demultiplexer_3_out8, demultiplexer_3_out9, demultiplexer_3_out10, demultiplexer_3_out11,
       demultiplexer_3_out12, demultiplexer_3_out13, demultiplexer_3_out14, demultiplexer_3_out15;
  wire [7:0] MEMORY_16B_0_data_out, MEMORY_16B_1_data_out, MEMORY_16B_2_data_out, MEMORY_16B_3_data_out,
       MEMORY_16B_4_data_out, MEMORY_16B_5_data_out, MEMORY_16B_6_data_out, MEMORY_16B_7_data_out,
       MEMORY_16B_8_data_out, MEMORY_16B_9_data_out, MEMORY_16B_10_data_out, MEMORY_16B_11_data_out,
       MEMORY_16B_12_data_out, MEMORY_16B_13_data_out, MEMORY_16B_14_data_out, MEMORY_16B_15_data_out;

  Demultiplexer #(.select(4)) demultiplexer_1 (
    .out0(demultiplexer_1_out0), .out1(demultiplexer_1_out1), .out2(demultiplexer_1_out2),
    .out3(demultiplexer_1_out3), .out4(demultiplexer_1_out4), .out5(demultiplexer_1_out5),
    .out6(demultiplexer_1_out6), .out7(demultiplexer_1_out7), .out8(demultiplexer_1_out8),
    .out9(demultiplexer_1_out9), .out10(demultiplexer_1_out10), .out11(demultiplexer_1_out11),
    .out12(demultiplexer_1_out12), .out13(demultiplexer_1_out13), .out14(demultiplexer_1_out14),
    .out15(demultiplexer_1_out15), .in(WRITE), .sel(WRITE_ADDRESS[7:4]));
  Demultiplexer #(.select(4), .width(4)) demultiplexer_2 (
    .out0(demultiplexer_2_out0), .out1(demultiplexer_2_out1), .out2(demultiplexer_2_out2),
    .out3(demultiplexer_2_out3), .out4(demultiplexer_2_out4), .out5(demultiplexer_2_out5),
    .out6(demultiplexer_2_out6), .out7(demultiplexer_2_out7), .out8(demultiplexer_2_out8),
    .out9(demultiplexer_2_out9), .out10(demultiplexer_2_out10), .out11(demultiplexer_2_out11),
    .out12(demultiplexer_2_out12), .out13(demultiplexer_2_out13), .out14(demultiplexer_2_out14),
    .out15(demultiplexer_2_out15), .in(WRITE_ADDRESS[3:0]), .sel(WRITE_ADDRESS[7:4]));
  MEMORY_16B MEMORY_16B_15 (
    .RESET(RESET), .READ_ADDRESS(demultiplexer_3_out15), .WRITE(demultiplexer_1_out15), .DATA_IN(DATA_IN),
    .WRITE_ADDRESS(demultiplexer_2_out15), .CLK(CLK), .DATA_OUT(MEMORY_16B_15_data_out));
  MEMORY_16B MEMORY_16B_14 (
    .RESET(RESET), .READ_ADDRESS(demultiplexer_3_out14), .WRITE(demultiplexer_1_out14), .DATA_IN(DATA_IN),
    .WRITE_ADDRESS(demultiplexer_2_out14), .CLK(CLK), .DATA_OUT(MEMORY_16B_14_data_out));
  MEMORY_16B MEMORY_16B_13 (
    .RESET(RESET), .READ_ADDRESS(demultiplexer_3_out13), .WRITE(demultiplexer_1_out13), .DATA_IN(DATA_IN),
    .WRITE_ADDRESS(demultiplexer_2_out13), .CLK(CLK), .DATA_OUT(MEMORY_16B_13_data_out));
  MEMORY_16B MEMORY_16B_12 (
    .RESET(RESET), .READ_ADDRESS(demultiplexer_3_out12), .WRITE(demultiplexer_1_out12), .DATA_IN(DATA_IN),
    .WRITE_ADDRESS(demultiplexer_2_out12), .CLK(CLK), .DATA_OUT(MEMORY_16B_12_data_out));
  MEMORY_16B MEMORY_16B_11 (
    .RESET(RESET), .READ_ADDRESS(demultiplexer_3_out11), .WRITE(demultiplexer_1_out11), .DATA_IN(DATA_IN),
    .WRITE_ADDRESS(demultiplexer_2_out11), .CLK(CLK), .DATA_OUT(MEMORY_16B_11_data_out));
  MEMORY_16B MEMORY_16B_10 (
    .RESET(RESET), .READ_ADDRESS(demultiplexer_3_out10), .WRITE(demultiplexer_1_out10), .DATA_IN(DATA_IN),
    .WRITE_ADDRESS(demultiplexer_2_out10), .CLK(CLK), .DATA_OUT(MEMORY_16B_10_data_out));
  MEMORY_16B MEMORY_16B_9 (
    .RESET(RESET), .READ_ADDRESS(demultiplexer_3_out9), .WRITE(demultiplexer_1_out9), .DATA_IN(DATA_IN),
    .WRITE_ADDRESS(demultiplexer_2_out9), .CLK(CLK), .DATA_OUT(MEMORY_16B_9_data_out));
  MEMORY_16B MEMORY_16B_8 (
    .RESET(RESET), .READ_ADDRESS(demultiplexer_3_out8), .WRITE(demultiplexer_1_out8), .DATA_IN(DATA_IN),
    .WRITE_ADDRESS(demultiplexer_2_out8), .CLK(CLK), .DATA_OUT(MEMORY_16B_8_data_out));
  MEMORY_16B MEMORY_16B_7 (
    .RESET(RESET), .READ_ADDRESS(demultiplexer_3_out7), .WRITE(demultiplexer_1_out7), .DATA_IN(DATA_IN),
    .WRITE_ADDRESS(demultiplexer_2_out7), .CLK(CLK), .DATA_OUT(MEMORY_16B_7_data_out));
  MEMORY_16B MEMORY_16B_6 (
    .RESET(RESET), .READ_ADDRESS(demultiplexer_3_out6), .WRITE(demultiplexer_1_out6), .DATA_IN(DATA_IN),
    .WRITE_ADDRESS(demultiplexer_2_out6), .CLK(CLK), .DATA_OUT(MEMORY_16B_6_data_out));
  MEMORY_16B MEMORY_16B_5 (
    .RESET(RESET), .READ_ADDRESS(demultiplexer_3_out5), .WRITE(demultiplexer_1_out5), .DATA_IN(DATA_IN),
    .WRITE_ADDRESS(demultiplexer_2_out5), .CLK(CLK), .DATA_OUT(MEMORY_16B_5_data_out));
  MEMORY_16B MEMORY_16B_4 (
    .RESET(RESET), .READ_ADDRESS(demultiplexer_3_out4), .WRITE(demultiplexer_1_out4), .DATA_IN(DATA_IN),
    .WRITE_ADDRESS(demultiplexer_2_out4), .CLK(CLK), .DATA_OUT(MEMORY_16B_4_data_out));
  MEMORY_16B MEMORY_16B_3 (
    .RESET(RESET), .READ_ADDRESS(demultiplexer_3_out3), .WRITE(demultiplexer_1_out3), .DATA_IN(DATA_IN),
    .WRITE_ADDRESS(demultiplexer_2_out3), .CLK(CLK), .DATA_OUT(MEMORY_16B_3_data_out));
  MEMORY_16B MEMORY_16B_2 (
    .RESET(RESET), .READ_ADDRESS(demultiplexer_3_out2), .WRITE(demultiplexer_1_out2), .DATA_IN(DATA_IN),
    .WRITE_ADDRESS(demultiplexer_2_out2), .CLK(CLK), .DATA_OUT(MEMORY_16B_2_data_out));
  MEMORY_16B MEMORY_16B_1 (
    .RESET(RESET), .READ_ADDRESS(demultiplexer_3_out1), .WRITE(demultiplexer_1_out1), .DATA_IN(DATA_IN),
    .WRITE_ADDRESS(demultiplexer_2_out1), .CLK(CLK), .DATA_OUT(MEMORY_16B_1_data_out));
  MEMORY_16B MEMORY_16B_0 (
    .RESET(RESET), .READ_ADDRESS(demultiplexer_3_out0), .WRITE(demultiplexer_1_out0), .DATA_IN(DATA_IN),
    .WRITE_ADDRESS(demultiplexer_2_out0), .CLK(CLK), .DATA_OUT(MEMORY_16B_0_data_out));
  Multiplexer #(.select(4), .width(8)) multiplexer_1 (
    .in0(MEMORY_16B_0_data_out), .in1(MEMORY_16B_1_data_out), .in2(MEMORY_16B_2_data_out),
    .in3(MEMORY_16B_3_data_out), .in4(MEMORY_16B_4_data_out), .in5(MEMORY_16B_5_data_out),
    .in6(MEMORY_16B_6_data_out), .in7(MEMORY_16B_7_data_out), .in8(MEMORY_16B_8_data_out),
    .in9(MEMORY_16B_9_data_out), .in10(MEMORY_16B_10_data_out), .in11(MEMORY_16B_11_data_out),
    .in12(MEMORY_16B_12_data_out), .in13(MEMORY_16B_13_data_out), .in14(MEMORY_16B_14_data_out),
    .in15(MEMORY_16B_15_data_out), .out(DATA_OUT), .sel(READ_ADDRESS[7:4]));
  Demultiplexer #(.select(4), .width(4)) demultiplexer_3 (
    .out0(demultiplexer_3_out0), .out1(demultiplexer_3_out1), .out2(demultiplexer_3_out2),
    .out3(demultiplexer_3_out3), .out4(demultiplexer_3_out4), .out5(demultiplexer_3_out5),
    .out6(demultiplexer_3_out6), .out7(demultiplexer_3_out7), .out8(demultiplexer_3_out8),
    .out9(demultiplexer_3_out9), .out10(demultiplexer_3_out10), .out11(demultiplexer_3_out11),
    .out12(demultiplexer_3_out12), .out13(demultiplexer_3_out13), .out14(demultiplexer_3_out14),
    .out15(demultiplexer_3_out15), .in(READ_ADDRESS[3:0]), .sel(READ_ADDRESS[7:4]));
endmodule

module MEMORY_16B (
  input  CLK,
  input  RESET,
  input  [7:0] DATA_IN,
  input  WRITE,
  input  [3:0] WRITE_ADDRESS,
  input  [3:0] READ_ADDRESS,
  output [7:0] DATA_OUT
);

  wire demultiplexer_1_out0, demultiplexer_1_out1, demultiplexer_1_out2, demultiplexer_1_out3,
       demultiplexer_1_out4, demultiplexer_1_out5, demultiplexer_1_out6, demultiplexer_1_out7,
       demultiplexer_1_out8, demultiplexer_1_out9, demultiplexer_1_out10, demultiplexer_1_out11,
       demultiplexer_1_out12, demultiplexer_1_out13, demultiplexer_1_out14, demultiplexer_1_out15;
  wire [7:0] register_1_q, register_2_q, register_3_q, register_4_q, register_5_q, register_6_q,
       register_7_q, register_8_q, register_9_q, register_10_q, register_11_q, register_12_q, register_13_q,
       register_14_q, register_15_q, register_16_q;

  Demultiplexer #(.select(4)) demultiplexer_1 (
    .out0(demultiplexer_1_out0), .out1(demultiplexer_1_out1), .out2(demultiplexer_1_out2),
    .out3(demultiplexer_1_out3), .out4(demultiplexer_1_out4), .out5(demultiplexer_1_out5),
    .out6(demultiplexer_1_out6), .out7(demultiplexer_1_out7), .out8(demultiplexer_1_out8),
    .out9(demultiplexer_1_out9), .out10(demultiplexer_1_out10), .out11(demultiplexer_1_out11),
    .out12(demultiplexer_1_out12), .out13(demultiplexer_1_out13), .out14(demultiplexer_1_out14),
    .out15(demultiplexer_1_out15), .in(WRITE), .sel(WRITE_ADDRESS));
  Register register_1 (.D(DATA_IN), .en(demultiplexer_1_out0), .clk(CLK), .Q(register_1_q), .clr(RESET));
  Register register_2 (.D(DATA_IN), .en(demultiplexer_1_out1), .clk(CLK), .Q(register_2_q), .clr(RESET));
  Register register_3 (.D(DATA_IN), .en(demultiplexer_1_out2), .clk(CLK), .Q(register_3_q), .clr(RESET));
  Register register_4 (.D(DATA_IN), .en(demultiplexer_1_out3), .clk(CLK), .Q(register_4_q), .clr(RESET));
  Register register_5 (.D(DATA_IN), .en(demultiplexer_1_out4), .clk(CLK), .Q(register_5_q), .clr(RESET));
  Register register_6 (.D(DATA_IN), .en(demultiplexer_1_out5), .clk(CLK), .Q(register_6_q), .clr(RESET));
  Register register_7 (.D(DATA_IN), .en(demultiplexer_1_out6), .clk(CLK), .Q(register_7_q), .clr(RESET));
  Register register_8 (.D(DATA_IN), .en(demultiplexer_1_out7), .clk(CLK), .Q(register_8_q), .clr(RESET));
  Register register_9 (.D(DATA_IN), .en(demultiplexer_1_out8), .clk(CLK), .Q(register_9_q), .clr(RESET));
  Register register_10 (.D(DATA_IN), .en(demultiplexer_1_out9), .clk(CLK), .Q(register_10_q), .clr(RESET));
  Register register_11 (.D(DATA_IN), .en(demultiplexer_1_out10), .clk(CLK), .Q(register_11_q), .clr(RESET));
  Register register_12 (.D(DATA_IN), .en(demultiplexer_1_out11), .clk(CLK), .Q(register_12_q), .clr(RESET));
  Register register_13 (.D(DATA_IN), .en(demultiplexer_1_out12), .clk(CLK), .Q(register_13_q), .clr(RESET));
  Register register_14 (.D(DATA_IN), .en(demultiplexer_1_out13), .clk(CLK), .Q(register_14_q), .clr(RESET));
  Register register_15 (.D(DATA_IN), .en(demultiplexer_1_out14), .clk(CLK), .Q(register_15_q), .clr(RESET));
  Register register_16 (.D(DATA_IN), .en(demultiplexer_1_out15), .clk(CLK), .Q(register_16_q), .clr(RESET));
  Multiplexer #(.select(4), .width(8)) multiplexer_1 (
    .in0(register_1_q), .in1(register_2_q), .in2(register_3_q), .in3(register_4_q), .in4(register_5_q),
    .in5(register_6_q), .in6(register_7_q), .in7(register_8_q), .in8(register_9_q), .in9(register_10_q),
    .in10(register_11_q), .in11(register_12_q), .in12(register_13_q), .in13(register_14_q),
    .in14(register_15_q), .in15(register_16_q), .out(DATA_OUT), .sel(READ_ADDRESS));
endmodule

module MEMORY_16B_2S (
  input  CLK,
  input  RESET,
  input  [3:0] READ_ADDRESS_2,
  input  [7:0] DATA_IN,
  input  WRITE,
  input  [3:0] WRITE_ADDRESS,
  input  [3:0] READ_ADDRESS_1,
  output [7:0] DATA_OUT_2,
  output [7:0] DATA_OUT_1
);

  wire demultiplexer_1_out0, demultiplexer_1_out1, demultiplexer_1_out2, demultiplexer_1_out3,
       demultiplexer_1_out4, demultiplexer_1_out5, demultiplexer_1_out6, demultiplexer_1_out7,
       demultiplexer_1_out8, demultiplexer_1_out9, demultiplexer_1_out10, demultiplexer_1_out11,
       demultiplexer_1_out12, demultiplexer_1_out13, demultiplexer_1_out14, demultiplexer_1_out15;
  wire [7:0] register_1_q, register_2_q, register_3_q, register_4_q, register_5_q, register_6_q,
       register_7_q, register_8_q, register_9_q, register_10_q, register_11_q, register_12_q, register_13_q,
       register_14_q, register_15_q, register_16_q;

  Demultiplexer #(.select(4)) demultiplexer_1 (
    .out0(demultiplexer_1_out0), .out1(demultiplexer_1_out1), .out2(demultiplexer_1_out2),
    .out3(demultiplexer_1_out3), .out4(demultiplexer_1_out4), .out5(demultiplexer_1_out5),
    .out6(demultiplexer_1_out6), .out7(demultiplexer_1_out7), .out8(demultiplexer_1_out8),
    .out9(demultiplexer_1_out9), .out10(demultiplexer_1_out10), .out11(demultiplexer_1_out11),
    .out12(demultiplexer_1_out12), .out13(demultiplexer_1_out13), .out14(demultiplexer_1_out14),
    .out15(demultiplexer_1_out15), .in(WRITE), .sel(WRITE_ADDRESS));
  Register register_1 (.D(DATA_IN), .en(demultiplexer_1_out0), .clk(CLK), .Q(register_1_q), .clr(RESET));
  Register register_2 (.D(DATA_IN), .en(demultiplexer_1_out1), .clk(CLK), .Q(register_2_q), .clr(RESET));
  Register register_3 (.D(DATA_IN), .en(demultiplexer_1_out2), .clk(CLK), .Q(register_3_q), .clr(RESET));
  Register register_4 (.D(DATA_IN), .en(demultiplexer_1_out3), .clk(CLK), .Q(register_4_q), .clr(RESET));
  Register register_5 (.D(DATA_IN), .en(demultiplexer_1_out4), .clk(CLK), .Q(register_5_q), .clr(RESET));
  Register register_6 (.D(DATA_IN), .en(demultiplexer_1_out5), .clk(CLK), .Q(register_6_q), .clr(RESET));
  Register register_7 (.D(DATA_IN), .en(demultiplexer_1_out6), .clk(CLK), .Q(register_7_q), .clr(RESET));
  Register register_8 (.D(DATA_IN), .en(demultiplexer_1_out7), .clk(CLK), .Q(register_8_q), .clr(RESET));
  Register register_9 (.D(DATA_IN), .en(demultiplexer_1_out8), .clk(CLK), .Q(register_9_q), .clr(RESET));
  Register register_10 (.D(DATA_IN), .en(demultiplexer_1_out9), .clk(CLK), .Q(register_10_q), .clr(RESET));
  Register register_11 (.D(DATA_IN), .en(demultiplexer_1_out10), .clk(CLK), .Q(register_11_q), .clr(RESET));
  Register register_12 (.D(DATA_IN), .en(demultiplexer_1_out11), .clk(CLK), .Q(register_12_q), .clr(RESET));
  Register register_13 (.D(DATA_IN), .en(demultiplexer_1_out12), .clk(CLK), .Q(register_13_q), .clr(RESET));
  Register register_14 (.D(DATA_IN), .en(demultiplexer_1_out13), .clk(CLK), .Q(register_14_q), .clr(RESET));
  Register register_15 (.D(DATA_IN), .en(demultiplexer_1_out14), .clk(CLK), .Q(register_15_q), .clr(RESET));
  Register register_16 (.D(DATA_IN), .en(demultiplexer_1_out15), .clk(CLK), .Q(register_16_q), .clr(RESET));
  Multiplexer #(.select(4), .width(8)) multiplexer_1 (
    .in0(register_1_q), .in1(register_2_q), .in2(register_3_q), .in3(register_4_q), .in4(register_5_q),
    .in5(register_6_q), .in6(register_7_q), .in7(register_8_q), .in8(register_9_q), .in9(register_10_q),
    .in10(register_11_q), .in11(register_12_q), .in12(register_13_q), .in13(register_14_q),
    .in14(register_15_q), .in15(register_16_q), .out(DATA_OUT_2), .sel(READ_ADDRESS_2));
  Multiplexer #(.select(4), .width(8)) multiplexer_2 (
    .in0(register_1_q), .in1(register_2_q), .in2(register_3_q), .in3(register_4_q), .in4(register_5_q),
    .in5(register_6_q), .in6(register_7_q), .in7(register_8_q), .in8(register_9_q), .in9(register_10_q),
    .in10(register_11_q), .in11(register_12_q), .in12(register_13_q), .in13(register_14_q),
    .in14(register_15_q), .in15(register_16_q), .out(DATA_OUT_1), .sel(READ_ADDRESS_1));
endmodule

module EXPERIMENTAL_PC (
  input  INCREMENT,
  input  RESET,
  input  OVERWRITE,
  input  [7:0] OVERWRITE_VALUE
);

  wire CLK_out, or_1_out, or_2_out, or_3_out, or_4_out, or_5_out, or_6_out, or_7_out, or_8_out, or_9_out,
       or_10_out, or_11_out, or_12_out, or_13_out, or_14_out, or_15_out, or_16_out;
  wire [7:0] j_k_ff_1_q;

  Clock CLK (.out(CLK_out));
  or or_1 (or_1_out, INCREMENT, OVERWRITE_VALUE[0]);
  J_K_Flip_Flop #(.trigger("falling")) j_k_ff_1 (
    .J(or_1_out), .K(or_1_out), .clk(or_2_out), .Q(j_k_ff_1_q[0]), .reset(RESET));  // open: Qn, preset
  or or_2 (or_2_out, CLK_out, OVERWRITE);
  or or_3 (or_3_out, INCREMENT, OVERWRITE_VALUE[1]);
  J_K_Flip_Flop #(.trigger("falling")) j_k_ff_2 (
    .J(or_3_out), .K(or_3_out), .clk(or_4_out), .Q(j_k_ff_1_q[1]), .reset(RESET));  // open: Qn, preset
  or or_4 (or_4_out, j_k_ff_1_q[0], OVERWRITE);
  or or_5 (or_5_out, INCREMENT, OVERWRITE_VALUE[2]);
  J_K_Flip_Flop #(.trigger("falling")) j_k_ff_3 (
    .J(or_5_out), .K(or_5_out), .clk(or_6_out), .Q(j_k_ff_1_q[2]), .reset(RESET));  // open: Qn, preset
  or or_6 (or_6_out, j_k_ff_1_q[1], OVERWRITE);
  or or_7 (or_7_out, INCREMENT, OVERWRITE_VALUE[3]);
  J_K_Flip_Flop #(.trigger("falling")) j_k_ff_4 (
    .J(or_7_out), .K(or_7_out), .clk(or_8_out), .Q(j_k_ff_1_q[3]), .reset(RESET));  // open: Qn, preset
  or or_8 (or_8_out, j_k_ff_1_q[2], OVERWRITE);
  or or_9 (or_9_out, INCREMENT, OVERWRITE_VALUE[4]);
  J_K_Flip_Flop #(.trigger("falling")) j_k_ff_5 (
    .J(or_9_out), .K(or_9_out), .clk(or_10_out), .Q(j_k_ff_1_q[4]), .reset(RESET));  // open: Qn, preset
  or or_10 (or_10_out, j_k_ff_1_q[3], OVERWRITE);
  or or_11 (or_11_out, INCREMENT, OVERWRITE_VALUE[5]);
  J_K_Flip_Flop #(.trigger("falling")) j_k_ff_6 (
    .J(or_11_out), .K(or_11_out), .clk(or_12_out), .Q(j_k_ff_1_q[5]), .reset(RESET));  // open: Qn, preset
  or or_12 (or_12_out, j_k_ff_1_q[4], OVERWRITE);
  or or_13 (or_13_out, INCREMENT, OVERWRITE_VALUE[6]);
  J_K_Flip_Flop #(.trigger("falling")) j_k_ff_7 (
    .J(or_13_out), .K(or_13_out), .clk(or_14_out), .Q(j_k_ff_1_q[6]), .reset(RESET));  // open: Qn, preset
  or or_14 (or_14_out, j_k_ff_1_q[5], OVERWRITE);
  or or_15 (or_15_out, INCREMENT, OVERWRITE_VALUE[7]);
  J_K_Flip_Flop #(.trigger("falling")) j_k_ff_8 (
    .J(or_15_out), .K(or_15_out), .clk(or_16_out), .Q(j_k_ff_1_q[7]), .reset(RESET));  // open: Qn, preset
  or or_16 (or_16_out, j_k_ff_1_q[6], OVERWRITE);
  Hex_Digit_Display #(.decimalPoint("false")) hex_digit_display_1 (.value(j_k_ff_1_q[7:4]));
  Hex_Digit_Display #(.decimalPoint("false")) hex_digit_display_2 (.value(j_k_ff_1_q[3:0]));
endmodule

module TCAdder (
  input  [7:0] A,
  input  [7:0] B,
  input  C,
  output [7:0] O,
  output S
);

  wire and_1_out, and_2_out, and_3_out, and_4_out, and_5_out, and_6_out, and_7_out, and_8_out, and_9_out,
       and_10_out, and_11_out, and_12_out, and_13_out, and_14_out, and_15_out, and_16_out, xor_1_out,
       xor_3_out, xor_4_out, xor_6_out, xor_7_out, xor_9_out, xor_10_out, xor_12_out, xor_13_out, xor_15_out,
       xor_16_out, xor_18_out, xor_19_out, xor_21_out, xor_22_out;

  and and_1 (and_1_out, A[0], B[0]);
  xor xor_1 (xor_1_out, A[0], B[0]);
  and and_2 (and_2_out, C, xor_1_out);
  xor xor_2 (O[0], xor_1_out, C);
  xor xor_3 (xor_3_out, and_2_out, and_1_out);
  and and_3 (and_3_out, A[1], B[1]);
  xor xor_4 (xor_4_out, A[1], B[1]);
  and and_4 (and_4_out, xor_3_out, xor_4_out);
  xor xor_5 (O[1], xor_4_out, xor_3_out);
  xor xor_6 (xor_6_out, and_4_out, and_3_out);
  and and_5 (and_5_out, A[2], B[2]);
  xor xor_7 (xor_7_out, A[2], B[2]);
  and and_6 (and_6_out, xor_6_out, xor_7_out);
  xor xor_8 (O[2], xor_7_out, xor_6_out);
  xor xor_9 (xor_9_out, and_6_out, and_5_out);
  and and_7 (and_7_out, A[3], B[3]);
  xor xor_10 (xor_10_out, A[3], B[3]);
  and and_8 (and_8_out, xor_9_out, xor_10_out);
  xor xor_11 (O[3], xor_10_out, xor_9_out);
  xor xor_12 (xor_12_out, and_8_out, and_7_out);
  and and_9 (and_9_out, A[4], B[4]);
  xor xor_13 (xor_13_out, A[4], B[4]);
  and and_10 (and_10_out, xor_12_out, xor_13_out);
  xor xor_14 (O[4], xor_13_out, xor_12_out);
  xor xor_15 (xor_15_out, and_10_out, and_9_out);
  and and_11 (and_11_out, A[5], B[5]);
  xor xor_16 (xor_16_out, A[5], B[5]);
  and and_12 (and_12_out, xor_15_out, xor_16_out);
  xor xor_17 (O[5], xor_16_out, xor_15_out);
  xor xor_18 (xor_18_out, and_12_out, and_11_out);
  and and_13 (and_13_out, A[6], B[6]);
  xor xor_19 (xor_19_out, A[6], B[6]);
  and and_14 (and_14_out, xor_18_out, xor_19_out);
  xor xor_20 (O[6], xor_19_out, xor_18_out);
  xor xor_21 (xor_21_out, and_14_out, and_13_out);
  and and_15 (and_15_out, A[7], B[7]);
  xor xor_22 (xor_22_out, A[7], B[7]);
  and and_16 (and_16_out, xor_21_out, xor_22_out);
  xor xor_23 (O[7], xor_22_out, xor_21_out);
  xor xor_24 (S, and_16_out, and_15_out);
endmodule

module FP_Adder (
  input  [7:0] A,
  input  [7:0] B,
  output [7:0] O
);

  wire fp_adder_block_1_co, fp_adder_block_1_so, fp_pre_adder_block_1_c, fp_pre_adder_block_1_sa,
       fp_pre_adder_block_1_sb;
  wire [3:0] fp_adder_block_1_s, fp_pre_adder_block_1_exp, fp_pre_adder_block_1_m_a, fp_pre_adder_block_1_m_b;

  FP_PRE_ADDER_BLOCK fp_pre_adder_block_1 (
    .A(A), .B(B), .SA(fp_pre_adder_block_1_sa), .SB(fp_pre_adder_block_1_sb), .C(fp_pre_adder_block_1_c),
    .Exp(fp_pre_adder_block_1_exp), .M_A(fp_pre_adder_block_1_m_a), .M_B(fp_pre_adder_block_1_m_b));
  FP_ADDER_BLOCK fp_adder_block_1 (
    .A_S(1'b0), .B(fp_pre_adder_block_1_m_b), .A(fp_pre_adder_block_1_m_a), .SB(fp_pre_adder_block_1_sb),
    .SA(fp_pre_adder_block_1_sa), .Comp(fp_pre_adder_block_1_c), .CO(fp_adder_block_1_co),
    .S(fp_adder_block_1_s), .SO(fp_adder_block_1_so));
  FP_STANDARDISING_BLOCK fp_standardising_block_1 (
    .S(fp_adder_block_1_so), .Co(fp_adder_block_1_co), .ES(fp_pre_adder_block_1_exp),
    .MS(fp_adder_block_1_s), .RESULT(O));
endmodule

module EXP_DIF (
  input  [3:0] B,
  input  [3:0] A,
  output S_DIFF,
  output [3:0] L_EXP,
  output [3:0] DIFF
);

  wire and_1_out, and_2_out, and_3_out, and_4_out, and_5_out, and_6_out, and_7_out, and_8_out,
       controlled_buffer_3_out, controlled_buffer_7_out, controlled_buffer_8_out, controlled_buffer_9_out,
       controlled_buffer_11_out, controlled_buffer_13_out, controlled_buffer_14_out,
       controlled_buffer_16_out, controlled_buffer_17_out, controlled_buffer_18_out,
       controlled_buffer_21_out, controlled_buffer_23_out, FullAdder_2_r, FullAdder_3_r, FullAdder_4_r,
       FullAdder_6_r, FullAdder_7_r, FullAdder_8_r, not_1_out, not_2_out, not_3_out, not_4_out, not_5_out,
       not_6_out, not_7_out, not_8_out, not_9_out, not_10_out, not_11_out, not_12_out, not_13_out,
       not_14_out, not_15_out, not_16_out, not_17_out, xnor_1_out, xnor_2_out, xnor_3_out, xnor_4_out;
  wire [3:0] FullAdder_4_o, FullAdder_8_o;
  wire [4:4] FullAdder_1_r;

  not not_1 (not_1_out, FullAdder_4_o[3]);
  FullAdder FullAdder_5 (.A(1'b0), .B(not_1_out), .C(FullAdder_6_r), .O(FullAdder_8_o[3]));  // open: R
  not not_2 (not_2_out, FullAdder_1_r[4]);
  assign DIFF = not_2_out ? FullAdder_8_o : 4'bz;  // Controlled_Buffer controlled_buffer_1
  assign DIFF = FullAdder_1_r[4] ? FullAdder_4_o : 4'bz;  // Controlled_Buffer controlled_buffer_2
  not not_3 (not_3_out, B[3]);
  FullAdder FullAdder_1 (.A(A[3]), .B(not_3_out), .C(FullAdder_2_r), .O(FullAdder_4_o[3]), .R(FullAdder_1_r[4]));
  not not_4 (not_4_out, FullAdder_4_o[2]);
  FullAdder FullAdder_6 (.A(1'b0), .B(not_4_out), .C(FullAdder_7_r), .O(FullAdder_8_o[2]), .R(FullAdder_6_r));
  not not_5 (not_5_out, B[2]);
  FullAdder FullAdder_2 (.A(A[2]), .B(not_5_out), .C(FullAdder_3_r), .O(FullAdder_4_o[2]), .R(FullAdder_2_r));
  not not_6 (not_6_out, FullAdder_4_o[1]);
  FullAdder FullAdder_7 (.A(1'b0), .B(not_6_out), .C(FullAdder_8_r), .O(FullAdder_8_o[1]), .R(FullAdder_7_r));
  not not_7 (not_7_out, B[1]);
  FullAdder FullAdder_3 (.A(A[1]), .B(not_7_out), .C(FullAdder_4_r), .O(FullAdder_4_o[1]), .R(FullAdder_3_r));
  not not_8 (not_8_out, FullAdder_4_o[0]);
  FullAdder FullAdder_8 (.A(1'b0), .B(not_8_out), .C(1'b1), .O(FullAdder_8_o[0]), .R(FullAdder_8_r));
  not not_9 (not_9_out, B[0]);
  FullAdder FullAdder_4 (.A(A[0]), .B(not_9_out), .C(1'b1), .O(FullAdder_4_o[0]), .R(FullAdder_4_r));
  assign controlled_buffer_3_out = controlled_buffer_8_out ? controlled_buffer_8_out : 1'bz;  // Controlled_Buffer controlled_buffer_3
  assign L_EXP = controlled_buffer_7_out ? A : 4'bz;  // Controlled_Buffer controlled_buffer_4
  assign L_EXP = controlled_buffer_3_out ? B : 4'bz;  // Controlled_Buffer controlled_buffer_5
  assign controlled_buffer_3_out = controlled_buffer_23_out ? controlled_buffer_23_out : 1'bz;  // Controlled_Buffer controlled_buffer_6
  not not_10 (not_10_out, A[3]);
  and and_1 (and_1_out, not_10_out, B[3]);
  assign controlled_buffer_7_out = and_1_out ? and_1_out : 1'bz;  // Controlled_Buffer controlled_buffer_7
  xnor xnor_1 (xnor_1_out, and_1_out, and_2_out);
  not not_11 (not_11_out, B[3]);
  not not_12 (not_12_out, A[2]);
  and and_2 (and_2_out, A[3], not_11_out);
  assign controlled_buffer_8_out = and_2_out ? and_2_out : 1'bz;  // Controlled_Buffer controlled_buffer_8
  assign controlled_buffer_9_out = and_3_out ? and_3_out : 1'bz;  // Controlled_Buffer controlled_buffer_9
  assign controlled_buffer_8_out = xnor_1_out ? controlled_buffer_9_out : 1'bz;  // Controlled_Buffer controlled_buffer_10
  not not_13 (not_13_out, B[2]);
  and and_3 (and_3_out, not_12_out, B[2]);
  and and_4 (and_4_out, A[2], not_13_out);
  assign controlled_buffer_11_out = and_4_out ? and_4_out : 1'bz;  // Controlled_Buffer controlled_buffer_11
  xnor xnor_2 (xnor_2_out, and_3_out, and_4_out);
  assign controlled_buffer_7_out = xnor_1_out ? controlled_buffer_11_out : 1'bz;  // Controlled_Buffer controlled_buffer_12
  assign controlled_buffer_13_out = xnor_1_out ? xnor_2_out : 1'bz;  // Controlled_Buffer controlled_buffer_13
  not not_14 (not_14_out, A[1]);
  and and_5 (and_5_out, not_14_out, B[1]);
  assign controlled_buffer_14_out = and_5_out ? and_5_out : 1'bz;  // Controlled_Buffer controlled_buffer_14
  xnor xnor_3 (xnor_3_out, and_5_out, and_6_out);
  assign controlled_buffer_8_out = controlled_buffer_13_out ? controlled_buffer_14_out : 1'bz;  // Controlled_Buffer controlled_buffer_15
  assign controlled_buffer_16_out = controlled_buffer_13_out ? xnor_3_out : 1'bz;  // Controlled_Buffer controlled_buffer_16
  not not_15 (not_15_out, B[1]);
  not not_16 (not_16_out, A[0]);
  and and_6 (and_6_out, A[1], not_15_out);
  assign controlled_buffer_17_out = and_6_out ? and_6_out : 1'bz;  // Controlled_Buffer controlled_buffer_17
  assign controlled_buffer_18_out = and_8_out ? and_8_out : 1'bz;  // Controlled_Buffer controlled_buffer_18
  assign controlled_buffer_7_out = controlled_buffer_13_out ? controlled_buffer_17_out : 1'bz;  // Controlled_Buffer controlled_buffer_19
  assign controlled_buffer_8_out = controlled_buffer_16_out ? controlled_buffer_18_out : 1'bz;  // Controlled_Buffer controlled_buffer_20
  not not_17 (not_17_out, B[0]);
  and and_7 (and_7_out, A[0], not_17_out);
  and and_8 (and_8_out, not_16_out, B[0]);
  assign controlled_buffer_21_out = and_7_out ? and_7_out : 1'bz;  // Controlled_Buffer controlled_buffer_21
  xnor xnor_4 (xnor_4_out, and_8_out, and_7_out);
  assign controlled_buffer_7_out = controlled_buffer_16_out ? controlled_buffer_21_out : 1'bz;  // Controlled_Buffer controlled_buffer_22
  assign controlled_buffer_23_out = controlled_buffer_16_out ? xnor_4_out : 1'bz;  // Controlled_Buffer controlled_buffer_23
  xor xor_1 (S_DIFF, B[3], A[3]);

  // Notes on the sheet:
  //   Two's Comp
  //   Return absolute value
  //   SUBTRACTOR
  //   SIGN-BIT
  //   COMPARATOR
endmodule

module FullAdder (
  input  A,
  input  B,
  input  C,
  output O,
  output R
);

  wire and_1_out, and_2_out, xor_1_out;

  xor xor_1 (xor_1_out, A, B);
  and and_1 (and_1_out, A, B);
  xor xor_2 (O, xor_1_out, C);
  and and_2 (and_2_out, xor_1_out, C);
  or or_1 (R, and_2_out, and_1_out);
endmodule

module RightShifter (
  input  [3:0] I,
  input  [1:0] S,
  output [3:0] O
);

  wire multiplexer_1_out, multiplexer_2_out, multiplexer_5_out, multiplexer_7_out;

  Multiplexer multiplexer_1 (.in0(I[3]), .in1(1'b0), .out(multiplexer_1_out), .sel(S[1]));
  Multiplexer multiplexer_2 (.in0(I[2]), .in1(1'b0), .out(multiplexer_2_out), .sel(S[1]));
  Multiplexer multiplexer_3 (.in0(multiplexer_1_out), .in1(1'b0), .out(O[3]), .sel(S[0]));
  Multiplexer multiplexer_4 (.in0(multiplexer_2_out), .in1(multiplexer_1_out), .out(O[2]), .sel(S[0]));
  Multiplexer multiplexer_5 (.in0(I[1]), .in1(I[3]), .out(multiplexer_5_out), .sel(S[1]));
  Multiplexer multiplexer_6 (.in0(multiplexer_5_out), .in1(multiplexer_2_out), .out(O[1]), .sel(S[0]));
  Multiplexer multiplexer_7 (.in0(I[0]), .in1(I[2]), .out(multiplexer_7_out), .sel(S[1]));
  Multiplexer multiplexer_8 (.in0(multiplexer_7_out), .in1(multiplexer_5_out), .out(O[0]), .sel(S[0]));
endmodule

module LeftShifter (
  input  [3:0] I,
  input  [1:0] S,
  output [3:0] O
);

  wire multiplexer_1_out, multiplexer_2_out, multiplexer_5_out, multiplexer_7_out;

  Multiplexer multiplexer_1 (.in0(I[0]), .in1(1'b0), .out(multiplexer_1_out), .sel(S[1]));
  Multiplexer multiplexer_2 (.in0(I[1]), .in1(1'b0), .out(multiplexer_2_out), .sel(S[1]));
  Multiplexer multiplexer_3 (.in0(multiplexer_1_out), .in1(1'b0), .out(O[0]), .sel(S[0]));
  Multiplexer multiplexer_4 (.in0(multiplexer_2_out), .in1(multiplexer_1_out), .out(O[1]), .sel(S[0]));
  Multiplexer multiplexer_5 (.in0(I[2]), .in1(I[0]), .out(multiplexer_5_out), .sel(S[1]));
  Multiplexer multiplexer_6 (.in0(multiplexer_5_out), .in1(multiplexer_2_out), .out(O[2]), .sel(S[0]));
  Multiplexer multiplexer_7 (.in0(I[3]), .in1(I[1]), .out(multiplexer_7_out), .sel(S[1]));
  Multiplexer multiplexer_8 (.in0(multiplexer_7_out), .in1(multiplexer_5_out), .out(O[3]), .sel(S[0]));
endmodule

module LOD_20b (
  input  [19:0] Input_bus_1,
  output [4:0] Output_bus_1
);

  wire and_1_out, and_2_out, and_3_out, LOD_4b_1_output_1, LOD_4b_2_output_1, LOD_4b_3_output_1,
       LOD_4b_4_output_1, not_1_out, not_2_out, not_3_out, not_4_out, priority_encoder_1_p1,
       priority_encoder_1_p3;
  wire [3:0] controlled_buffer_1_out, controlled_buffer_3_out, controlled_buffer_5_out,
       LOD_4b_1_output_bus_1, LOD_4b_2_output_bus_1, LOD_4b_3_output_bus_1, LOD_4b_4_output_bus_1,
       LOD_4b_5_output_bus_1;
  wire [19:16] controlled_buffer_6_out;

  LOD_4b LOD_4b_1 (
    .Input_bus_1(Input_bus_1[19:16]), .Output_bus_1(LOD_4b_1_output_bus_1), .Output_1(LOD_4b_1_output_1));
  LOD_4b LOD_4b_2 (
    .Input_bus_1(Input_bus_1[15:12]), .Output_bus_1(LOD_4b_2_output_bus_1), .Output_1(LOD_4b_2_output_1));
  assign controlled_buffer_1_out = LOD_4b_1_output_1 ? LOD_4b_2_output_bus_1 : 4'bz;  // Controlled_Buffer controlled_buffer_1
  not not_1 (not_1_out, LOD_4b_1_output_1);
  assign controlled_buffer_1_out = not_1_out ? 4'b0000 : 4'bz;  // Controlled_Buffer controlled_buffer_2
  LOD_4b LOD_4b_3 (.Input_bus_1(Input_bus_1[11:8]), .Output_bus_1(LOD_4b_3_output_bus_1), .Output_1(LOD_4b_3_output_1));
  and and_1 (and_1_out, LOD_4b_2_output_1, LOD_4b_1_output_1);
  assign controlled_buffer_3_out = and_1_out ? LOD_4b_3_output_bus_1 : 4'bz;  // Controlled_Buffer controlled_buffer_3
  not not_2 (not_2_out, and_1_out);
  assign controlled_buffer_3_out = not_2_out ? 4'b0000 : 4'bz;  // Controlled_Buffer controlled_buffer_4
  LOD_4b LOD_4b_4 (.Input_bus_1(Input_bus_1[7:4]), .Output_bus_1(LOD_4b_4_output_bus_1), .Output_1(LOD_4b_4_output_1));
  and and_2 (and_2_out, LOD_4b_3_output_1, and_1_out);
  assign controlled_buffer_5_out = and_2_out ? LOD_4b_4_output_bus_1 : 4'bz;  // Controlled_Buffer controlled_buffer_5
  not not_3 (not_3_out, and_2_out);
  LOD_4b LOD_4b_5 (.Input_bus_1(Input_bus_1[3:0]), .Output_bus_1(LOD_4b_5_output_bus_1));  // open: Output_1
  and and_3 (and_3_out, LOD_4b_4_output_1, and_2_out);
  assign controlled_buffer_6_out = and_3_out ? LOD_4b_5_output_bus_1 : 4'bz;  // Controlled_Buffer controlled_buffer_6
  not not_4 (not_4_out, and_3_out);
  assign controlled_buffer_5_out = not_3_out ? 4'b0000 : 4'bz;  // Controlled_Buffer controlled_buffer_7
  // Priority_Encoder #(.select(5)) priority_encoder_1: pin names not known; wires that end beside it: priority_encoder_1_p1, Output_bus_1, priority_encoder_1_p3, priority_encoder_1_p3
  assign controlled_buffer_6_out = not_4_out ? 4'b0000 : 4'bz;  // Controlled_Buffer controlled_buffer_8
endmodule

module LOD_4b (
  input  [3:0] Input_bus_1,
  output [3:0] Output_bus_1,
  output Output_1
);

  wire and_1_out, not_2_out, not_3_out, not_4_out, or_1_out, or_2_out, or_3_out;

  or or_1 (or_1_out, Input_bus_1[0], Input_bus_1[1]);
  or or_2 (or_2_out, or_1_out, or_3_out);
  not not_1 (Output_1, or_2_out);
  not not_2 (not_2_out, Input_bus_1[1]);
  and and_1 (and_1_out, Input_bus_1[0], not_2_out);
  and and_2 (Output_bus_1[3], and_1_out, not_3_out);
  or or_3 (or_3_out, Input_bus_1[2], Input_bus_1[3]);
  not not_3 (not_3_out, or_3_out);
  and and_3 (Output_bus_1[2], Input_bus_1[1], not_3_out);
  not not_4 (not_4_out, Input_bus_1[3]);
  and and_4 (Output_bus_1[1], Input_bus_1[2], not_4_out);

  assign Output_bus_1[0] = Input_bus_1[3];

  // Notes on the sheet:
  //   4bit LOD
endmodule

module LOD_32b (
  input  [31:0] in_1
);

  wire [3:0] lod_4b_1_output_bus_1, lod_4b_2_output_bus_1, lod_4b_3_output_bus_1, lod_4b_5_output_bus_1,
       or_4_out;

  LOD_4b lod_4b_1 (.Input_bus_1(in_1[31:28]), .Output_bus_1(lod_4b_1_output_bus_1));  // open: Output_1
  or or_1 (or_4_out[3], in_1[31], in_1[30], in_1[29], in_1[28]);
  LOD_4b lod_4b_2 (.Input_bus_1(in_1[27:24]), .Output_bus_1(lod_4b_2_output_bus_1));  // open: Output_1
  or or_2 (or_4_out[2], in_1[27], in_1[26], in_1[25], in_1[24]);
  LOD_4b lod_4b_3 (.Input_bus_1(in_1[23:20]), .Output_bus_1(lod_4b_3_output_bus_1));  // open: Output_1
  or or_3 (or_4_out[1], in_1[23], in_1[22], in_1[21], in_1[20]);
  LOD_4b lod_4b_4 (.Input_bus_1(or_4_out));  // open: Output_bus_1, Output_1
  LOD_4b lod_4b_5 (.Input_bus_1(in_1[19:16]), .Output_bus_1(lod_4b_5_output_bus_1));  // open: Output_1
  or or_4 (or_4_out[0], in_1[19], in_1[18], in_1[17], in_1[16]);
  // OR_Gate or_5 has open pins: in0=or_4_out[3], in1=or_4_out[2], in2=or_4_out[1], in3=or_4_out[0], out=open
endmodule

module RightRotator (
  input  [7:0] I,
  input  [3:0] S,
  output [7:0] O
);

  wire [7:0] RotateRight_1_output_bus_1, RotateRight_2_output_bus_1, RotateRight_3_output_bus_1,
       RotateRight_4_output_bus_1, RotateRight_5_output_bus_1, RotateRight_6_output_bus_1,
       RotateRight_7_output_bus_1;

  RotateRight RotateRight_1 (.Input_bus_1(I), .Output_bus_1(RotateRight_1_output_bus_1));
  RotateRight RotateRight_2 (.Input_bus_1(RotateRight_1_output_bus_1), .Output_bus_1(RotateRight_2_output_bus_1));
  RotateRight RotateRight_3 (.Input_bus_1(RotateRight_2_output_bus_1), .Output_bus_1(RotateRight_3_output_bus_1));
  RotateRight RotateRight_4 (.Input_bus_1(RotateRight_3_output_bus_1), .Output_bus_1(RotateRight_4_output_bus_1));
  RotateRight RotateRight_5 (.Input_bus_1(RotateRight_4_output_bus_1), .Output_bus_1(RotateRight_5_output_bus_1));
  RotateRight RotateRight_6 (.Input_bus_1(RotateRight_5_output_bus_1), .Output_bus_1(RotateRight_6_output_bus_1));
  RotateRight RotateRight_7 (.Input_bus_1(RotateRight_6_output_bus_1), .Output_bus_1(RotateRight_7_output_bus_1));
  Multiplexer #(.select(4), .width(8)) multiplexer_1 (
    .in0(I), .in1(RotateRight_1_output_bus_1), .in2(RotateRight_2_output_bus_1),
    .in3(RotateRight_3_output_bus_1), .in4(RotateRight_4_output_bus_1), .in5(RotateRight_5_output_bus_1),
    .in6(RotateRight_6_output_bus_1), .in7(RotateRight_7_output_bus_1), .in8(I),
    .in9(RotateRight_1_output_bus_1), .in10(RotateRight_2_output_bus_1), .in11(RotateRight_3_output_bus_1),
    .in12(RotateRight_4_output_bus_1), .in13(RotateRight_5_output_bus_1), .in14(RotateRight_6_output_bus_1),
    .in15(RotateRight_7_output_bus_1), .out(O), .sel(S));
endmodule

module RotateRight (
  input  [7:0] Input_bus_1,
  output [7:0] Output_bus_1
);


  assign Output_bus_1 = {Input_bus_1[0], Input_bus_1[7:1]};
endmodule

module Hexdecoder (
  input  [3:0] Input_bus_1,
  input  E,
  output [6:0] Output_bus_1
);

  wire not_1_out, not_2_out, not_3_out, not_4_out;
  wire [6:0] or_7_out;
  wire [15:0] and_1_out;

  not not_1 (not_1_out, Input_bus_1[3]);
  not not_2 (not_2_out, Input_bus_1[2]);
  not not_3 (not_3_out, Input_bus_1[1]);
  not not_4 (not_4_out, Input_bus_1[0]);
  and and_1 (and_1_out[0], not_4_out, not_3_out, not_2_out, not_1_out);
  and and_2 (and_1_out[1], Input_bus_1[0], not_3_out, not_2_out, not_1_out);
  and and_3 (and_1_out[2], not_4_out, Input_bus_1[1], not_2_out, not_1_out);
  and and_4 (and_1_out[3], Input_bus_1[0], Input_bus_1[1], not_2_out, not_1_out);
  and and_5 (and_1_out[4], not_4_out, not_3_out, Input_bus_1[2], not_1_out);
  and and_6 (and_1_out[5], Input_bus_1[0], not_3_out, Input_bus_1[2], not_1_out);
  and and_7 (and_1_out[6], not_4_out, Input_bus_1[1], Input_bus_1[2], not_1_out);
  and and_8 (and_1_out[7], Input_bus_1[0], Input_bus_1[1], Input_bus_1[2], not_1_out);
  and and_9 (and_1_out[8], not_4_out, not_3_out, not_2_out, Input_bus_1[3]);
  and and_10 (and_1_out[9], Input_bus_1[0], not_3_out, not_2_out, Input_bus_1[3]);
  and and_11 (and_1_out[10], not_4_out, Input_bus_1[1], not_2_out, Input_bus_1[3]);
  and and_12 (and_1_out[11], Input_bus_1[0], Input_bus_1[1], not_2_out, Input_bus_1[3]);
  and and_13 (and_1_out[12], not_4_out, not_3_out, Input_bus_1[2], Input_bus_1[3]);
  and and_14 (and_1_out[13], Input_bus_1[0], not_3_out, Input_bus_1[2], Input_bus_1[3]);
  and and_15 (and_1_out[14], not_4_out, Input_bus_1[1], Input_bus_1[2], Input_bus_1[3]);
  and and_16 (and_1_out[15], Input_bus_1[0], Input_bus_1[1], Input_bus_1[2], Input_bus_1[3]);
  or or_1 (or_7_out[6], and_1_out[0], and_1_out[2], and_1_out[3], and_1_out[5], and_1_out[6], and_1_out[7], and_1_out[8], and_1_out[9], and_1_out[10], and_1_out[12], and_1_out[14], and_1_out[15]);
  or or_2 (or_7_out[5], and_1_out[0], and_1_out[1], and_1_out[2], and_1_out[3], and_1_out[4], and_1_out[7], and_1_out[8], and_1_out[9], and_1_out[10], and_1_out[13]);
  or or_3 (or_7_out[4], and_1_out[0], and_1_out[1], and_1_out[3], and_1_out[4], and_1_out[5], and_1_out[6], and_1_out[7], and_1_out[8], and_1_out[9], and_1_out[10], and_1_out[11], and_1_out[13]);
  or or_4 (or_7_out[3], and_1_out[0], and_1_out[2], and_1_out[3], and_1_out[5], and_1_out[6], and_1_out[8], and_1_out[9], and_1_out[11], and_1_out[12], and_1_out[13], and_1_out[14]);
  or or_5 (or_7_out[2], and_1_out[0], and_1_out[2], and_1_out[6], and_1_out[8], and_1_out[10], and_1_out[11], and_1_out[12], and_1_out[13], and_1_out[14], and_1_out[15]);
  or or_6 (or_7_out[1], and_1_out[0], and_1_out[4], and_1_out[5], and_1_out[6], and_1_out[8], and_1_out[9], and_1_out[10], and_1_out[11], and_1_out[12], and_1_out[14], and_1_out[15]);
  or or_7 (or_7_out[0], and_1_out[2], and_1_out[3], and_1_out[4], and_1_out[5], and_1_out[6], and_1_out[8], and_1_out[9], and_1_out[10], and_1_out[11], and_1_out[13], and_1_out[14], and_1_out[15]);
  Multiplexer #(.width(7)) multiplexer_1 (.in0(7'b0000001), .in1(or_7_out), .out(Output_bus_1), .sel(E));

  // Notes on the sheet:
  //   A
  //   B
  //   C
  //   D
  //   E
  //   F
  //   G
endmodule

module BUS_COORDINATOR (
  input  RAM_E,
  input  ALU_E,
  input  xy_E,
  input  REGS_E,
  input  [7:0] xy,
  input  [7:0] REGS,
  input  [7:0] RAM,
  input  [7:0] ALU,
  output [7:0] BUS_OUT
);

  wire BC_ENCODER_o_e;
  wire [1:0] BC_ENCODER_o_0;

  PEncoder_2 BC_ENCODER (
    .I_3(ALU_E), .I_2(RAM_E), .I_1(REGS_E), .I_0(xy_E), .O_E(BC_ENCODER_o_e), .O_0(BC_ENCODER_o_0[0]),
    .O_1(BC_ENCODER_o_0[1]));
  Multiplexer #(.enable("true"), .select(2), .width(8)) multiplexer_1 (
    .in0(xy), .in1(REGS), .in2(RAM), .in3(ALU), .out(BUS_OUT), .sel(BC_ENCODER_o_0), .en(BC_ENCODER_o_e));
endmodule

module PEncoder_3 (
  input  I_7,
  input  I_6,
  input  I_5,
  input  I_4,
  input  I_3,
  input  I_2,
  input  I_1,
  input  I_0,
  output O_2,
  output O_1,
  output O_0,
  output O_E
);

  or or_1 (O_E, I_7, I_6, I_5, I_4, I_3, I_2, I_1, I_0);
  or or_2 (O_2, I_4, I_5, I_6, I_7);
  or or_3 (O_1, I_2, I_3, I_6, I_7);
  or or_4 (O_0, I_1, I_3, I_5, I_7);
endmodule

module PEncoder_2 (
  input  I_3,
  input  I_2,
  input  I_1,
  input  I_0,
  output O_0,
  output O_1,
  output O_E
);

  wire and_1_out, not_1_out;

  or or_1 (O_1, I_3, I_2);
  not not_1 (not_1_out, I_2);
  or or_2 (O_E, I_1, O_1, I_0);
  and and_1 (and_1_out, I_1, not_1_out);
  or or_3 (O_0, and_1_out, I_3);
endmodule

module FP_PRE_ADDER_BLOCK (
  input  [7:0] A,
  input  [7:0] B,
  output SA,
  output SB,
  output C,
  output [3:0] Exp,
  output [3:0] M_A,
  output [3:0] M_B
);

  wire n_normal_1_comp, n_normal_1_sa, n_normal_1_sb, n_subn_1_comp, n_subn_1_sa, n_subn_1_sb;
  wire [1:0] selector_1_e_data;
  wire [3:0] n_normal_1_eo, n_normal_1_ma, n_normal_1_mb, n_subn_1_eo, n_subn_1_ma, n_subn_1_mb;
  wire [8:0] demultiplexer_1_out0, demultiplexer_1_out1, demultiplexer_1_out2, demultiplexer_2_out0,
       demultiplexer_2_out1, demultiplexer_2_out3, multiplexer_1_out, multiplexer_2_out, n_mixedn_1_ma,
       n_mixedn_1_mb, selector_1_na, selector_1_nb;

  selector selector_1 (.A(A), .B(B), .NA(selector_1_na), .NB(selector_1_nb), .E_Data(selector_1_e_data));
  Demultiplexer #(.select(2), .width(9)) demultiplexer_1 (
    .out0(demultiplexer_1_out0), .out1(demultiplexer_1_out1), .out2(demultiplexer_1_out2),
    .in(selector_1_na), .sel(selector_1_e_data));  // open: out3
  Demultiplexer #(.select(2), .width(9)) demultiplexer_2 (
    .out0(demultiplexer_2_out0), .out1(demultiplexer_2_out1), .out3(demultiplexer_2_out3),
    .in(selector_1_nb), .sel(selector_1_e_data));  // open: out2
  Multiplexer #(.width(9)) multiplexer_1 (
    .in0(demultiplexer_1_out1), .in1(n_mixedn_1_ma), .out(multiplexer_1_out), .sel(selector_1_e_data[1]));
  Multiplexer #(.width(9)) multiplexer_2 (
    .in0(demultiplexer_2_out1), .in1(n_mixedn_1_mb), .out(multiplexer_2_out), .sel(selector_1_e_data[1]));
  n_subn n_subn_1 (
    .A(demultiplexer_1_out0), .B(demultiplexer_2_out0), .SA(n_subn_1_sa), .SB(n_subn_1_sb), .MA(n_subn_1_ma),
    .MB(n_subn_1_mb), .Comp(n_subn_1_comp), .EO(n_subn_1_eo));
  n_mixedn n_mixedn_1 (.A(demultiplexer_1_out2), .B(demultiplexer_2_out3), .MA(n_mixedn_1_ma), .MB(n_mixedn_1_mb));
  n_normal n_normal_1 (
    .A(multiplexer_1_out), .B(multiplexer_2_out), .SA(n_normal_1_sa), .SB(n_normal_1_sb), .EO(n_normal_1_eo),
    .MA(n_normal_1_ma), .Comp(n_normal_1_comp), .MB(n_normal_1_mb));
  Multiplexer multiplexer_3 (.in0(n_subn_1_sa), .in1(n_normal_1_sa), .out(SA), .sel(selector_1_e_data[0]));
  Multiplexer multiplexer_4 (.in0(n_subn_1_sb), .in1(n_normal_1_sb), .out(SB), .sel(selector_1_e_data[0]));
  Multiplexer multiplexer_5 (.in0(n_subn_1_comp), .in1(n_normal_1_comp), .out(C), .sel(selector_1_e_data[0]));
  Multiplexer #(.width(4)) multiplexer_6 (
    .in0(n_subn_1_eo), .in1(n_normal_1_eo), .out(Exp), .sel(selector_1_e_data[0]));
  Multiplexer #(.width(4)) multiplexer_7 (
    .in0(n_subn_1_ma), .in1(n_normal_1_ma), .out(M_A), .sel(selector_1_e_data[0]));
  Multiplexer #(.width(4)) multiplexer_8 (
    .in0(n_subn_1_mb), .in1(n_normal_1_mb), .out(M_B), .sel(selector_1_e_data[0]));
endmodule

module FP_ADDER_BLOCK (
  input  SB,
  input  A_S,
  input  SA,
  input  Comp,
  input  [3:0] A,
  input  [3:0] B,
  output SO,
  output [3:0] S,
  output CO
);

  wire and_1_out, fulladder_1_r, fulladder_2_r, fulladder_3_r;
  wire [3:0] multiplexer_1_out, not_1_out;

  Multiplexer #(.width(4)) multiplexer_1 (.in0(B), .in1(not_1_out), .out(multiplexer_1_out), .sel(and_1_out));
  assign not_1_out = ~B;  // NOT_Gate not_1, 4 bits wide
  and and_1 (and_1_out, A_S, SO);
  FullAdder fulladder_1 (.A(A[0]), .B(multiplexer_1_out[0]), .C(and_1_out), .O(S[0]), .R(fulladder_1_r));
  FullAdder fulladder_2 (.A(A[1]), .B(multiplexer_1_out[1]), .C(fulladder_1_r), .O(S[1]), .R(fulladder_2_r));
  FullAdder fulladder_3 (.A(A[2]), .B(multiplexer_1_out[2]), .C(fulladder_2_r), .O(S[2]), .R(fulladder_3_r));
  FullAdder fulladder_4 (.A(A[3]), .B(multiplexer_1_out[3]), .C(fulladder_3_r), .O(S[3]), .R(CO));
  Multiplexer multiplexer_2 (.in0(SB), .in1(SA), .out(SO), .sel(Comp));
  Multiplexer multiplexer_3 ();  // open: in0, in1, out, sel
endmodule

module FP_STANDARDISING_BLOCK (
  input  S,
  input  Co,
  input  [3:0] ES,
  input  [3:0] MS,
  output [7:0] RESULT
);

  block_norm block_norm_1 (.Co(Co), .ES(ES), .MS(MS), .E(RESULT[6:3]), .M(RESULT[2:0]));

  assign RESULT[7] = S;
endmodule

module n_subn (
  input  [8:0] A,
  input  [8:0] B,
  output SA,
  output SB,
  output [3:0] EO,
  output [3:0] MA,
  output [3:0] MB,
  output Comp
);

  wire comparator_4b_1_eq, comparator_4b_1_gt;

  COMPARATOR_4b comparator_4b_1 (
    .B(B[7:4]), .A(A[7:4]), .EQ(comparator_4b_1_eq), .GT(comparator_4b_1_gt));  // open: S_DIFF, LT
  Multiplexer #(.width(4)) multiplexer_1 (.in0(B[3:0]), .in1(A[3:0]), .out(MA), .sel(Comp));
  Multiplexer #(.width(4)) multiplexer_2 (.in0(A[3:0]), .in1(B[3:0]), .out(MB), .sel(Comp));
  or or_1 (Comp, comparator_4b_1_gt, comparator_4b_1_eq);
  Multiplexer #(.width(4)) multiplexer_3 (.in0(A[7:4]), .in1(B[7:4]), .out(EO), .sel(Comp));

  assign SA = A[8];
  assign SB = B[8];
endmodule

module COMPARATOR_4b (
  input  [3:0] B,
  input  [3:0] A,
  output S_DIFF,
  output EQ,
  output GT,
  output LT
);

  wire and_2_out, and_3_out, and_4_out, and_5_out, and_6_out, and_7_out, and_8_out, and_9_out, not_1_out,
       not_2_out, not_3_out, not_4_out, not_5_out, not_6_out, not_7_out, not_8_out, not_9_out, not_10_out,
       not_11_out, not_12_out, xnor_1_out, xnor_2_out, xnor_3_out, xnor_4_out;
  wire [1:0] pencoder_2_1_o_0;

  and and_1 (EQ, xnor_1_out, xnor_2_out, xnor_3_out, xnor_4_out);
  not not_1 (not_1_out, xnor_4_out);
  not not_2 (not_2_out, xnor_3_out);
  not not_3 (not_3_out, xnor_2_out);
  not not_4 (not_4_out, xnor_1_out);
  PEncoder_2 pencoder_2_1 (
    .I_3(not_4_out), .I_2(not_3_out), .I_1(not_2_out), .I_0(not_1_out), .O_0(pencoder_2_1_o_0[0]),
    .O_1(pencoder_2_1_o_0[1]));  // open: O_E
  not not_5 (not_5_out, B[3]);
  and and_2 (and_2_out, not_5_out, A[3]);
  xnor xnor_1 (xnor_1_out, and_2_out, and_3_out);
  Multiplexer #(.select(2)) multiplexer_1 (
    .in0(and_9_out), .in1(and_6_out), .in2(and_4_out), .in3(and_2_out), .out(GT), .sel(pencoder_2_1_o_0));
  not not_6 (not_6_out, A[3]);
  not not_7 (not_7_out, B[2]);
  and and_3 (and_3_out, B[3], not_6_out);
  Multiplexer #(.select(2)) multiplexer_2 (
    .in0(and_8_out), .in1(and_7_out), .in2(and_5_out), .in3(and_3_out), .out(LT), .sel(pencoder_2_1_o_0));
  not not_8 (not_8_out, A[2]);
  and and_4 (and_4_out, not_7_out, A[2]);
  and and_5 (and_5_out, B[2], not_8_out);
  xnor xnor_2 (xnor_2_out, and_4_out, and_5_out);
  not not_9 (not_9_out, B[1]);
  and and_6 (and_6_out, not_9_out, A[1]);
  xnor xnor_3 (xnor_3_out, and_6_out, and_7_out);
  not not_10 (not_10_out, A[1]);
  not not_11 (not_11_out, B[0]);
  and and_7 (and_7_out, B[1], not_10_out);
  not not_12 (not_12_out, A[0]);
  and and_8 (and_8_out, B[0], not_12_out);
  and and_9 (and_9_out, not_11_out, A[0]);
  xnor xnor_4 (xnor_4_out, and_9_out, and_8_out);
  xor xor_1 (S_DIFF, A[3], B[3]);

  // Notes on the sheet:
  //   EQ
  //   COMPARATOR
endmodule

module n_mixedn (
  input  [8:0] A,
  input  [8:0] B,
  output [8:0] MA,
  output [8:0] MB
);

  wire [1:0] zero_counter_1_zcount;
  wire [7:0] subnormal_comp_1_nb;

  SUBNORMAL_COMP subnormal_comp_1 (
    .A(A), .B(B), .NA(MA), .NB({MB[0], subnormal_comp_1_nb[7:4], MB[8:6], subnormal_comp_1_nb[0]}));
  ZERO_COUNTER zero_counter_1 (.T({MB[8:6], subnormal_comp_1_nb[0]}), .ZCount(zero_counter_1_zcount));
  LeftShifter leftshifter_1 (.S(zero_counter_1_zcount), .I({MB[8:6], subnormal_comp_1_nb[0]}), .O(MB[4:1]));

  assign MB[5] = 1'b1;
endmodule

module SUBNORMAL_COMP (
  input  [8:0] A,
  input  [8:0] B,
  output [8:0] NA,
  output [8:0] NB
);

  wire or_1_out;

  or or_1 (or_1_out, A[7], A[6], A[5], A[4]);
  Multiplexer #(.width(9)) multiplexer_1 (.in0(A), .in1(B), .out(NA), .sel(or_1_out));
  Multiplexer #(.width(9)) multiplexer_2 (.in0(B), .in1(A), .out(NB), .sel(or_1_out));

  // Notes on the sheet:
  //   Note that this assumes one of the inputs is subnormal
endmodule

module ZERO_COUNTER (
  input  [3:0] T,
  output [1:0] ZCount
);

  LZD_4b lzd_4b_1 (.I_0(T[0]), .I_1(T[1]), .I_2(T[2]), .I_3(T[3]), .Q_0(ZCount[0]), .Q_1(ZCount[1]));  // open: A
endmodule

module LZD_2b (
  input  I_0,
  input  I_1,
  output v,
  output p
);

  wire not_1_out;

  not not_1 (not_1_out, I_1);
  or or_1 (v, I_0, not_1_out);
  and and_1 (p, I_0, not_1_out);
endmodule

module LZD_4b (
  input  I_0,
  input  I_1,
  input  I_2,
  input  I_3,
  output A,
  output Q_0,
  output Q_1
);

  wire not_1_out, not_2_out, or_1_out;

  not not_1 (not_1_out, I_3);
  or or_1 (or_1_out, I_2, not_2_out);
  not not_2 (not_2_out, I_1);
  nor nor_1 (Q_1, I_3, I_2);
  nor nor_2 (A, I_0, I_1, I_2, I_3);
  and and_1 (Q_0, not_1_out, or_1_out);
endmodule

module n_normal (
  input  [8:0] A,
  input  [8:0] B,
  output SA,
  output SB,
  output [3:0] EO,
  output [3:0] MA,
  output Comp,
  output [3:0] MB
);

  wire [3:0] exp_comp_1_dexp, exp_comp_1_mshift;

  EXP_COMP exp_comp_1 (
    .A(A), .B(B), .DExp(exp_comp_1_dexp), .SB(SB), .EMax(EO), .SA(SA), .MMax(MA), .MShift(exp_comp_1_mshift),
    .Comp(Comp));
  RightShifter rightshifter_1 (.S(exp_comp_1_dexp[1:0]), .I(exp_comp_1_mshift), .O(MB));

  // Notes on the sheet:
  //   <-- THIS IS A VERY PROBLEMATIC SOLUTION
endmodule

module EXP_COMP (
  input  [8:0] A,
  input  [8:0] B,
  output SA,
  output SB,
  output [3:0] EMax,
  output [3:0] MMax,
  output Comp,
  output [3:0] MShift,
  output [3:0] DExp
);

  wire comparator_4b_1_eq, comparator_4b_1_gt, comparator_4b_tc_1_eq, comparator_4b_tc_1_gt, FullAdder_2_r,
       FullAdder_3_r, FullAdder_4_r, FullAdder_6_r, FullAdder_7_r, FullAdder_8_r, not_1_out, not_2_out,
       not_3_out, not_4_out, not_5_out, not_6_out, not_7_out, not_8_out, or_1_out;
  wire [3:0] FullAdder_4_o, FullAdder_8_o;
  wire [4:4] FullAdder_1_r;

  not not_1 (not_1_out, FullAdder_4_o[3]);
  Multiplexer #(.width(4)) multiplexer_1 (.in0(FullAdder_4_o), .in1(FullAdder_8_o), .out(DExp), .sel(FullAdder_1_r[4]));
  not not_2 (not_2_out, B[7]);
  FullAdder FullAdder_1 (.A(A[7]), .B(not_2_out), .C(FullAdder_2_r), .O(FullAdder_4_o[3]), .R(FullAdder_1_r[4]));
  not not_3 (not_3_out, FullAdder_4_o[2]);
  FullAdder FullAdder_5 (.A(1'b0), .B(not_1_out), .C(FullAdder_6_r), .O(FullAdder_8_o[3]));  // open: R
  FullAdder FullAdder_6 (.A(1'b0), .B(not_3_out), .C(FullAdder_7_r), .O(FullAdder_8_o[2]), .R(FullAdder_6_r));
  not not_4 (not_4_out, B[6]);
  FullAdder FullAdder_2 (.A(A[6]), .B(not_4_out), .C(FullAdder_3_r), .O(FullAdder_4_o[2]), .R(FullAdder_2_r));
  not not_5 (not_5_out, FullAdder_4_o[1]);
  FullAdder FullAdder_7 (.A(1'b0), .B(not_5_out), .C(FullAdder_8_r), .O(FullAdder_8_o[1]), .R(FullAdder_7_r));
  not not_6 (not_6_out, B[5]);
  FullAdder FullAdder_3 (.A(A[5]), .B(not_6_out), .C(FullAdder_4_r), .O(FullAdder_4_o[1]), .R(FullAdder_3_r));
  not not_7 (not_7_out, FullAdder_4_o[0]);
  FullAdder FullAdder_8 (.A(1'b0), .B(not_7_out), .C(1'b1), .O(FullAdder_8_o[0]), .R(FullAdder_8_r));
  not not_8 (not_8_out, B[4]);
  FullAdder FullAdder_4 (.A(A[4]), .B(not_8_out), .C(1'b1), .O(FullAdder_4_o[0]), .R(FullAdder_4_r));
  COMPARATOR_4b_TC comparator_4b_tc_1 (
    .B(B[7:4]), .A(A[7:4]), .EQ(comparator_4b_tc_1_eq), .GT(comparator_4b_tc_1_gt));  // open: S_DIFF, LT
  Multiplexer #(.width(4)) multiplexer_2 (.in0(B[7:4]), .in1(A[7:4]), .out(EMax), .sel(Comp));
  COMPARATOR_4b comparator_4b_1 (
    .B(B[3:0]), .A(A[3:0]), .EQ(comparator_4b_1_eq), .GT(comparator_4b_1_gt));  // open: S_DIFF, LT
  Multiplexer multiplexer_3 (.in0(comparator_4b_tc_1_gt), .in1(or_1_out), .out(Comp), .sel(comparator_4b_tc_1_eq));
  or or_1 (or_1_out, comparator_4b_1_gt, comparator_4b_1_eq);
  Multiplexer #(.width(4)) multiplexer_4 (.in0(A[3:0]), .in1(B[3:0]), .out(MMax), .sel(Comp));
  Multiplexer #(.width(4)) multiplexer_5 (.in0(B[3:0]), .in1(A[3:0]), .out(MShift), .sel(Comp));

  assign SA = A[8];
  assign SB = B[8];

  // Notes on the sheet:
  //   Two's Comp
  //   Return absolute value
  //   SUBTRACTOR
endmodule

module selector (
  input  [7:0] A,
  input  [7:0] B,
  output [8:0] NA,
  output [8:0] NB,
  output [1:0] E_Data
);

  wire not_1_out, not_2_out, not_3_out, not_4_out, not_5_out, not_6_out, not_7_out, not_8_out;

  and and_1 (NA[0], not_1_out, not_2_out, not_3_out, not_4_out);
  not not_1 (not_1_out, A[6]);
  not not_2 (not_2_out, A[5]);
  not not_3 (not_3_out, A[4]);
  not not_4 (not_4_out, A[3]);
  not not_5 (not_5_out, B[6]);
  not not_6 (not_6_out, B[5]);
  not not_7 (not_7_out, B[4]);
  not not_8 (not_8_out, B[3]);
  and and_2 (NB[0], not_5_out, not_6_out, not_7_out, not_8_out);
  nor nor_1 (E_Data[0], NA[0], NB[0]);
  xor xor_1 (E_Data[1], NA[0], NB[0]);

  assign NA[8:1] = A;
  assign NB[8:1] = B;
endmodule

module COMPARATOR_4b_TC (
  input  [3:0] B,
  input  [3:0] A,
  output S_DIFF,
  output EQ,
  output GT,
  output LT
);

  wire and_2_out, and_3_out, and_4_out, and_5_out, and_6_out, and_7_out, and_8_out, and_9_out, not_1_out,
       not_2_out, not_3_out, not_4_out, not_5_out, not_6_out, not_7_out, not_8_out, not_9_out, not_10_out,
       not_11_out, not_12_out, xnor_1_out, xnor_2_out, xnor_3_out, xnor_4_out;
  wire [1:0] pencoder_2_1_o_0;

  and and_1 (EQ, xnor_1_out, xnor_2_out, xnor_3_out, xnor_4_out);
  not not_1 (not_1_out, xnor_4_out);
  not not_2 (not_2_out, xnor_3_out);
  not not_3 (not_3_out, xnor_2_out);
  not not_4 (not_4_out, xnor_1_out);
  PEncoder_2 pencoder_2_1 (
    .I_3(not_4_out), .I_2(not_3_out), .I_1(not_2_out), .I_0(not_1_out), .O_0(pencoder_2_1_o_0[0]),
    .O_1(pencoder_2_1_o_0[1]));  // open: O_E
  not not_5 (not_5_out, A[3]);
  not not_6 (not_6_out, B[3]);
  and and_2 (and_2_out, B[3], not_5_out);
  xnor xnor_1 (xnor_1_out, and_2_out, and_3_out);
  Multiplexer #(.select(2)) multiplexer_1 (
    .in0(and_9_out), .in1(and_6_out), .in2(and_4_out), .in3(and_2_out), .out(GT), .sel(pencoder_2_1_o_0));
  not not_7 (not_7_out, B[2]);
  and and_3 (and_3_out, not_6_out, A[3]);
  Multiplexer #(.select(2)) multiplexer_2 (
    .in0(and_8_out), .in1(and_7_out), .in2(and_5_out), .in3(and_3_out), .out(LT), .sel(pencoder_2_1_o_0));
  not not_8 (not_8_out, A[2]);
  and and_4 (and_4_out, not_7_out, A[2]);
  and and_5 (and_5_out, B[2], not_8_out);
  xnor xnor_2 (xnor_2_out, and_4_out, and_5_out);
  not not_9 (not_9_out, B[1]);
  and and_6 (and_6_out, not_9_out, A[1]);
  xnor xnor_3 (xnor_3_out, and_6_out, and_7_out);
  not not_10 (not_10_out, A[1]);
  not not_11 (not_11_out, B[0]);
  and and_7 (and_7_out, B[1], not_10_out);
  not not_12 (not_12_out, A[0]);
  and and_8 (and_8_out, B[0], not_12_out);
  and and_9 (and_9_out, not_11_out, A[0]);
  xnor xnor_4 (xnor_4_out, and_9_out, and_8_out);
  xor xor_1 (S_DIFF, A[3], B[3]);

  // Notes on the sheet:
  //   EQ
  //   COMPARATOR
endmodule

module ROUND_4_3 (
  input  [3:0] I,
  output [2:0] O
);


  assign O = I[3:1];
endmodule

module block_norm (
  input  Co,
  input  [3:0] ES,
  input  [3:0] MS,
  output [3:0] E,
  output [2:0] M
);

  wire [1:0] exp_stand_1_shift, zero_counter_1_zcount;
  wire [3:0] leftshifter_1_o;

  ZERO_COUNTER zero_counter_1 (.T(MS), .ZCount(zero_counter_1_zcount));
  EXP_STAND exp_stand_1 (.Co(Co), .ES(ES), .Z_c(zero_counter_1_zcount), .E(E), .shift(exp_stand_1_shift));
  LeftShifter leftshifter_1 (.S(exp_stand_1_shift), .I(MS), .O(leftshifter_1_o));
  ROUND_4_3 round_4_3_1 (.I(leftshifter_1_o), .O(M));
endmodule

module EXP_STAND (
  input  Co,
  input  [3:0] ES,
  input  [1:0] Z_c,
  output [3:0] E,
  output [1:0] shift
);

  wire comparator_4b_1_eq, comparator_4b_1_gt, fulladder_1_o, fulladder_1_r, fulladder_2_o, fulladder_2_r,
       fulladder_3_o, fulladder_3_r, fulladder_4_o, fulladder_5_r, fulladder_6_r, fulladder_7_r, not_1_out,
       or_1_out;
  wire [3:0] fulladder_5_o, multiplexer_2_out;

  COMPARATOR_4b comparator_4b_1 (
    .B({2'b00, Z_c}), .A(ES), .EQ(comparator_4b_1_eq), .GT(comparator_4b_1_gt));  // open: S_DIFF, LT
  FullAdder fulladder_1 (.A(ES[0]), .B(Z_c[0]), .C(1'b1), .O(fulladder_1_o), .R(fulladder_1_r));
  FullAdder fulladder_2 (.A(ES[1]), .B(Z_c[1]), .C(fulladder_1_r), .O(fulladder_2_o), .R(fulladder_2_r));
  FullAdder fulladder_3 (.A(ES[2]), .B(1'b0), .C(fulladder_2_r), .O(fulladder_3_o), .R(fulladder_3_r));
  FullAdder fulladder_4 (.A(ES[3]), .B(1'b0), .C(fulladder_3_r), .O(fulladder_4_o));  // open: R
  or or_1 (or_1_out, comparator_4b_1_eq, comparator_4b_1_gt);
  Multiplexer #(.width(2)) multiplexer_1 (.in0(ES[1:0]), .in1(Z_c), .out(shift), .sel(or_1_out));
  FullAdder fulladder_5 (.A(fulladder_1_o), .B(1'b0), .C(Co), .O(fulladder_5_o[0]), .R(fulladder_5_r));
  FullAdder fulladder_6 (.A(fulladder_2_o), .B(1'b0), .C(fulladder_5_r), .O(fulladder_5_o[1]), .R(fulladder_6_r));
  FullAdder fulladder_7 (.A(fulladder_3_o), .B(1'b0), .C(fulladder_6_r), .O(fulladder_5_o[2]), .R(fulladder_7_r));
  FullAdder fulladder_8 (.A(fulladder_4_o), .B(1'b0), .C(fulladder_7_r), .O(fulladder_5_o[3]));  // open: R
  Multiplexer #(.width(4)) multiplexer_2 (
    .in0(4'b0001), .in1(4'b0000), .out(multiplexer_2_out), .sel(comparator_4b_1_eq));
  Multiplexer #(.width(4)) multiplexer_3 (.in0(fulladder_5_o), .in1(multiplexer_2_out), .out(E), .sel(not_1_out));
  not not_1 (not_1_out, comparator_4b_1_gt);
endmodule

module OLD_BUS_VER (
);

  wire and_1_out, and_2_out, and_3_out, and_4_out, and_5_out, and_6_out, and_7_out, and_8_out, and_9_out,
       and_10_out, and_11_out, and_12_out, and_13_out, and_14_out, and_15_out, and_16_out, and_17_out,
       and_18_out, and_19_out, and_20_out, and_21_out, and_22_out, and_23_out, and_24_out, and_25_out,
       and_26_out, and_27_out, and_28_out, and_29_out, and_30_out, and_31_out, and_32_out, and_33_out,
       and_34_out, and_35_out, and_36_out, and_37_out, and_38_out, and_39_out, and_40_out, and_41_out,
       and_42_out, and_43_out, AUTO_p1, CLK_out, CONTROL_UNIT_alu_read, CONTROL_UNIT_hlt,
       CONTROL_UNIT_increment_pc, CONTROL_UNIT_load_acc, CONTROL_UNIT_load_cir, CONTROL_UNIT_load_mar,
       CONTROL_UNIT_load_out, CONTROL_UNIT_load_pc, CONTROL_UNIT_read_acc, CONTROL_UNIT_read_mbr,
       CONTROL_UNIT_read_ram, CONTROL_UNIT_register_read, CONTROL_UNIT_register_write,
       CONTROL_UNIT_write_ram, controlled_buffer_2_out, demultiplexer_1_out0, demultiplexer_1_out1,
       demultiplexer_1_out2, demultiplexer_1_out3, demultiplexer_2_out0, demultiplexer_2_out1,
       demultiplexer_2_out2, demultiplexer_2_out3, demultiplexer_3_out0, demultiplexer_3_out1,
       demultiplexer_3_out2, demultiplexer_3_out3, demultiplexer_4_out0, demultiplexer_4_out1,
       demultiplexer_4_out2, demultiplexer_4_out3, HLT_REGISTER_q, HLT_REGISTER_qn, MAIN_ALU_sr,
       MAIN_ALU_sr_w, not_3_out, not_6_out, or_1_out, RESET_out, STATUS_REG_q, STEP_out;
  wire [2:0] CONTROL_UNIT_alu_instr, not_4_out_2, not_5_out_2, not_7_out_2, not_9_out_2, not_20_out_2,
       not_21_out_2;
  wire [3:0] CIR_q, CIR_q_2, CIR_q_3, CIR_q_4, CONTROL_UNIT_register_read_select,
       CONTROL_UNIT_register_write_select, controlled_buffer_4_out, controlled_buffer_4_out_2, j_k_ff_1_q,
       j_k_ff_5_q, MAR_q, MAR_q_2, not_4_out, not_5_out, not_7_out, not_9_out, not_20_out, not_21_out,
       OUTPUT_REG_q, OUTPUT_REG_q_2;
  wire [6:0] Hexdecoder_1_output_bus_1, Hexdecoder_2_output_bus_1, Hexdecoder_3_output_bus_1,
       Hexdecoder_4_output_bus_1, Hexdecoder_5_output_bus_1, Hexdecoder_6_output_bus_1,
       Hexdecoder_7_output_bus_1, Hexdecoder_8_output_bus_1, Hexdecoder_9_output_bus_1,
       Hexdecoder_10_output_bus_1, Hexdecoder_11_output_bus_1, Hexdecoder_12_output_bus_1,
       Hexdecoder_13_output_bus_1, Hexdecoder_14_output_bus_1, Hexdecoder_15_output_bus_1,
       Hexdecoder_16_output_bus_1, Hexdecoder_17_output_bus_1, Hexdecoder_18_output_bus_1,
       Hexdecoder_19_output_bus_1, not_1_out, not_2_out, not_8_out, not_10_out, not_11_out, not_12_out,
       not_13_out, not_14_out, not_15_out, not_16_out, not_17_out, not_18_out, not_19_out;
  wire [7:0] controlled_buffer_1_out, MAIN_MEMORY_data_out, REG_0_q, REG_1_q, REG_2_q, REG_3_q, REG_4_q,
       REG_5_q, REG_6_q, REG_7_q, REG_8_q, REG_9_q, REG_10_q, REG_11_q, REG_12_q, REG_13_q, REG_14_q,
       REG_15_q, register_1_q, register_2_q;
  wire [15:0] INSTRUCTIONS_data;

  _7_Segment_Display #(.active("false"), .decimalPoint("false")) R_WRITE (
    .g(not_1_out[0]), .f(not_1_out[1]), .a(not_1_out[6]), .b(not_1_out[5]), .e(not_1_out[2]),
    .d(not_1_out[3]), .c(not_1_out[4]));
  assign not_1_out = ~Hexdecoder_12_output_bus_1;  // NOT_Gate not_1, 7 bits wide
  Hexdecoder Hexdecoder_12 (
    .Input_bus_1(CONTROL_UNIT_register_write_select), .E(CONTROL_UNIT_register_write),
    .Output_bus_1(Hexdecoder_12_output_bus_1));
  Demultiplexer #(.enable("true"), .select(2)) demultiplexer_1 (
    .out0(demultiplexer_1_out0), .out1(demultiplexer_1_out1), .out2(demultiplexer_1_out2),
    .out3(demultiplexer_1_out3), .in(CONTROL_UNIT_register_read),
    .sel(CONTROL_UNIT_register_read_select[3:2]), .en(CONTROL_UNIT_register_read));
  Demultiplexer #(.enable("true"), .select(2)) demultiplexer_2 (
    .out0(demultiplexer_2_out0), .out1(demultiplexer_2_out1), .out2(demultiplexer_2_out2),
    .out3(demultiplexer_2_out3), .in(CONTROL_UNIT_register_write),
    .sel(CONTROL_UNIT_register_write_select[3:2]), .en(CONTROL_UNIT_register_write));
  _7_Segment_Display #(.active("false"), .decimalPoint("false")) R_READ (
    .g(not_2_out[0]), .f(not_2_out[1]), .a(not_2_out[6]), .b(not_2_out[5]), .e(not_2_out[2]),
    .d(not_2_out[3]), .c(not_2_out[4]));
  assign not_2_out = ~Hexdecoder_13_output_bus_1;  // NOT_Gate not_2, 7 bits wide
  Hexdecoder Hexdecoder_13 (
    .Input_bus_1(CONTROL_UNIT_register_read_select), .E(CONTROL_UNIT_register_read),
    .Output_bus_1(Hexdecoder_13_output_bus_1));
  and and_1 (and_1_out, CONTROL_UNIT_increment_pc, and_26_out);
  and and_2 (and_2_out, demultiplexer_3_out0, demultiplexer_2_out0);
  and and_3 (and_3_out, demultiplexer_3_out0, demultiplexer_2_out1);
  and and_4 (and_4_out, demultiplexer_3_out0, demultiplexer_2_out2);
  and and_5 (and_5_out, demultiplexer_3_out0, demultiplexer_2_out3);
  MEMORY_16B REGISTERS ();  // open: RESET, READ_ADDRESS, WRITE, DATA_IN, WRITE_ADDRESS, CLK, DATA_OUT
  not not_3 (not_3_out, and_1_out);
  Register #(.trigger("falling")) REG_0 (
    .D({controlled_buffer_4_out_2, controlled_buffer_4_out}), .en(and_2_out), .clk(and_26_out), .Q(REG_0_q),
    .clr(RESET_out));
  Register #(.trigger("falling")) REG_4 (
    .D({controlled_buffer_4_out_2, controlled_buffer_4_out}), .en(and_3_out), .clk(and_26_out), .Q(REG_4_q),
    .clr(RESET_out));
  Register #(.trigger("falling")) REG_8 (
    .D({controlled_buffer_4_out_2, controlled_buffer_4_out}), .en(and_4_out), .clk(and_26_out), .Q(REG_8_q),
    .clr(RESET_out));
  Register #(.trigger("falling")) REG_12 (
    .D({controlled_buffer_4_out_2, controlled_buffer_4_out}), .en(and_5_out), .clk(and_26_out), .Q(REG_12_q),
    .clr(RESET_out));
  J_K_Flip_Flop #(.trigger("falling")) j_k_ff_1 (
    .J(1'b1), .K(1'b1), .clk(and_1_out), .Q(j_k_ff_1_q[0]), .preset(controlled_buffer_1_out[0]),
    .reset(controlled_buffer_2_out));  // open: Qn
  assign controlled_buffer_1_out = and_6_out ? {controlled_buffer_4_out_2, controlled_buffer_4_out} : 8'bz;  // Controlled_Buffer controlled_buffer_1
  and and_6 (and_6_out, CONTROL_UNIT_load_pc, not_3_out);
  assign controlled_buffer_2_out = RESET_out ? RESET_out : 1'bz;  // Controlled_Buffer controlled_buffer_2
  assign controlled_buffer_2_out = CONTROL_UNIT_load_pc ? CONTROL_UNIT_load_pc : 1'bz;  // Controlled_Buffer controlled_buffer_3
  _7_Segment_Display #(.active("false"), .decimalPoint("false")) PC_1 (
    .g(not_4_out[0]), .f(not_4_out[1]), .a(not_4_out[3]), .b(not_4_out[2]), .e(not_4_out_2[0]),
    .d(not_4_out_2[1]), .c(not_4_out_2[2]));
  and and_7 (and_7_out, demultiplexer_1_out0, demultiplexer_4_out0);
  assign {controlled_buffer_4_out_2, controlled_buffer_4_out} = and_7_out ? REG_0_q : 8'bz;  // Controlled_Buffer controlled_buffer_4
  and and_8 (and_8_out, demultiplexer_1_out1, demultiplexer_4_out0);
  assign {controlled_buffer_4_out_2, controlled_buffer_4_out} = and_8_out ? REG_4_q : 8'bz;  // Controlled_Buffer controlled_buffer_5
  and and_9 (and_9_out, demultiplexer_1_out2, demultiplexer_4_out0);
  assign {controlled_buffer_4_out_2, controlled_buffer_4_out} = and_9_out ? REG_8_q : 8'bz;  // Controlled_Buffer controlled_buffer_6
  and and_10 (and_10_out, demultiplexer_1_out3, demultiplexer_4_out0);
  assign {controlled_buffer_4_out_2, controlled_buffer_4_out} = and_10_out ? REG_12_q : 8'bz;  // Controlled_Buffer controlled_buffer_7
  Hexdecoder Hexdecoder_7 (.Input_bus_1(j_k_ff_5_q), .E(1'b1), .Output_bus_1(Hexdecoder_7_output_bus_1));
  Hexdecoder Hexdecoder_8 (.Input_bus_1(j_k_ff_1_q), .E(1'b1), .Output_bus_1(Hexdecoder_8_output_bus_1));
  assign {not_4_out[3:2], not_4_out_2, not_4_out[1:0]} = ~Hexdecoder_7_output_bus_1;  // NOT_Gate not_4, 7 bits wide
  assign {not_5_out[3:2], not_5_out_2, not_5_out[1:0]} = ~Hexdecoder_8_output_bus_1;  // NOT_Gate not_5, 7 bits wide
  _7_Segment_Display #(.active("false"), .decimalPoint("false")) PC_0 (
    .g(not_5_out[0]), .f(not_5_out[1]), .a(not_5_out[3]), .b(not_5_out[2]), .e(not_5_out_2[0]),
    .d(not_5_out_2[1]), .c(not_5_out_2[2]));
  Demultiplexer #(.enable("true"), .select(2)) demultiplexer_3 (
    .out0(demultiplexer_3_out0), .out1(demultiplexer_3_out1), .out2(demultiplexer_3_out2),
    .out3(demultiplexer_3_out3), .in(CONTROL_UNIT_register_write),
    .sel(CONTROL_UNIT_register_write_select[1:0]), .en(CONTROL_UNIT_register_write));
  Register #(.trigger("falling")) REG_1 (
    .D({controlled_buffer_4_out_2, controlled_buffer_4_out}), .en(and_11_out), .clk(and_26_out), .Q(REG_1_q),
    .clr(RESET_out));
  and and_11 (and_11_out, demultiplexer_3_out1, demultiplexer_2_out0);
  Register #(.trigger("falling")) REG_5 (
    .D({controlled_buffer_4_out_2, controlled_buffer_4_out}), .en(and_12_out), .clk(and_26_out), .Q(REG_5_q),
    .clr(RESET_out));
  and and_12 (and_12_out, demultiplexer_3_out1, demultiplexer_2_out1);
  Register #(.trigger("falling")) REG_9 (
    .D({controlled_buffer_4_out_2, controlled_buffer_4_out}), .en(and_13_out), .clk(and_26_out), .Q(REG_9_q),
    .clr(RESET_out));
  and and_13 (and_13_out, demultiplexer_3_out1, demultiplexer_2_out2);
  Register #(.trigger("falling")) REG_13 (
    .D({controlled_buffer_4_out_2, controlled_buffer_4_out}), .en(and_14_out), .clk(and_26_out),
    .Q(REG_13_q), .clr(RESET_out));
  and and_14 (and_14_out, demultiplexer_3_out1, demultiplexer_2_out3);
  J_K_Flip_Flop #(.trigger("falling")) j_k_ff_2 (
    .J(j_k_ff_1_q[0]), .K(j_k_ff_1_q[0]), .clk(and_1_out), .Q(j_k_ff_1_q[1]),
    .preset(controlled_buffer_1_out[1]), .reset(controlled_buffer_2_out));  // open: Qn
  ROM #(.dataWidth(16)) INSTRUCTIONS (.addr({j_k_ff_5_q, j_k_ff_1_q}), .data(INSTRUCTIONS_data));
  and and_15 (and_15_out, demultiplexer_1_out0, demultiplexer_4_out1);
  assign {controlled_buffer_4_out_2, controlled_buffer_4_out} = and_15_out ? REG_1_q : 8'bz;  // Controlled_Buffer controlled_buffer_8
  and and_16 (and_16_out, demultiplexer_1_out1, demultiplexer_4_out1);
  assign {controlled_buffer_4_out_2, controlled_buffer_4_out} = and_16_out ? REG_5_q : 8'bz;  // Controlled_Buffer controlled_buffer_9
  and and_17 (and_17_out, demultiplexer_1_out2, demultiplexer_4_out1);
  assign {controlled_buffer_4_out_2, controlled_buffer_4_out} = and_17_out ? REG_9_q : 8'bz;  // Controlled_Buffer controlled_buffer_10
  and and_18 (and_18_out, demultiplexer_1_out3, demultiplexer_4_out1);
  assign {controlled_buffer_4_out_2, controlled_buffer_4_out} = and_18_out ? REG_13_q : 8'bz;  // Controlled_Buffer controlled_buffer_11
  J_K_Flip_Flop #(.trigger("falling")) j_k_ff_3 (
    .J(and_19_out), .K(and_19_out), .clk(and_1_out), .Q(j_k_ff_1_q[2]), .preset(controlled_buffer_1_out[2]),
    .reset(controlled_buffer_2_out));  // open: Qn
  and and_19 (and_19_out, j_k_ff_1_q[1], j_k_ff_1_q[0]);
  and and_20 (and_20_out, demultiplexer_3_out2, demultiplexer_2_out0);
  and and_21 (and_21_out, demultiplexer_3_out2, demultiplexer_2_out1);
  and and_22 (and_22_out, demultiplexer_3_out2, demultiplexer_2_out2);
  and and_23 (and_23_out, demultiplexer_3_out2, demultiplexer_2_out3);
  and and_24 (and_24_out, j_k_ff_1_q[2], and_19_out);
  Demultiplexer #(.enable("true"), .select(2)) demultiplexer_4 (
    .out0(demultiplexer_4_out0), .out1(demultiplexer_4_out1), .out2(demultiplexer_4_out2),
    .out3(demultiplexer_4_out3), .in(CONTROL_UNIT_register_read),
    .sel(CONTROL_UNIT_register_read_select[1:0]), .en(CONTROL_UNIT_register_read));
  Register #(.trigger("falling")) REG_2 (
    .D({controlled_buffer_4_out_2, controlled_buffer_4_out}), .en(and_20_out), .clk(and_26_out), .Q(REG_2_q),
    .clr(RESET_out));
  Register #(.trigger("falling")) REG_6 (
    .D({controlled_buffer_4_out_2, controlled_buffer_4_out}), .en(and_21_out), .clk(and_26_out), .Q(REG_6_q),
    .clr(RESET_out));
  Register #(.trigger("falling")) REG_10 (
    .D({controlled_buffer_4_out_2, controlled_buffer_4_out}), .en(and_22_out), .clk(and_26_out),
    .Q(REG_10_q), .clr(RESET_out));
  Register #(.trigger("falling")) REG_14 (
    .D({controlled_buffer_4_out_2, controlled_buffer_4_out}), .en(and_23_out), .clk(and_26_out),
    .Q(REG_14_q), .clr(RESET_out));
  J_K_Flip_Flop #(.trigger("falling")) j_k_ff_4 (
    .J(and_24_out), .K(and_24_out), .clk(and_1_out), .Q(j_k_ff_1_q[3]), .preset(controlled_buffer_1_out[3]),
    .reset(controlled_buffer_2_out));  // open: Qn
  and and_25 (and_25_out, j_k_ff_1_q[3], and_24_out);
  Register #(.width(16)) CIR (
    .D(INSTRUCTIONS_data), .en(CONTROL_UNIT_load_cir), .clk(and_26_out),
    .Q({CIR_q_4, CIR_q_3, CIR_q_2, CIR_q}), .clr(RESET_out));
  and and_26 (and_26_out, or_1_out, HLT_REGISTER_qn);
  D_Flip_Flop #(.trigger("falling")) HLT_REGISTER (
    .D(CONTROL_UNIT_hlt), .clk(and_26_out), .Q(HLT_REGISTER_q), .Qn(HLT_REGISTER_qn), .reset(RESET_out));  // open: preset
  and and_27 (and_27_out, demultiplexer_1_out0, demultiplexer_4_out2);
  assign {controlled_buffer_4_out_2, controlled_buffer_4_out} = and_27_out ? REG_2_q : 8'bz;  // Controlled_Buffer controlled_buffer_12
  and and_28 (and_28_out, demultiplexer_1_out1, demultiplexer_4_out2);
  assign {controlled_buffer_4_out_2, controlled_buffer_4_out} = and_28_out ? REG_6_q : 8'bz;  // Controlled_Buffer controlled_buffer_13
  and and_29 (and_29_out, demultiplexer_1_out2, demultiplexer_4_out2);
  assign {controlled_buffer_4_out_2, controlled_buffer_4_out} = and_29_out ? REG_10_q : 8'bz;  // Controlled_Buffer controlled_buffer_14
  and and_30 (and_30_out, demultiplexer_1_out3, demultiplexer_4_out2);
  assign {controlled_buffer_4_out_2, controlled_buffer_4_out} = and_30_out ? REG_14_q : 8'bz;  // Controlled_Buffer controlled_buffer_15
  J_K_Flip_Flop #(.trigger("falling")) j_k_ff_5 (
    .J(and_25_out), .K(and_25_out), .clk(and_1_out), .Q(j_k_ff_5_q[0]), .preset(controlled_buffer_1_out[4]),
    .reset(controlled_buffer_2_out));  // open: Qn
  and and_31 (and_31_out, STEP_out, not_6_out);
  or or_1 (or_1_out, and_31_out, and_32_out);
  and and_32 (and_32_out, AUTO_p1, CLK_out);
  LED HLT_REG (.in(HLT_REGISTER_q));
  Register #(.trigger("falling")) REG_3 (
    .D({controlled_buffer_4_out_2, controlled_buffer_4_out}), .en(and_33_out), .clk(and_26_out), .Q(REG_3_q),
    .clr(RESET_out));
  and and_33 (and_33_out, demultiplexer_3_out3, demultiplexer_2_out0);
  Register #(.trigger("falling")) REG_7 (
    .D({controlled_buffer_4_out_2, controlled_buffer_4_out}), .en(and_34_out), .clk(and_26_out), .Q(REG_7_q),
    .clr(RESET_out));
  and and_34 (and_34_out, demultiplexer_3_out3, demultiplexer_2_out1);
  Register #(.trigger("falling")) REG_11 (
    .D({controlled_buffer_4_out_2, controlled_buffer_4_out}), .en(and_35_out), .clk(and_26_out),
    .Q(REG_11_q), .clr(RESET_out));
  and and_35 (and_35_out, demultiplexer_3_out3, demultiplexer_2_out2);
  Register #(.trigger("falling")) REG_15 (
    .D({controlled_buffer_4_out_2, controlled_buffer_4_out}), .en(and_36_out), .clk(and_26_out),
    .Q(REG_15_q), .clr(RESET_out));
  and and_36 (and_36_out, demultiplexer_3_out3, demultiplexer_2_out3);
  J_K_Flip_Flop #(.trigger("falling")) j_k_ff_6 (
    .J(and_37_out), .K(and_37_out), .clk(and_1_out), .Q(j_k_ff_5_q[1]), .preset(controlled_buffer_1_out[5]),
    .reset(controlled_buffer_2_out));  // open: Qn
  and and_37 (and_37_out, j_k_ff_5_q[0], and_25_out);
  not not_6 (not_6_out, AUTO_p1);
  LED CLK_L (.in(CLK_out));
  and and_38 (and_38_out, j_k_ff_5_q[1], and_37_out);
  Button RESET (.out(RESET_out));
  Button STEP (.out(STEP_out));
  // DipSwitch #(.number(1)) AUTO: pin names not known; wires that end beside it: AUTO_p1
  Clock CLK (.out(CLK_out));
  and and_39 (and_39_out, demultiplexer_1_out0, demultiplexer_4_out3);
  assign {controlled_buffer_4_out_2, controlled_buffer_4_out} = and_39_out ? REG_3_q : 8'bz;  // Controlled_Buffer controlled_buffer_16
  and and_40 (and_40_out, demultiplexer_1_out1, demultiplexer_4_out3);
  assign {controlled_buffer_4_out_2, controlled_buffer_4_out} = and_40_out ? REG_7_q : 8'bz;  // Controlled_Buffer controlled_buffer_17
  and and_41 (and_41_out, demultiplexer_1_out2, demultiplexer_4_out3);
  assign {controlled_buffer_4_out_2, controlled_buffer_4_out} = and_41_out ? REG_11_q : 8'bz;  // Controlled_Buffer controlled_buffer_18
  and and_42 (and_42_out, demultiplexer_1_out3, demultiplexer_4_out3);
  assign {controlled_buffer_4_out_2, controlled_buffer_4_out} = and_42_out ? REG_15_q : 8'bz;  // Controlled_Buffer controlled_buffer_19
  J_K_Flip_Flop #(.trigger("falling")) j_k_ff_7 (
    .J(and_38_out), .K(and_38_out), .clk(and_1_out), .Q(j_k_ff_5_q[2]), .preset(controlled_buffer_1_out[6]),
    .reset(controlled_buffer_2_out));  // open: Qn
  Register #(.trigger("falling")) MAR (
    .D({controlled_buffer_4_out_2, controlled_buffer_4_out}), .en(CONTROL_UNIT_load_mar), .clk(and_26_out),
    .Q({MAR_q_2, MAR_q}), .clr(RESET_out));
  J_K_Flip_Flop #(.trigger("falling")) j_k_ff_8 (
    .J(and_43_out), .K(and_43_out), .clk(and_1_out), .Q(j_k_ff_5_q[3]), .preset(controlled_buffer_1_out[7]),
    .reset(controlled_buffer_2_out));  // open: Qn
  and and_43 (and_43_out, j_k_ff_5_q[2], and_38_out);
  Hexdecoder Hexdecoder_18 (.Input_bus_1(MAR_q_2), .E(1'b1), .Output_bus_1(Hexdecoder_18_output_bus_1));
  assign {not_7_out[3:2], not_7_out_2, not_7_out[1:0]} = ~Hexdecoder_18_output_bus_1;  // NOT_Gate not_7, 7 bits wide
  _7_Segment_Display #(.active("false"), .decimalPoint("false")) L_7_Segment_Display_1 (
    .g(not_7_out[0]), .f(not_7_out[1]), .a(not_7_out[3]), .b(not_7_out[2]), .e(not_7_out_2[0]),
    .d(not_7_out_2[1]), .c(not_7_out_2[2]));
  assign not_8_out = ~Hexdecoder_1_output_bus_1;  // NOT_Gate not_8, 7 bits wide
  Hexdecoder Hexdecoder_1 (.Input_bus_1(CIR_q_4), .E(1'b1), .Output_bus_1(Hexdecoder_1_output_bus_1));
  OLD_CU CONTROL_UNIT (
    .Run(RESET_out), .SR(STATUS_REG_q), .INSTRUCTION({CIR_q_4, CIR_q_3, CIR_q_2, CIR_q}), .CLK(and_26_out),
    .LOAD_CIR(CONTROL_UNIT_load_cir), .INCREMENT_PC(CONTROL_UNIT_increment_pc),
    .ALU_INSTR(CONTROL_UNIT_alu_instr), .LOAD_OUT(CONTROL_UNIT_load_out), .LOAD_MAR(CONTROL_UNIT_load_mar),
    .READ_RAM(CONTROL_UNIT_read_ram), .WRITE_RAM(CONTROL_UNIT_write_ram), .READ_MBR(CONTROL_UNIT_read_mbr),
    .READ_ACC(CONTROL_UNIT_read_acc), .LOAD_ACC(CONTROL_UNIT_load_acc), .ALU_READ(CONTROL_UNIT_alu_read),
    .REGISTER_READ_SELECT(CONTROL_UNIT_register_read_select),
    .REGISTER_WRITE_SELECT(CONTROL_UNIT_register_write_select),
    .xy({controlled_buffer_4_out_2, controlled_buffer_4_out}), .LOAD_PC(CONTROL_UNIT_load_pc),
    .HLT(CONTROL_UNIT_hlt), .REGISTER_READ(CONTROL_UNIT_register_read),
    .REGISTER_WRITE(CONTROL_UNIT_register_write));
  Register #(.trigger("falling")) register_1 (
    .D({controlled_buffer_4_out_2, controlled_buffer_4_out}), .en(CONTROL_UNIT_load_acc), .clk(and_26_out),
    .Q(register_1_q), .clr(RESET_out));
  assign {controlled_buffer_4_out_2, controlled_buffer_4_out} = CONTROL_UNIT_read_acc ? register_1_q : 8'bz;  // Controlled_Buffer controlled_buffer_20
  assign {controlled_buffer_4_out_2, controlled_buffer_4_out} = CONTROL_UNIT_read_mbr ? register_2_q : 8'bz;  // Controlled_Buffer controlled_buffer_21
  Hexdecoder Hexdecoder_19 (.Input_bus_1(MAR_q), .E(1'b1), .Output_bus_1(Hexdecoder_19_output_bus_1));
  assign {not_9_out[3:2], not_9_out_2, not_9_out[1:0]} = ~Hexdecoder_19_output_bus_1;  // NOT_Gate not_9, 7 bits wide
  _7_Segment_Display #(.active("false"), .decimalPoint("false")) MAR_0 (
    .g(not_9_out[0]), .f(not_9_out[1]), .a(not_9_out[3]), .b(not_9_out[2]), .e(not_9_out_2[0]),
    .d(not_9_out_2[1]), .c(not_9_out_2[2]));
  _7_Segment_Display #(.active("false"), .decimalPoint("false")) CIR_3 (
    .g(not_8_out[0]), .f(not_8_out[1]), .a(not_8_out[6]), .b(not_8_out[5]), .e(not_8_out[2]),
    .d(not_8_out[3]), .c(not_8_out[4]));
  _7_Segment_Display #(.active("false"), .decimalPoint("false")) CIR_2 (
    .g(not_10_out[0]), .f(not_10_out[1]), .a(not_10_out[6]), .b(not_10_out[5]), .e(not_10_out[2]),
    .d(not_10_out[3]), .c(not_10_out[4]));
  assign not_10_out = ~Hexdecoder_2_output_bus_1;  // NOT_Gate not_10, 7 bits wide
  Hexdecoder Hexdecoder_2 (.Input_bus_1(CIR_q_3), .E(1'b1), .Output_bus_1(Hexdecoder_2_output_bus_1));
  _7_Segment_Display #(.active("false"), .decimalPoint("false")) CIR_1 (
    .g(not_11_out[0]), .f(not_11_out[1]), .a(not_11_out[6]), .b(not_11_out[5]), .e(not_11_out[2]),
    .d(not_11_out[3]), .c(not_11_out[4]));
  assign not_11_out = ~Hexdecoder_3_output_bus_1;  // NOT_Gate not_11, 7 bits wide
  assign not_12_out = ~Hexdecoder_4_output_bus_1;  // NOT_Gate not_12, 7 bits wide
  Hexdecoder Hexdecoder_3 (.Input_bus_1(CIR_q_2), .E(1'b1), .Output_bus_1(Hexdecoder_3_output_bus_1));
  Hexdecoder Hexdecoder_4 (.Input_bus_1(CIR_q), .E(1'b1), .Output_bus_1(Hexdecoder_4_output_bus_1));
  LED HLT (.in(CONTROL_UNIT_hlt));
  Hexdecoder Hexdecoder_14 (.Input_bus_1(register_1_q[7:4]), .E(1'b1), .Output_bus_1(Hexdecoder_14_output_bus_1));
  Hexdecoder Hexdecoder_15 (.Input_bus_1(register_1_q[3:0]), .E(1'b1), .Output_bus_1(Hexdecoder_15_output_bus_1));
  _7_Segment_Display #(.active("false"), .decimalPoint("false")) CIR_0 (
    .g(not_12_out[0]), .f(not_12_out[1]), .a(not_12_out[6]), .b(not_12_out[5]), .e(not_12_out[2]),
    .d(not_12_out[3]), .c(not_12_out[4]));
  OLD_ALU MAIN_ALU (
    .INSTR(CONTROL_UNIT_alu_instr), .DATA_IN({controlled_buffer_4_out_2, controlled_buffer_4_out}),
    .ACCUMULATOR(register_1_q), .CLK(and_26_out), .READ(CONTROL_UNIT_alu_read), .SR_W(MAIN_ALU_sr_w),
    .SR(MAIN_ALU_sr), .DATA_OUT({controlled_buffer_4_out_2, controlled_buffer_4_out}));
  MEMORY_256B MAIN_MEMORY (
    .READ_ADDRESS({MAR_q_2, MAR_q}), .WRITE(CONTROL_UNIT_write_ram), .WRITE_ADDRESS({MAR_q_2, MAR_q}),
    .DATA_IN({controlled_buffer_4_out_2, controlled_buffer_4_out}), .RESET(RESET_out), .CLK(and_26_out),
    .DATA_OUT(MAIN_MEMORY_data_out));
  LED PC_INCR (.in(CONTROL_UNIT_increment_pc));
  LED CIR_LOAD (.in(CONTROL_UNIT_load_cir));
  LED REG_READ (.in(CONTROL_UNIT_register_read));
  LED REG_WRITE (.in(CONTROL_UNIT_register_write));
  LED MAR_LOAD (.in(CONTROL_UNIT_load_mar));
  LED RAM_READ (.in(CONTROL_UNIT_read_ram));
  LED RAM_WRITE (.in(CONTROL_UNIT_write_ram));
  LED MBR_READ (.in(CONTROL_UNIT_read_mbr));
  LED ACC_READ (.in(CONTROL_UNIT_read_acc));
  LED ACC_LOAD (.in(CONTROL_UNIT_load_acc));
  LED OUT_LOAD (.in(CONTROL_UNIT_load_out));
  LED PC_LOAD (.in(CONTROL_UNIT_load_pc));
  assign not_13_out = ~Hexdecoder_14_output_bus_1;  // NOT_Gate not_13, 7 bits wide
  assign not_14_out = ~Hexdecoder_15_output_bus_1;  // NOT_Gate not_14, 7 bits wide
  Register #(.width(1)) STATUS_REG (
    .D(MAIN_ALU_sr), .en(MAIN_ALU_sr_w), .clk(and_26_out), .Q(STATUS_REG_q), .clr(RESET_out));
  Register #(.trigger("falling")) register_2 (
    .D(MAIN_MEMORY_data_out), .en(CONTROL_UNIT_read_ram), .clk(and_26_out), .Q(register_2_q), .clr(RESET_out));
  _7_Segment_Display #(.active("false"), .decimalPoint("false")) ACC_1 (
    .g(not_13_out[0]), .f(not_13_out[1]), .a(not_13_out[6]), .b(not_13_out[5]), .e(not_13_out[2]),
    .d(not_13_out[3]), .c(not_13_out[4]));
  assign not_15_out = ~Hexdecoder_5_output_bus_1;  // NOT_Gate not_15, 7 bits wide
  Hexdecoder Hexdecoder_5 (.Input_bus_1(OUTPUT_REG_q_2), .E(1'b1), .Output_bus_1(Hexdecoder_5_output_bus_1));
  _7_Segment_Display #(.active("false"), .decimalPoint("false")) ACC_0 (
    .g(not_14_out[0]), .f(not_14_out[1]), .a(not_14_out[6]), .b(not_14_out[5]), .e(not_14_out[2]),
    .d(not_14_out[3]), .c(not_14_out[4]));
  LED SR (.in(STATUS_REG_q));
  _7_Segment_Display #(.active("false"), .decimalPoint("false")) MBR_1 (
    .g(not_16_out[0]), .f(not_16_out[1]), .a(not_16_out[6]), .b(not_16_out[5]), .e(not_16_out[2]),
    .d(not_16_out[3]), .c(not_16_out[4]));
  assign not_16_out = ~Hexdecoder_16_output_bus_1;  // NOT_Gate not_16, 7 bits wide
  assign not_17_out = ~Hexdecoder_17_output_bus_1;  // NOT_Gate not_17, 7 bits wide
  Hexdecoder Hexdecoder_16 (.Input_bus_1(register_2_q[7:4]), .E(1'b1), .Output_bus_1(Hexdecoder_16_output_bus_1));
  Hexdecoder Hexdecoder_17 (.Input_bus_1(register_2_q[3:0]), .E(1'b1), .Output_bus_1(Hexdecoder_17_output_bus_1));
  _7_Segment_Display #(.active("false"), .decimalPoint("false")) OUTPUT_1 (
    .g(not_15_out[0]), .f(not_15_out[1]), .a(not_15_out[6]), .b(not_15_out[5]), .e(not_15_out[2]),
    .d(not_15_out[3]), .c(not_15_out[4]));
  assign not_18_out = ~Hexdecoder_6_output_bus_1;  // NOT_Gate not_18, 7 bits wide
  Hexdecoder Hexdecoder_6 (.Input_bus_1(OUTPUT_REG_q), .E(1'b1), .Output_bus_1(Hexdecoder_6_output_bus_1));
  Register #(.trigger("falling")) OUTPUT_REG (
    .D({controlled_buffer_4_out_2, controlled_buffer_4_out}), .en(CONTROL_UNIT_load_out), .clk(and_26_out),
    .Q({OUTPUT_REG_q_2, OUTPUT_REG_q}), .clr(RESET_out));
  _7_Segment_Display #(.active("false"), .decimalPoint("false")) MBR_0 (
    .g(not_17_out[0]), .f(not_17_out[1]), .a(not_17_out[6]), .b(not_17_out[5]), .e(not_17_out[2]),
    .d(not_17_out[3]), .c(not_17_out[4]));
  _7_Segment_Display #(.active("false"), .decimalPoint("false")) OUTPUT_0 (
    .g(not_18_out[0]), .f(not_18_out[1]), .a(not_18_out[6]), .b(not_18_out[5]), .e(not_18_out[2]),
    .d(not_18_out[3]), .c(not_18_out[4]));
  _7_Segment_Display #(.active("false"), .decimalPoint("false")) ALU_INSTR (
    .g(not_19_out[0]), .f(not_19_out[1]), .a(not_19_out[6]), .b(not_19_out[5]), .e(not_19_out[2]),
    .d(not_19_out[3]), .c(not_19_out[4]));
  assign not_19_out = ~Hexdecoder_9_output_bus_1;  // NOT_Gate not_19, 7 bits wide
  Hexdecoder Hexdecoder_9 (
    .Input_bus_1({1'b0, CONTROL_UNIT_alu_instr}), .E(CONTROL_UNIT_alu_read),
    .Output_bus_1(Hexdecoder_9_output_bus_1));
  LED ALU_READ (.in(CONTROL_UNIT_alu_read));
  Hexdecoder Hexdecoder_10 (
    .Input_bus_1(controlled_buffer_4_out_2), .E(1'b0), .Output_bus_1(Hexdecoder_10_output_bus_1));
  assign {not_20_out[3:2], not_20_out_2, not_20_out[1:0]} = ~Hexdecoder_10_output_bus_1;  // NOT_Gate not_20, 7 bits wide
  _7_Segment_Display #(.active("false"), .decimalPoint("false")) XY_1_x (
    .g(not_20_out[0]), .f(not_20_out[1]), .a(not_20_out[3]), .b(not_20_out[2]), .e(not_20_out_2[0]),
    .d(not_20_out_2[1]), .c(not_20_out_2[2]));
  _7_Segment_Display #(.active("false"), .decimalPoint("false")) XY_0_y (
    .g(not_21_out[0]), .f(not_21_out[1]), .a(not_21_out[3]), .b(not_21_out[2]), .e(not_21_out_2[0]),
    .d(not_21_out_2[1]), .c(not_21_out_2[2]));
  Hexdecoder Hexdecoder_11 (.Input_bus_1(controlled_buffer_4_out), .E(1'b0), .Output_bus_1(Hexdecoder_11_output_bus_1));
  assign {not_21_out[3:2], not_21_out_2, not_21_out[1:0]} = ~Hexdecoder_11_output_bus_1;  // NOT_Gate not_21, 7 bits wide
  MainMemory OLD_MAIN_MEMORY ();  // open: READ, WRITE, CLK, RESET, READ_ADDRESS, WRITE_ADDRESS, DATA_IN, DATA_OUT

  // Notes on the sheet:
  //   READ COL
  //   WRITE COL
  //   REG_WRITE
  //   RESET_PC
  //   REG_READ
  //   INCREMENT
  //   WRITE COL
  //   contents of INSTRUCTIONS (hex, n*v repeats v):
  //   2001 2102 2203 2304 2405 2506 2607 2708 2809 290a 2a0b 2b0c 2c0d 2d0e 2e0f 2f10 3000 3101 3202 3303
  //   3404 3505 3606 3707 3808 3909 3a0a 3b0b 3c0c 3d0d 3e0e 3f0f 100f 110e 120d 130c 140b 150a 1609 1708
  //   1807 1906 1a05 1b04 1c03 1d02 1e01 1f00 40f0 40e1 40d2 40c3 40b4 40a5 4096 4087 2023 2144 5201 6301
  //   7401 8501 9601 a704 2000 2f05 2eff 2c02 2d03 b047 ffff 5ccd 5ffe bf46 b047
  //   READ
  //   PROGRAM COUNTER
  //   Register Bus
  //   READ COL
  //   Memory Address Register
  //   Accumulator
  //   Read MBR
  //   Memory Buffer Register
  //   OUTPUT
  //   TOO ANNOYING
endmodule

module OLD_CU (
  input  Run,
  input  CLK,
  input  [15:0] INSTRUCTION,
  input  SR,
  output LOAD_CIR,
  output INCREMENT_PC,
  output LOAD_OUT,
  output LOAD_MAR,
  output READ_RAM,
  output WRITE_RAM,
  output READ_MBR,
  output READ_ACC,
  output LOAD_ACC,
  output ALU_READ,
  output REGISTER_READ,
  output [3:0] REGISTER_READ_SELECT,
  output REGISTER_WRITE,
  output [3:0] REGISTER_WRITE_SELECT,
  output [7:0] xy,
  output LOAD_PC,
  output HLT,
  output [2:0] ALU_INSTR
);

  wire and_1_out, and_2_out, and_3_out, and_4_out, and_5_out, and_6_out, and_7_out, and_8_out, and_9_out,
       and_10_out, and_11_out, and_12_out, and_13_out, and_14_out, and_15_out, and_17_out, and_18_out,
       and_19_out, and_22_out, and_23_out, and_24_out, and_26_out, and_27_out, and_28_out, and_29_out,
       and_30_out, and_31_out, and_33_out, and_34_out, and_35_out, and_37_out, and_38_out, and_40_out,
       and_41_out, and_43_out, and_44_out, and_46_out, and_47_out, and_49_out, and_52_out, and_53_out,
       and_54_out, and_55_out, and_56_out, d_ff_2_q, d_ff_3_q, d_ff_4_q, nor_1_out, not_1_out, not_2_out,
       not_3_out, not_4_out, or_1_out, or_2_out, or_3_out, or_4_out, or_5_out, or_6_out, or_7_out, or_8_out,
       or_10_out, or_11_out, priority_encoder_1_p3, priority_encoder_1_p4, priority_encoder_1_p6,
       priority_encoder_1_p7, priority_encoder_1_p8, priority_encoder_1_p9, undriven;
  wire [3:0] controlled_buffer_1_out, controlled_buffer_4_out;

  not not_1 (not_1_out, INSTRUCTION[15]);
  not not_2 (not_2_out, INSTRUCTION[14]);
  not not_3 (not_3_out, INSTRUCTION[13]);
  assign controlled_buffer_1_out = or_4_out ? INSTRUCTION[11:8] : 4'bz;  // Controlled_Buffer controlled_buffer_1
  assign controlled_buffer_1_out = undriven ? INSTRUCTION[7:4] : 4'bz;  // Controlled_Buffer controlled_buffer_2
  assign controlled_buffer_1_out = or_5_out ? INSTRUCTION[3:0] : 4'bz;  // Controlled_Buffer controlled_buffer_3
  and and_1 (and_1_out, not_1_out, not_2_out, not_3_out, not_4_out);
  and and_2 (and_2_out, not_1_out, not_2_out, not_3_out, INSTRUCTION[12]);
  and and_3 (and_3_out, not_1_out, not_2_out, INSTRUCTION[13], not_4_out);
  and and_4 (and_4_out, not_1_out, not_2_out, INSTRUCTION[13], INSTRUCTION[12]);
  and and_5 (and_5_out, not_1_out, INSTRUCTION[14], not_3_out, not_4_out);
  and and_6 (and_6_out, not_1_out, INSTRUCTION[14], not_3_out, INSTRUCTION[12]);
  and and_7 (and_7_out, not_1_out, INSTRUCTION[14], INSTRUCTION[13], not_4_out);
  and and_8 (and_8_out, not_1_out, INSTRUCTION[14], INSTRUCTION[13], INSTRUCTION[12]);
  and and_9 (and_9_out, INSTRUCTION[15], not_2_out, not_3_out, not_4_out);
  and and_10 (and_10_out, INSTRUCTION[15], not_2_out, not_3_out, INSTRUCTION[12]);
  and and_11 (and_11_out, INSTRUCTION[15], not_2_out, INSTRUCTION[13], not_4_out);
  and and_12 (and_12_out, INSTRUCTION[15], not_2_out, INSTRUCTION[13], INSTRUCTION[12]);
  and and_13 (and_13_out, INSTRUCTION[15], INSTRUCTION[14], not_3_out, not_4_out);
  and and_14 (and_14_out, INSTRUCTION[15], INSTRUCTION[14], not_3_out, INSTRUCTION[12]);
  and and_15 (and_15_out, INSTRUCTION[15], INSTRUCTION[14], INSTRUCTION[13], not_4_out);
  and and_16 (HLT, INSTRUCTION[15], INSTRUCTION[14], INSTRUCTION[13], INSTRUCTION[12]);
  not not_4 (not_4_out, INSTRUCTION[12]);
  assign controlled_buffer_4_out = priority_encoder_1_p9 ? 4'b0000 : 4'bz;  // Controlled_Buffer controlled_buffer_4
  assign controlled_buffer_4_out = or_1_out ? INSTRUCTION[11:8] : 4'bz;  // Controlled_Buffer controlled_buffer_5
  assign controlled_buffer_4_out = or_2_out ? INSTRUCTION[7:4] : 4'bz;  // Controlled_Buffer controlled_buffer_6
  assign controlled_buffer_4_out = or_3_out ? INSTRUCTION[3:0] : 4'bz;  // Controlled_Buffer controlled_buffer_7
  or or_1 (or_1_out, WRITE_RAM, priority_encoder_1_p8, and_47_out, LOAD_OUT);
  or or_2 (or_2_out, and_27_out, and_29_out, priority_encoder_1_p3, priority_encoder_1_p4, priority_encoder_1_p6, priority_encoder_1_p7);
  or or_3 (or_3_out, and_30_out, and_33_out, and_35_out, and_38_out, and_41_out);
  or or_4 (or_4_out, READ_MBR, and_22_out, and_31_out, and_34_out, and_37_out, and_40_out, and_43_out, and_46_out);
  D_Flip_Flop #(.trigger("falling")) d_ff_1 (
    .D(d_ff_4_q), .clk(CLK), .Q(LOAD_CIR), .preset(or_6_out));  // open: Qn, reset
  and and_17 (and_17_out, and_1_out, LOAD_CIR);
  and and_18 (and_18_out, and_1_out, d_ff_2_q);
  and and_19 (and_19_out, LOAD_CIR, and_2_out);
  and and_20 (READ_RAM, d_ff_2_q, and_2_out);
  and and_21 (READ_MBR, d_ff_3_q, and_2_out);
  D_Flip_Flop #(.trigger("falling")) d_ff_2 (
    .D(LOAD_CIR), .clk(CLK), .Q(d_ff_2_q), .reset(or_6_out));  // open: Qn, preset
  and and_22 (and_22_out, and_3_out, LOAD_CIR);
  and and_23 (and_23_out, and_3_out, d_ff_2_q);
  or or_5 (or_5_out, and_27_out, and_44_out);
  D_Flip_Flop #(.trigger("falling")) d_ff_3 (
    .D(d_ff_2_q), .clk(CLK), .Q(d_ff_3_q), .reset(or_6_out));  // open: Qn, preset
  and and_24 (and_24_out, and_4_out, LOAD_CIR);
  and and_25 (WRITE_RAM, and_4_out, d_ff_2_q);
  and and_26 (and_26_out, and_4_out, d_ff_3_q);
  D_Flip_Flop #(.trigger("falling")) d_ff_4 (
    .D(d_ff_3_q), .clk(CLK), .Q(d_ff_4_q), .reset(or_6_out));  // open: Qn, preset
  and and_27 (and_27_out, and_5_out, LOAD_CIR);
  and and_28 (and_28_out, and_5_out, d_ff_2_q);
  and and_29 (and_29_out, and_6_out, LOAD_CIR);
  and and_30 (and_30_out, and_6_out, d_ff_2_q);
  and and_31 (and_31_out, and_6_out, d_ff_3_q);
  nor nor_1 (nor_1_out, and_30_out, priority_encoder_1_p3, priority_encoder_1_p4, priority_encoder_1_p6, priority_encoder_1_p7, priority_encoder_1_p8, priority_encoder_1_p9);
  // Priority_Encoder priority_encoder_1: pin names not known; wires that end beside it: nor_1_out, and_30_out, priority_encoder_1_p3, priority_encoder_1_p4, ALU_INSTR, priority_encoder_1_p6, priority_encoder_1_p7, priority_encoder_1_p8, priority_encoder_1_p9
  and and_32 (priority_encoder_1_p3, and_7_out, d_ff_2_q);
  and and_33 (and_33_out, and_7_out, LOAD_CIR);
  and and_34 (and_34_out, and_7_out, d_ff_3_q);
  and and_35 (and_35_out, and_8_out, LOAD_CIR);
  and and_36 (priority_encoder_1_p4, and_8_out, d_ff_2_q);
  and and_37 (and_37_out, and_8_out, d_ff_3_q);
  and and_38 (and_38_out, and_9_out, LOAD_CIR);
  and and_39 (priority_encoder_1_p6, and_9_out, d_ff_2_q);
  and and_40 (and_40_out, and_9_out, d_ff_3_q);
  and and_41 (and_41_out, and_10_out, LOAD_CIR);
  and and_42 (priority_encoder_1_p7, and_10_out, d_ff_2_q);
  and and_43 (and_43_out, and_10_out, d_ff_3_q);
  and and_44 (and_44_out, and_11_out, LOAD_CIR);
  and and_45 (priority_encoder_1_p8, and_11_out, d_ff_2_q);
  or or_6 (or_6_out, Run, or_8_out);
  and and_46 (and_46_out, and_11_out, d_ff_3_q);
  and and_47 (and_47_out, and_12_out, LOAD_CIR);
  and and_48 (priority_encoder_1_p9, and_12_out, d_ff_2_q);
  and and_49 (and_49_out, and_12_out, d_ff_3_q);
  and and_50 (LOAD_OUT, and_13_out, LOAD_CIR);
  and and_51 (LOAD_PC, and_49_out, SR);
  and and_52 (and_52_out, and_13_out, d_ff_2_q);
  and and_53 (and_53_out, and_14_out, LOAD_CIR);
  and and_54 (and_54_out, and_14_out, d_ff_2_q);
  and and_55 (and_55_out, and_15_out, LOAD_CIR);
  and and_56 (and_56_out, and_15_out, d_ff_2_q);
  or or_7 (or_7_out, and_55_out, and_53_out, LOAD_OUT, and_27_out, WRITE_RAM, and_22_out, and_17_out);
  or or_8 (or_8_out, LOAD_PC, or_10_out);
  or or_9 (INCREMENT_PC, d_ff_4_q, or_7_out);
  or or_10 (or_10_out, and_56_out, and_54_out, and_52_out, and_28_out, and_26_out, and_23_out, and_18_out);
  or or_11 (or_11_out, and_19_out, and_22_out, and_24_out, and_44_out, LOAD_PC);
  assign xy = or_11_out ? INSTRUCTION[7:0] : 8'bz;  // Controlled_Buffer controlled_buffer_8
  or or_12 (REGISTER_WRITE, READ_MBR, and_22_out, and_27_out, and_31_out, and_34_out, and_37_out, and_40_out, and_43_out, and_46_out);
  assign REGISTER_WRITE_SELECT = REGISTER_WRITE ? controlled_buffer_1_out : 4'bz;  // Controlled_Buffer controlled_buffer_9
  or or_13 (REGISTER_READ, WRITE_RAM, and_27_out, and_29_out, and_30_out, and_33_out, priority_encoder_1_p3, and_35_out, priority_encoder_1_p4, and_38_out, priority_encoder_1_p6, and_41_out, priority_encoder_1_p7, and_47_out, priority_encoder_1_p8, priority_encoder_1_p9, LOAD_OUT);
  assign REGISTER_READ_SELECT = REGISTER_READ ? controlled_buffer_4_out : 4'bz;  // Controlled_Buffer controlled_buffer_10
  or or_14 (LOAD_MAR, and_19_out, and_24_out);
  or or_15 (LOAD_ACC, and_29_out, and_33_out, and_35_out, and_38_out, and_41_out, and_44_out, and_47_out);
  or or_16 (ALU_READ, and_31_out, and_34_out, and_37_out, and_40_out, and_43_out, and_46_out);

  // Notes on the sheet:
  //   READ
  //   WRITE
  //   RING COUNTER
  //   EARLY INCREMENT PC
  //   EARLY RESET RC
  //   CURRENTLY UNUSED
  //   ALU INSTRUCTION SET
  //   000 : -
  //   001 : ADD (TC)
  //   010 : ADD (FP)
  //   011 : OR
  //   100 : AND
  //   101 : XOR
  //   110 : RIGHT ROTATE
  //   111 : EQ
endmodule
