// Logisim project SAP_1.circ as structural Verilog: 11 circuits, main circuit main
module main (
);

  wire controller_1_clk, controller_1_clr, controller_1_nclk, controller_1_nclr;
  wire [3:0] inputandmar_1_out_4, inputandmar_1_out_5, instructionregister_1_out_7, programcounter_1_out_5,
       ram16x8_1_out_4;
  wire [7:0] accumulatora_1_out_6, bregister_1_out_3, outputregister_1_out_4;
  wire [11:0] controller_1_out_6;

  ProgramCounter programcounter_1 (
    .Cp(controller_1_out_6[11]), .n_CLK(controller_1_nclk), .n_CLR(controller_1_nclr),
    .Ep(controller_1_out_6[10]), .out_5(programcounter_1_out_5));
  InputAndMAR inputandmar_1 (
    .n_Lm(controller_1_out_6[9]), .CLK(controller_1_clk), .in_2(programcounter_1_out_5),
    .out_4(inputandmar_1_out_4), .out_5(inputandmar_1_out_5));
  RAM16x8 ram16x8_1 (
    .n_CE(controller_1_out_6[8]), .in_1(inputandmar_1_out_4), .in_2(inputandmar_1_out_5),
    .out_4({ram16x8_1_out_4, programcounter_1_out_5}));
  InstructionRegister instructionregister_1 (
    .n_Li(controller_1_out_6[7]), .CLK(controller_1_clk), .CLR(controller_1_clr),
    .n_Ei(controller_1_out_6[6]), .in_2({ram16x8_1_out_4, programcounter_1_out_5}),
    .out_7(instructionregister_1_out_7), .out_6(programcounter_1_out_5));
  Controller controller_1 (
    .in_1(instructionregister_1_out_7), .out_6(controller_1_out_6), .CLK(controller_1_clk),
    .nCLK(controller_1_nclk), .CLR(controller_1_clr), .nCLR(controller_1_nclr));
  AccumulatorA accumulatora_1 (
    .in_2({ram16x8_1_out_4, programcounter_1_out_5}), .n_La(controller_1_out_6[5]), .CLK(controller_1_clk),
    .Ea(controller_1_out_6[4]), .out_5({ram16x8_1_out_4, programcounter_1_out_5}),
    .out_6(accumulatora_1_out_6));
  AdderSubtractor addersubtractor_1 (
    .in_1(accumulatora_1_out_6), .in_4(bregister_1_out_3), .Su(controller_1_out_6[3]),
    .Eu(controller_1_out_6[2]), .out_5({ram16x8_1_out_4, programcounter_1_out_5}));
  BRegister bregister_1 (
    .n_Lb(controller_1_out_6[1]), .CLK(controller_1_clk), .out_4({ram16x8_1_out_4, programcounter_1_out_5}),
    .out_3(bregister_1_out_3));
  OutputRegister outputregister_1 (
    .in_2({ram16x8_1_out_4, programcounter_1_out_5}), .n_Lo(controller_1_out_6[0]), .CLK(controller_1_clk),
    .out_4(outputregister_1_out_4));
  BinaryDisplay binarydisplay_1 (.in_1(outputregister_1_out_4));
endmodule

module ProgramCounter (
  input  Cp,
  input  n_CLK,
  input  n_CLR,
  input  Ep,
  output [3:0] out_5
);

  J_K_Flip_Flop #(.trigger("falling")) j_k_ff_1 (
    .J(Cp), .K(Cp), .clk(n_CLK), .Q(out_5[0]), .reset(n_CLR));  // open: Qn, preset
  J_K_Flip_Flop #(.trigger("falling")) j_k_ff_2 (
    .J(Cp), .K(Cp), .clk(out_5[0]), .Q(out_5[1]), .reset(n_CLR));  // open: Qn, preset
  J_K_Flip_Flop #(.trigger("falling")) j_k_ff_3 (
    .J(Cp), .K(Cp), .clk(out_5[1]), .Q(out_5[2]), .reset(n_CLR));  // open: Qn, preset
  J_K_Flip_Flop #(.trigger("falling")) j_k_ff_4 (
    .J(Cp), .K(Cp), .clk(out_5[2]), .Q(out_5[3]), .reset(n_CLR));  // open: Qn, preset
endmodule

module InputAndMAR (
  input  n_Lm,
  input  [3:0] in_2,
  input  CLK,
  output [3:0] out_4,
  output [3:0] out_5
);
endmodule

module RAM16x8 (
  input  [3:0] in_1,
  input  [3:0] in_2,
  input  n_CE,
  output [7:0] out_4
);
endmodule

module InstructionRegister (
  input  n_Li,
  input  [7:0] in_2,
  input  CLK,
  input  CLR,
  input  n_Ei,
  output [3:0] out_6,
  output [3:0] out_7
);
endmodule

module Controller (
  input  [3:0] in_1,
  output CLK,
  output nCLK,
  output CLR,
  output nCLR,
  output [11:0] out_6
);
endmodule

module AccumulatorA (
  input  n_La,
  input  [7:0] in_2,
  input  CLK,
  input  Ea,
  output [7:0] out_5,
  output [7:0] out_6
);
endmodule

module AdderSubtractor (
  input  [7:0] in_1,
  input  Su,
  input  Eu,
  input  [7:0] in_4,
  output [7:0] out_5
);
endmodule

module BRegister (
  input  n_Lb,
  input  CLK,
  output [7:0] out_3,
  output [7:0] out_4
);
endmodule

module OutputRegister (
  input  n_Lo,
  input  [7:0] in_2,
  input  CLK,
  output [7:0] out_4
);
endmodule

module BinaryDisplay (
  input  [7:0] in_1
);
endmodule
